// Logisim project cpu_forward_pipeline_with_singleInt.circ as structural Verilog: 22 circuits, main circuit ◇单周期MIPS
module \单周期MIPS  (
  input  clk,
  input  IR1,
  input  IR2,
  input  IR3,
  output RegWrite,
  output MemWrite,
  output [31:0] PC,
  output [31:0] IR,
  output [31:0] RDin,
  output [31:0] MDin,
  output [31:0] LedData
);

  wire and_3_out, and_4_out, and_5_out, and_6_out, and_10_out, and_11_out, and_12_out, and_13_out,
       comparator_1_eq, comparator_3_eq, comparator_4_gt, comparator_5_lt, comparator_6_eq, comparator_7_eq,
       comparator_8_eq, d_ff_1_q, d_ff_2_q, d_ff_3_q, decoder_1_out0, decoder_1_out1, decoder_2_out1,
       decoder_2_out2, decoder_2_out3, decoder_3_out1, decoder_3_out2, decoder_3_out3, demultiplexer_1_out1,
       demultiplexer_1_out2, demultiplexer_1_out3, demultiplexer_2_out1, demultiplexer_2_out2,
       demultiplexer_2_out3, EN, eq, ERET, Go, IE, Interupt, IR1_q, IR1_t, IR2_q, IR2_t, IR3_q, IR3_t, IRA,
       IRB, IRC, J, JAL, JR, MFC0, MTC0, multiplexer_5_out, not_1_out, not_2_out, not_3_out, or_5_out,
       or_6_out, or_7_out, or_9_out, or_11_out, or_12_out, or_13_out, or_14_out, SignedExt, syscall, W1, W2,
       W3, \单周期硬布线控制器_1_alu_src , \单周期硬布线控制器_1_beq , \单周期硬布线控制器_1_bne , \单周期硬布线控制器_1_memtoreg ,
       \单周期硬布线控制器_1_regdst ;
  wire [1:0] and_7_out, IRX, multiplexer_6_out, register_1_q, register_2_q, register_3_q;
  wire [3:0] \单周期硬布线控制器_1_alu_op ;
  wire [4:0] multiplexer_7_out, multiplexer_8_out, multiplexer_9_out, multiplexer_10_out;
  wire [9:0] mips_alu_1_result_2;
  wire [15:0] multiplexer_19_out, multiplexer_20_out, multiplexer_20_out_2, \总周期数 ;
  wire [21:0] mips_alu_1_result;
  wire [31:0] adder_1_out, adder_2_out, bit_extender_1_out, bit_extender_2_out, bit_extender_3_out,
       counter_1_q, epc_q, EPCtoPC, JRADDR, multiplexer_2_out, multiplexer_3_out, multiplexer_4_out,
       multiplexer_11_out, multiplexer_13_out, multiplexer_14_out, multiplexer_16_out, multiplexer_17_out,
       normalPC, ram_1_data, realPC, register_4_q, register_5_q, register_6_q, shifter_1_out, shifter_2_out;

  Button _1 (.out(IRA));
  Button _2 (.out(IRB));
  Button _3 (.out(IRC));
  Button \u_继续运行  (.out(Go));
  LED led_1 (.in(W1));
  LED led_2 (.in(W2));
  LED led_3 (.in(W3));
  Hex_Digit_Display hex_digit_display_1 (.value(LedData[31:28]));  // open: dp
  Hex_Digit_Display hex_digit_display_2 (.value(LedData[27:24]));  // open: dp
  Hex_Digit_Display hex_digit_display_3 (.value(LedData[23:20]));  // open: dp
  Demultiplexer #(.select(2), .enable("false")) demultiplexer_1 (
    .out1(demultiplexer_1_out1), .out2(demultiplexer_1_out2), .out3(demultiplexer_1_out3), .in(ERET),
    .sel(IRX));  // open: out0
  Hex_Digit_Display hex_digit_display_4 (.value(LedData[19:16]));  // open: dp
  Hex_Digit_Display hex_digit_display_5 (.value(LedData[15:12]));  // open: dp
  Hex_Digit_Display hex_digit_display_6 (.value(LedData[7:4]));  // open: dp
  Hex_Digit_Display hex_digit_display_7 (.value(LedData[11:8]));  // open: dp
  // Probe on \总周期数 
  Decoder #(.enable("false")) decoder_1 (.out0(decoder_1_out0), .out1(decoder_1_out1), .sel(IR[23]));
  Comparator #(.width(6)) comparator_1 (.a(IR[31:26]), .b(6'b010000), .eq(comparator_1_eq));  // open: gt, lt
  Comparator #(.width(32)) comparator_2 (.a(IR), .b(32'h42000018), .eq(ERET));  // open: gt, lt
  Hex_Digit_Display hex_digit_display_8 (.value(LedData[3:0]));  // open: dp
  Multiplexer #(.width(32), .enable("false")) multiplexer_1 (
    .in0(adder_1_out), .in1(multiplexer_3_out), .out(normalPC), .sel(or_9_out));
  or or_1 (W1, IR1_q, d_ff_1_q);
  or or_2 (W2, IR2_q, d_ff_2_q);
  or or_3 (W3, IR3_q, d_ff_3_q);
  or or_4 (IR1_t, IR1, IRA);
  and and_1 (MFC0, decoder_1_out0, comparator_1_eq);
  and and_2 (MTC0, comparator_1_eq, decoder_1_out1);
  D_Flip_Flop d_ff_1 (.clk(IR1_t), .D(1'b1), .Q(d_ff_1_q), .reset(IR1_q));  // open: Qn, preset, en
  D_Flip_Flop d_ff_2 (.clk(IR2_t), .D(1'b1), .Q(d_ff_2_q), .reset(IR2_q));  // open: Qn, preset, en
  D_Flip_Flop d_ff_3 (.clk(IR3_t), .D(1'b1), .Q(d_ff_3_q), .reset(IR3_q));  // open: Qn, preset, en
  Multiplexer #(.width(32), .enable("false")) multiplexer_2 (
    .in0(realPC), .in1(EPCtoPC), .out(multiplexer_2_out), .sel(ERET));
  or or_5 (or_5_out, d_ff_1_q, IR1_q);
  or or_6 (or_6_out, d_ff_2_q, IR2_q);
  or or_7 (or_7_out, d_ff_3_q, IR3_q);
  or or_8 (IR2_t, IR2, IRB);
  Register #(.width(32)) u_PC (.D(multiplexer_2_out), .en(EN), .Q(PC), .clk(clk));  // open: clr
  and and_3 (and_3_out, or_5_out, ~demultiplexer_1_out1);  // AND_Gate
  and and_4 (and_4_out, or_6_out, ~demultiplexer_1_out2);  // AND_Gate
  and and_5 (and_5_out, or_7_out, ~demultiplexer_1_out3);  // AND_Gate
  or or_9 (or_9_out, or_14_out, J);
  Adder #(.width(32)) adder_1 (.a(PC), .b(32'h4), .out(adder_1_out));  // open: cin, cout
  Multiplexer #(.width(32), .enable("false")) multiplexer_3 (
    .in0(adder_2_out), .in1(multiplexer_4_out), .out(multiplexer_3_out), .sel(J));
  not not_1 (not_1_out, Go);
  and and_6 (and_6_out, syscall, not_2_out);
  not not_2 (not_2_out, eq);
  D_Flip_Flop u_IR1 (.clk(clk), .D(and_3_out), .Q(IR1_q));  // open: Qn, preset, en, reset
  D_Flip_Flop u_IR2 (.clk(clk), .D(and_4_out), .Q(IR2_q));  // open: Qn, preset, en, reset
  D_Flip_Flop u_IR3 (.clk(clk), .D(and_5_out), .Q(IR3_q));  // open: Qn, preset, en, reset
  Counter #(.width(32), .max('hffffffff)) counter_1 (.Q(counter_1_q), .clk(clk));  // open: load, D, count, carry, clr
  or or_10 (IR3_t, IR3, IRC);
  Multiplexer #(.width(32), .enable("false")) multiplexer_4 (
    .in0(shifter_1_out), .in1(JRADDR), .out(multiplexer_4_out), .sel(JR));
  nand nand_1 (EN, not_1_out, and_6_out);
  Decoder #(.select(2), .enable("false")) decoder_2 (
    .out1(decoder_2_out1), .out2(decoder_2_out2), .out3(decoder_2_out3), .sel(IRX));  // open: out0
  Demultiplexer #(.select(2), .enable("false")) demultiplexer_2 (
    .out1(demultiplexer_2_out1), .out2(demultiplexer_2_out2), .out3(demultiplexer_2_out3), .in(ERET),
    .sel(IRX));  // open: out0
  or or_11 (or_11_out, Interupt, MTC0);
  ROM #(.addrWidth(10), .dataWidth(32)) rom_1 (.addr(PC[11:2]), .data(IR));  // open: sel
  Multiplexer #(.enable("false")) multiplexer_5 (.in0(1'b1), .in1(1'b0), .out(multiplexer_5_out), .sel(or_11_out));
  or or_12 (or_12_out, MTC0, MFC0, comparator_3_eq, ERET, Interupt);
  Comparator #(.width(32), .mode("unsigned")) comparator_3 (
    .a(counter_1_q), .b({32{1'b0}}), .eq(comparator_3_eq));  // open: gt, lt
  Register #(.width(2)) register_1 (
    .D(2'b01), .en(decoder_2_out1), .Q(register_1_q), .clk(clk), .clr(demultiplexer_2_out1));
  Register #(.width(2)) register_2 (
    .D(2'b10), .en(decoder_2_out2), .Q(register_2_q), .clk(clk), .clr(demultiplexer_2_out2));
  Register #(.width(2)) register_3 (
    .D(2'b11), .en(decoder_2_out3), .Q(register_3_q), .clk(clk), .clr(demultiplexer_2_out3));
  Register #(.width(1)) u_ie (.D(multiplexer_5_out), .en(or_12_out), .Q(IE), .clk(clk));  // open: clr
  assign bit_extender_1_out = {{16{1'b0}}, IR[15:0]};  // Bit_Extender bit_extender_1
  assign bit_extender_2_out = {{16{IR[15]}}, IR[15:0]};  // Bit_Extender bit_extender_2
  assign bit_extender_3_out = {{6{1'b0}}, IR[25:0]};  // Bit_Extender bit_extender_3
  Counter #(.width(16), .max('hffff)) counter_2 (.count(EN), .Q(\总周期数 ), .clk(clk));  // open: load, D, carry, clr
  Multiplexer #(.select(2), .width(2), .enable("false")) multiplexer_6 (
    .in0(2'b00), .in1(register_1_q), .in2(register_2_q), .in3(register_3_q), .out(multiplexer_6_out),
    .sel(IRX));
  \单周期硬布线控制器  \u_单周期硬布线控制器_1  (
    .Func(IR[5:0]), .OP(IR[31:26]), .ALU_OP(\单周期硬布线控制器_1_alu_op ), .MemToReg(\单周期硬布线控制器_1_memtoreg ),
    .MemWrite(MemWrite), .ALU_SRC(\单周期硬布线控制器_1_alu_src ), .RegWrite(RegWrite), .SysCALL(syscall),
    .SignedExt(SignedExt), .RegDst(\单周期硬布线控制器_1_regdst ), .JR(JR), .JMP(J), .Beq(\单周期硬布线控制器_1_beq ),
    .JAL(JAL), .Bne(\单周期硬布线控制器_1_bne ));
  Multiplexer #(.width(5), .enable("false")) multiplexer_7 (
    .in0(IR[25:21]), .in1(5'b00010), .out(multiplexer_7_out), .sel(syscall));
  Shifter #(.width(32)) shifter_1 (.in(bit_extender_3_out), .\dist (5'b00010), .out(shifter_1_out));
  Priority_Encoder #(.select(2), .disabled(0)) priority_encoder_1 (
    .in0(1'b1), .in1(IR1_q), .in2(IR2_q), .in3(IR3_q), .out(IRX));  // open: gs, en_out, en_in
  Multiplexer #(.width(5), .enable("false")) multiplexer_8 (
    .in0(IR[20:16]), .in1(5'b00100), .out(multiplexer_8_out), .sel(syscall));
  Multiplexer #(.width(5), .enable("false")) multiplexer_9 (
    .in0(IR[20:16]), .in1(IR[15:11]), .out(multiplexer_9_out), .sel(\单周期硬布线控制器_1_regdst ));
  Multiplexer #(.width(5), .enable("false")) multiplexer_10 (
    .in0(multiplexer_9_out), .in1({5{1'b1}}), .out(multiplexer_10_out), .sel(JAL));
  Comparator #(.width(2), .mode("unsigned")) comparator_4 (.a(IRX), .b(2'b00), .gt(comparator_4_gt));  // open: eq, lt
  Comparator #(.width(2), .mode("unsigned")) comparator_5 (
    .a(multiplexer_6_out), .b(IRX), .lt(comparator_5_lt));  // open: gt, eq
  Multiplexer #(.width(32), .enable("false")) multiplexer_11 (
    .in0(bit_extender_1_out), .in1(bit_extender_2_out), .out(multiplexer_11_out), .sel(SignedExt));
  Multiplexer #(.width(32), .enable("false")) multiplexer_12 (
    .in0(multiplexer_14_out), .in1({IR[15:0], {16{1'b0}}}), .out(RDin), .sel(comparator_6_eq));
  Comparator #(.width(6), .mode("unsigned")) comparator_6 (
    .a(IR[31:26]), .b(6'b001111), .eq(comparator_6_eq));  // open: gt, lt
  and and_7 (and_7_out[0], IE, IRX[0]);
  and and_8 (and_7_out[1], IRX[1], IE);
  and and_9 (Interupt, comparator_4_gt, comparator_5_lt, IE);
  Register #(.width(32)) epc (.D(normalPC), .en(Interupt), .Q(epc_q), .clk(clk));  // open: clr
  and and_10 (and_10_out, eq, \单周期硬布线控制器_1_beq );
  MIPS_Regifile mips_regifile_1 (
    .Din(RDin), .Clk(clk), .R1(JRADDR), .R2(MDin), .WE(RegWrite), .W_num(multiplexer_10_out),
    .R1_num(multiplexer_7_out), .R2_num(multiplexer_8_out));
  Multiplexer #(.width(32), .enable("false")) multiplexer_13 (
    .in0(MDin), .in1(multiplexer_11_out), .out(multiplexer_13_out), .sel(\单周期硬布线控制器_1_alu_src ));
  Multiplexer #(.width(32), .enable("false")) multiplexer_14 (
    .in0(multiplexer_17_out), .in1(adder_1_out), .out(multiplexer_14_out), .sel(JAL));
  Multiplexer #(.select(2), .width(32), .enable("false")) multiplexer_15 (
    .in0(normalPC), .in1(32'h30ac), .in2(32'h3158), .in3(32'h3204), .out(realPC), .sel(and_7_out));
  Decoder #(.select(2), .enable("false")) decoder_3 (
    .out1(decoder_3_out1), .out2(decoder_3_out2), .out3(decoder_3_out3), .sel(IRX));  // open: out0
  not not_3 (not_3_out, eq);
  and and_11 (and_11_out, not_3_out, \单周期硬布线控制器_1_bne );
  and and_12 (and_12_out, syscall, eq);
  Shifter #(.width(32)) shifter_2 (.in(multiplexer_11_out), .\dist (5'b00010), .out(shifter_2_out));
  Register #(.width(32)) register_4 (.D(epc_q), .en(decoder_3_out1), .Q(register_4_q), .clk(clk));  // open: clr
  Register #(.width(32)) register_5 (.D(epc_q), .en(decoder_3_out2), .Q(register_5_q), .clk(clk));  // open: clr
  Register #(.width(32)) register_6 (.D(epc_q), .en(decoder_3_out3), .Q(register_6_q), .clk(clk));  // open: clr
  or or_13 (or_13_out, and_10_out, and_11_out);
  Register #(.width(32)) PC_2 (.D(MDin), .en(and_12_out), .Q(LedData), .clk(clk));  // open: clr
  Multiplexer #(.width(32), .enable("false")) multiplexer_16 (
    .in0(multiplexer_13_out), .in1(32'h22), .out(multiplexer_16_out), .sel(syscall));
  Adder #(.width(32)) adder_2 (.a(shifter_2_out), .b(adder_1_out), .out(adder_2_out));  // open: cin, cout
  Multiplexer #(.width(32), .enable("false")) multiplexer_17 (
    .in0({multiplexer_20_out_2, multiplexer_20_out}), .in1({{16{1'b0}}, multiplexer_19_out}),
    .out(multiplexer_17_out), .sel(comparator_7_eq));
  or or_14 (or_14_out, or_13_out, and_13_out);
  MIPS_ALU mips_alu_1 (
    .X(JRADDR), .Y(multiplexer_16_out), .AluOP(\单周期硬布线控制器_1_alu_op ), .Equal(eq),
    .Result({mips_alu_1_result[21:2], mips_alu_1_result_2, mips_alu_1_result[1:0]}), .shamt(IR[10:6]));  // open: Result_2
  Comparator #(.width(6), .mode("unsigned")) comparator_7 (
    .a(IR[31:26]), .b(6'b100101), .eq(comparator_7_eq));  // open: gt, lt
  Multiplexer #(.select(2), .width(32), .enable("false")) multiplexer_18 (
    .in1(register_4_q), .in2(register_5_q), .in3(register_6_q), .out(EPCtoPC), .sel(IRX));  // open: in0
  and and_13 (and_13_out, comparator_8_eq, mips_alu_1_result[0]);
  Comparator #(.width(6), .mode("unsigned")) comparator_8 (
    .a(IR[31:26]), .b(6'b000001), .eq(comparator_8_eq));  // open: gt, lt
  Multiplexer #(.width(16), .enable("false")) multiplexer_19 (
    .in0(multiplexer_20_out), .in1(multiplexer_20_out_2), .out(multiplexer_19_out), .sel(IR[1]));
  RAM #(.addrWidth(10), .dataWidth(32), .bus("separate")) ram_1 (
    .addr(mips_alu_1_result_2), .din(MDin), .data(ram_1_data), .str(MemWrite), .sel(1'b1), .clk(clk));  // open: ld, clr
  Multiplexer #(.width(32), .enable("false")) multiplexer_20 (
    .in0({mips_alu_1_result[21:2], mips_alu_1_result_2, mips_alu_1_result[1:0]}), .in1(ram_1_data),
    .out({multiplexer_20_out_2, multiplexer_20_out}), .sel(\单周期硬布线控制器_1_memtoreg ));
  // AND_Gate and_14 is placed but not wired

  // Other names for the same wires on the sheet: OP[5:0] = IR[31:26]; mw = MemWrite

  // Notes on the sheet:
  //   中断源
  //   中断等待指示
  //   总复位信号应将除ROM以外所有存储组件全部清零
  //   数码管输出
  //   数码管输出应该用寄存器锁存，否则显示数据只能一闪而过
  //   Reset 
  //   Reset 
  //   Reset 
  //   为方便自动评测，需要输出PC，IR，寄存器文件写入端口RDin，内存写入端口MDin等信号
  //   指令存储器
  //   contents of rom_1 (hex, n*v repeats v):
  //   20110001 8000c05 20110001 20120002 20130003 8000c09 20110001 20120002 20130003 8000c0d 20110001
  //   20120002 20130003 8000c11 20110001 20120002 20130003 c000cb8 20100001 20110001 118fc0 112020
  //   20020022 c 118882 12200001 8000c15 112020 20020022 c 20110001 118880 112020 20020022 c 12200001
  //   8000c1f 20110001 118fc0 112020 20020022 c 1188c3 112020 20020022 c 118903 112020 20020022 c 118903
  //   112020 20020022 c 118903 112020 20020022 c 118903 112020 20020022 c 118903 112020 20020022 c 118903
  //   112020 20020022 c 118903 112020 20020022 c 20100001 109fc0 139fc3 8021 2012000c 24160003 26100001
  //   3210000f 20080008 20090001 139900 2709825 132020 20020022 c 1094022 1500fff9 22100001 2018000f
  //   2188024 108700 20080008 20090001 139902 2709825 132021 20020022 c 1094022 1500fff9 108702 2c9b022
  //   12c00001 8000c50 4020 1084027 84400 3508ffff 82021 20020022 c 2010ffff 20110000 ae300000 22100001
  //   22310004 ae300000 22100001 22310004 ae300000 22100001 22310004 ae300000 22100001 22310004 ae300000
  //   22100001 22310004 ae300000 22100001 22310004 ae300000 22100001 22310004 ae300000 22100001 22310004
  //   ae300000 22100001 22310004 ae300000 22100001 22310004 ae300000 22100001 22310004 ae300000 22100001
  //   22310004 ae300000 22100001 22310004 ae300000 22100001 22310004 ae300000 22100001 22310004 ae300000
  //   22100001 22310004 22100001 8020 2011003c 8e130000 8e340000 274402a 11000002 ae330000 ae140000
  //   2231fffc 1611fff8 102020 20020022 c 22100004 2011003c 1611fff2 20020032 c 20100000 22100001 102020
  //   20020022 c 22100002 102020 20020022 c 22100003 102020 20020022 c 22100004 102020 20020022 c 22100005
  //   102020 20020022 c 22100006 102020 20020022 c 22100007 102020 20020022 c 22100008 102020 20020022
  //   20020022 c 3e00008
  //   rs
  //   指令字
  //   rt
  //   rd
  //   JMP
  //   JR
  //   OP
  //   Func
  //   Beq
  //   Bne
  //   MemToReg
  //   MemWrite
  //   AluOP
  //   AluSrcB
  //   RegWrite
  //   JAL
  //   RegDst
  //   Syscall
endmodule

module \单周期MIPS_单级中断  (
  input  IR1,
  input  IR2,
  input  IR3,
  output RegWrite,
  output MemWrite,
  output [31:0] PC,
  output [31:0] IR,
  output [31:0] RDin,
  output [31:0] MDin,
  output [31:0] LedData
);

  wire and_1_out, and_2_out, and_3_out, and_4_out, and_8_out, and_9_out, and_10_out, and_11_out, CLK,
       comparator_2_eq, comparator_3_gt, comparator_4_eq, comparator_5_eq, comparator_6_eq, d_ff_1_q,
       d_ff_2_q, d_ff_3_q, demultiplexer_1_out1, demultiplexer_1_out2, demultiplexer_1_out3, EN, eq, ERET,
       Go, IE, Interupt, IR1_q, IR1_t, IR2_q, IR2_t, IR3_q, IR3_t, IRA, IRB, IRC, J, JAL, JR,
       multiplexer_5_out, not_1_out, not_2_out, not_3_out, or_4_out, or_5_out, or_6_out, or_9_out, or_11_out,
       or_12_out, or_13_out, SignedExt, syscall, W1, W2, W3, \单周期硬布线控制器_1_alu_src , \单周期硬布线控制器_1_beq ,
       \单周期硬布线控制器_1_bne , \单周期硬布线控制器_1_memtoreg , \单周期硬布线控制器_1_regdst ;
  wire [1:0] and_5_out, IRX, IRX_;
  wire [3:0] \单周期硬布线控制器_1_alu_op ;
  wire [4:0] multiplexer_6_out, multiplexer_7_out, multiplexer_8_out, multiplexer_9_out;
  wire [9:0] mips_alu_1_result_2;
  wire [15:0] multiplexer_17_out, multiplexer_18_out, multiplexer_18_out_2, \总周期数 ;
  wire [21:0] mips_alu_1_result;
  wire [31:0] adder_1_out, adder_2_out, bit_extender_1_out, bit_extender_2_out, bit_extender_3_out,
       counter_2_q, EPCtoPC, JRADDR, multiplexer_2_out, multiplexer_3_out, multiplexer_4_out,
       multiplexer_10_out, multiplexer_12_out, multiplexer_13_out, multiplexer_15_out, multiplexer_16_out,
       normalPC, ram_1_data, realPC, shifter_1_out, shifter_2_out;

  Clock clock_1 (.out(CLK));
  Button _1 (.out(IRA));
  Button _2 (.out(IRB));
  Button _3 (.out(IRC));
  Button \u_继续运行  (.out(Go));
  LED led_1 (.in(W1));
  LED led_2 (.in(W2));
  LED led_3 (.in(W3));
  Hex_Digit_Display hex_digit_display_1 (.value(LedData[31:28]));  // open: dp
  Demultiplexer #(.select(2), .enable("false")) demultiplexer_1 (
    .out1(demultiplexer_1_out1), .out2(demultiplexer_1_out2), .out3(demultiplexer_1_out3), .in(ERET),
    .sel(IRX_));  // open: out0
  Hex_Digit_Display hex_digit_display_2 (.value(LedData[23:20]));  // open: dp
  Hex_Digit_Display hex_digit_display_3 (.value(LedData[27:24]));  // open: dp
  Counter #(.width(16), .max('hffff)) counter_1 (.count(EN), .Q(\总周期数 ), .clk(CLK));  // open: load, D, carry, clr
  Hex_Digit_Display hex_digit_display_4 (.value(LedData[19:16]));  // open: dp
  Hex_Digit_Display hex_digit_display_5 (.value(LedData[15:12]));  // open: dp
  not not_1 (not_1_out, Go);
  and and_1 (and_1_out, syscall, not_2_out);
  not not_2 (not_2_out, eq);
  Comparator #(.width(32)) comparator_1 (.a(IR), .b(32'h42000018), .eq(ERET));  // open: gt, lt
  Hex_Digit_Display hex_digit_display_6 (.value(LedData[7:4]));  // open: dp
  Hex_Digit_Display hex_digit_display_7 (.value(LedData[11:8]));  // open: dp
  // Probe on \总周期数 
  Multiplexer #(.width(32), .enable("false")) multiplexer_1 (
    .in0(adder_1_out), .in1(multiplexer_3_out), .out(normalPC), .sel(or_9_out));
  or or_1 (W1, IR1_q, d_ff_1_q);
  or or_2 (W2, IR2_q, d_ff_2_q);
  or or_3 (W3, IR3_q, d_ff_3_q);
  Hex_Digit_Display hex_digit_display_8 (.value(LedData[3:0]));  // open: dp
  nand nand_1 (EN, not_1_out, and_1_out);
  D_Flip_Flop d_ff_1 (.clk(IR1_t), .D(1'b1), .Q(d_ff_1_q), .reset(IR1_q));  // open: Qn, preset, en
  D_Flip_Flop d_ff_2 (.clk(IR2_t), .D(1'b1), .Q(d_ff_2_q), .reset(IR2_q));  // open: Qn, preset, en
  D_Flip_Flop d_ff_3 (.clk(IR3_t), .D(1'b1), .Q(d_ff_3_q), .reset(IR3_q));  // open: Qn, preset, en
  Multiplexer #(.width(32), .enable("false")) multiplexer_2 (
    .in0(realPC), .in1(EPCtoPC), .out(multiplexer_2_out), .sel(ERET));
  or or_4 (or_4_out, d_ff_1_q, IR1_q);
  or or_5 (or_5_out, d_ff_2_q, IR2_q);
  or or_6 (or_6_out, d_ff_3_q, IR3_q);
  or or_7 (IR1_t, IR1, IRA);
  Register #(.width(32)) u_PC (.D(multiplexer_2_out), .en(EN), .Q(PC), .clk(CLK));  // open: clr
  and and_2 (and_2_out, or_4_out, ~demultiplexer_1_out1);  // AND_Gate
  and and_3 (and_3_out, or_5_out, ~demultiplexer_1_out2);  // AND_Gate
  and and_4 (and_4_out, or_6_out, ~demultiplexer_1_out3);  // AND_Gate
  or or_8 (IR2_t, IR2, IRB);
  or or_9 (or_9_out, or_13_out, J);
  Adder #(.width(32)) adder_1 (.a(PC), .b(32'h4), .out(adder_1_out));  // open: cin, cout
  Multiplexer #(.width(32), .enable("false")) multiplexer_3 (
    .in0(adder_2_out), .in1(multiplexer_4_out), .out(multiplexer_3_out), .sel(J));
  D_Flip_Flop u_IR1 (.clk(CLK), .D(and_2_out), .Q(IR1_q));  // open: Qn, preset, en, reset
  D_Flip_Flop u_IR2 (.clk(CLK), .D(and_3_out), .Q(IR2_q));  // open: Qn, preset, en, reset
  D_Flip_Flop u_IR3 (.clk(CLK), .D(and_4_out), .Q(IR3_q));  // open: Qn, preset, en, reset
  Counter #(.width(32), .max('hffffffff)) counter_2 (.Q(counter_2_q), .clk(CLK));  // open: load, D, count, carry, clr
  Multiplexer #(.width(32), .enable("false")) multiplexer_4 (
    .in0(shifter_1_out), .in1(JRADDR), .out(multiplexer_4_out), .sel(JR));
  or or_10 (IR3_t, IR3, IRC);
  ROM #(.addrWidth(10), .dataWidth(32)) rom_1 (.addr(PC[11:2]), .data(IR));  // open: sel
  Multiplexer #(.enable("false")) multiplexer_5 (.in0(1'b1), .in1(1'b0), .out(multiplexer_5_out), .sel(Interupt));
  or or_11 (or_11_out, comparator_2_eq, ERET, Interupt);
  Comparator #(.width(32), .mode("unsigned")) comparator_2 (
    .a(counter_2_q), .b({32{1'b0}}), .eq(comparator_2_eq));  // open: gt, lt
  Register #(.width(1)) u_ie (.D(multiplexer_5_out), .en(or_11_out), .Q(IE), .clk(CLK));  // open: clr
  assign bit_extender_1_out = {{16{1'b0}}, IR[15:0]};  // Bit_Extender bit_extender_1
  assign bit_extender_2_out = {{16{IR[15]}}, IR[15:0]};  // Bit_Extender bit_extender_2
  assign bit_extender_3_out = {{6{1'b0}}, IR[25:0]};  // Bit_Extender bit_extender_3
  \单周期硬布线控制器  \u_单周期硬布线控制器_1  (
    .Func(IR[5:0]), .OP(IR[31:26]), .ALU_OP(\单周期硬布线控制器_1_alu_op ), .MemToReg(\单周期硬布线控制器_1_memtoreg ),
    .MemWrite(MemWrite), .ALU_SRC(\单周期硬布线控制器_1_alu_src ), .RegWrite(RegWrite), .SysCALL(syscall),
    .SignedExt(SignedExt), .RegDst(\单周期硬布线控制器_1_regdst ), .JR(JR), .JMP(J), .Beq(\单周期硬布线控制器_1_beq ),
    .JAL(JAL), .Bne(\单周期硬布线控制器_1_bne ));
  Multiplexer #(.width(5), .enable("false")) multiplexer_6 (
    .in0(IR[25:21]), .in1(5'b00010), .out(multiplexer_6_out), .sel(syscall));
  Shifter #(.width(32)) shifter_1 (.in(bit_extender_3_out), .\dist (5'b00010), .out(shifter_1_out));
  Priority_Encoder #(.select(2), .disabled(0)) priority_encoder_1 (
    .in0(1'b1), .in1(IR1_q), .in2(IR2_q), .in3(IR3_q), .out(IRX));  // open: gs, en_out, en_in
  Multiplexer #(.width(5), .enable("false")) multiplexer_7 (
    .in0(IR[20:16]), .in1(5'b00100), .out(multiplexer_7_out), .sel(syscall));
  Multiplexer #(.width(5), .enable("false")) multiplexer_8 (
    .in0(IR[20:16]), .in1(IR[15:11]), .out(multiplexer_8_out), .sel(\单周期硬布线控制器_1_regdst ));
  Multiplexer #(.width(5), .enable("false")) multiplexer_9 (
    .in0(multiplexer_8_out), .in1({5{1'b1}}), .out(multiplexer_9_out), .sel(JAL));
  Comparator #(.width(2), .mode("unsigned")) comparator_3 (.a(IRX), .b(2'b00), .gt(comparator_3_gt));  // open: eq, lt
  Multiplexer #(.width(32), .enable("false")) multiplexer_10 (
    .in0(bit_extender_1_out), .in1(bit_extender_2_out), .out(multiplexer_10_out), .sel(SignedExt));
  Multiplexer #(.width(32), .enable("false")) multiplexer_11 (
    .in0(multiplexer_13_out), .in1({IR[15:0], {16{1'b0}}}), .out(RDin), .sel(comparator_4_eq));
  Comparator #(.width(6), .mode("unsigned")) comparator_4 (
    .a(IR[31:26]), .b(6'b001111), .eq(comparator_4_eq));  // open: gt, lt
  and and_5 (and_5_out[0], IE, IRX[0]);
  and and_6 (and_5_out[1], IRX[1], IE);
  and and_7 (Interupt, comparator_3_gt, IE);
  Register #(.width(32)) epc (.D(normalPC), .en(Interupt), .Q(EPCtoPC), .clk(CLK));  // open: clr
  and and_8 (and_8_out, eq, \单周期硬布线控制器_1_beq );
  MIPS_Regifile mips_regifile_1 (
    .Din(RDin), .Clk(CLK), .R1(JRADDR), .R2(MDin), .WE(RegWrite), .W_num(multiplexer_9_out),
    .R1_num(multiplexer_6_out), .R2_num(multiplexer_7_out));
  Multiplexer #(.width(32), .enable("false")) multiplexer_12 (
    .in0(MDin), .in1(multiplexer_10_out), .out(multiplexer_12_out), .sel(\单周期硬布线控制器_1_alu_src ));
  Multiplexer #(.width(32), .enable("false")) multiplexer_13 (
    .in0(multiplexer_16_out), .in1(adder_1_out), .out(multiplexer_13_out), .sel(JAL));
  Multiplexer #(.select(2), .width(32), .enable("false")) multiplexer_14 (
    .in0(normalPC), .in1(32'h30ac), .in2(32'h3150), .in3(32'h31f4), .out(realPC), .sel(and_5_out));
  not not_3 (not_3_out, eq);
  and and_9 (and_9_out, not_3_out, \单周期硬布线控制器_1_bne );
  and and_10 (and_10_out, syscall, eq);
  Shifter #(.width(32)) shifter_2 (.in(multiplexer_10_out), .\dist (5'b00010), .out(shifter_2_out));
  or or_12 (or_12_out, and_8_out, and_9_out);
  Register #(.width(32)) PC_2 (.D(MDin), .en(and_10_out), .Q(LedData), .clk(CLK));  // open: clr
  Multiplexer #(.width(32), .enable("false")) multiplexer_15 (
    .in0(multiplexer_12_out), .in1(32'h22), .out(multiplexer_15_out), .sel(syscall));
  Adder #(.width(32)) adder_2 (.a(shifter_2_out), .b(adder_1_out), .out(adder_2_out));  // open: cin, cout
  Multiplexer #(.width(32), .enable("false")) multiplexer_16 (
    .in0({multiplexer_18_out_2, multiplexer_18_out}), .in1({{16{1'b0}}, multiplexer_17_out}),
    .out(multiplexer_16_out), .sel(comparator_5_eq));
  or or_13 (or_13_out, or_12_out, and_11_out);
  MIPS_ALU mips_alu_1 (
    .X(JRADDR), .Y(multiplexer_15_out), .AluOP(\单周期硬布线控制器_1_alu_op ), .Equal(eq),
    .Result({mips_alu_1_result[21:2], mips_alu_1_result_2, mips_alu_1_result[1:0]}), .shamt(IR[10:6]));  // open: Result_2
  Comparator #(.width(6), .mode("unsigned")) comparator_5 (
    .a(IR[31:26]), .b(6'b100101), .eq(comparator_5_eq));  // open: gt, lt
  Register #(.width(2)) register_1 (.D(IRX), .en(IE), .Q(IRX_), .clk(CLK));  // open: clr
  and and_11 (and_11_out, comparator_6_eq, mips_alu_1_result[0]);
  Comparator #(.width(6), .mode("unsigned")) comparator_6 (
    .a(IR[31:26]), .b(6'b000001), .eq(comparator_6_eq));  // open: gt, lt
  Multiplexer #(.width(16), .enable("false")) multiplexer_17 (
    .in0(multiplexer_18_out), .in1(multiplexer_18_out_2), .out(multiplexer_17_out), .sel(IR[1]));
  RAM #(.addrWidth(10), .dataWidth(32), .bus("separate")) ram_1 (
    .addr(mips_alu_1_result_2), .din(MDin), .data(ram_1_data), .str(MemWrite), .sel(1'b1), .clk(CLK));  // open: ld, clr
  Multiplexer #(.width(32), .enable("false")) multiplexer_18 (
    .in0({mips_alu_1_result[21:2], mips_alu_1_result_2, mips_alu_1_result[1:0]}), .in1(ram_1_data),
    .out({multiplexer_18_out_2, multiplexer_18_out}), .sel(\单周期硬布线控制器_1_memtoreg ));
  // AND_Gate and_12 is placed but not wired

  // Other names for the same wires on the sheet: OP[5:0] = IR[31:26]; mw = MemWrite

  // Notes on the sheet:
  //   中断源
  //   中断等待指示
  //   总复位信号应将除ROM以外所有存储组件全部清零
  //   数码管输出
  //   数码管输出应该用寄存器锁存，否则显示数据只能一闪而过
  //   Reset 
  //   Reset 
  //   Reset 
  //   指令存储器
  //   contents of rom_1 (hex, n*v repeats v):
  //   201d07d0 20100001 109fc0 139fc3 8021 2012000c 24160008 26100001 3210000f 20080008 20090001 139900
  //   2709825 132020 20020022 c 1094022 1500fff9 22100001 2018000f 2188024 108700 20080008 20090001 139902
  //   2709825 132021 20020022 c 1094022 1500fff9 108702 2c9b022 12c00001 8000c07 4020 1084027 84400
  //   3508ffff 82021 20020022 c 8000c01 afa20000 23bd0004 afa40000 23bd0004 afb00000 23bd0004 afb30000
  //   23bd0004 afb40000 23bd0004 afb50000 23bd0004 afb60000 23bd0004 20160001 20140003 20150001 168020
  //   108100 2149825 132020 20020022 c 1600fffa 295a022 1680fff7 23bdfffc 8fb60000 23bdfffc 8fb50000
  //   23bdfffc 8fb40000 23bdfffc 8fb30000 23bdfffc 8fb00000 23bdfffc 8fa40000 23bdfffc 8fa20000 42000018
  //   afa20000 23bd0004 afa40000 23bd0004 afb00000 23bd0004 afb30000 23bd0004 afb40000 23bd0004 afb50000
  //   23bd0004 afb60000 23bd0004 20160002 20140003 20150001 168020 108100 2149825 132020 20020022 c
  //   1600fffa 295a022 1680fff7 23bdfffc 8fb60000 23bdfffc 8fb50000 23bdfffc 8fb40000 23bdfffc 8fb30000
  //   23bdfffc 8fb00000 23bdfffc 8fa40000 23bdfffc 8fa20000 42000018 afa20000 23bd0004 afa40000 23bd0004
  //   afb00000 23bd0004 afb30000 23bd0004 afb40000 23bd0004 afb50000 23bd0004 afb60000 23bd0004 20160003
  //   20140003 20150001 168020 108100 2149825 132020 20020022 c 1600fffa 295a022 1680fff7 23bdfffc
  //   8fb60000 23bdfffc 8fb50000 23bdfffc 8fb40000 23bdfffc 8fb30000 23bdfffc 8fb00000 23bdfffc 8fa40000
  //   23bdfffc 8fa20000 42000018
  //   rs
  //   指令字
  //   rt
  //   rd
  //   JMP
  //   JR
  //   OP
  //   Func
  //   为方便自动评测，需要输出PC，IR，寄存器堆写如数据RDin
  //   Beq
  //   Bne
  //   MemToReg
  //   MemWrite
  //   AluOP
  //   AluSrcB
  //   RegWrite
  //   JAL
  //   RegDst
  //   Syscall
  //   RAM写使能MemWrite、RAM写入数据MDin等信号
endmodule

module \单周期MIPS_多级中断  (
  input  IR1,
  input  IR2,
  input  IR3,
  output RegWrite,
  output MemWrite,
  output [31:0] PC,
  output [31:0] IR,
  output [31:0] RDin,
  output [31:0] MDin,
  output [31:0] LedData
);

  wire and_3_out, and_4_out, and_5_out, and_6_out, and_10_out, and_11_out, and_12_out, and_13_out,
       and_14_out, and_15_out, and_16_out, and_17_out, and_18_out, and_19_out, CLK, comparator_1_eq,
       comparator_3_eq, comparator_4_gt, comparator_5_eq, comparator_6_eq, comparator_7_eq, d_ff_1_q,
       d_ff_2_q, d_ff_3_q, decoder_1_out0, decoder_1_out1, decoder_2_out1, decoder_2_out2, decoder_2_out3,
       decoder_3_out1, decoder_3_out2, decoder_3_out3, demultiplexer_1_out1, demultiplexer_1_out2,
       demultiplexer_1_out3, EN, eq, ERET, Go, IE, Interupt, IR1_q, IR1_t, IR2_q, IR2_t, IR3_q, IR3_t, IRA,
       IRB, IRC, J, JAL, JR, lower, MFC0, MTC0, multiplexer_5_out, not_1_out, not_2_out, not_3_out, or_5_out,
       or_6_out, or_7_out, or_9_out, or_11_out, or_12_out, or_13_out, or_14_out, or_15_out, SignedExt,
       syscall, W1, W2, W3, \单周期硬布线控制器_1_alu_src , \单周期硬布线控制器_1_beq , \单周期硬布线控制器_1_bne ,
       \单周期硬布线控制器_1_memtoreg , \单周期硬布线控制器_1_regdst ;
  wire [1:0] adder_3_out, and_7_out, cur, cur_IR, IRX, load, multiplexer_18_out, register_4_q, register_5_q,
       register_6_q;
  wire [3:0] \单周期硬布线控制器_1_alu_op ;
  wire [4:0] multiplexer_6_out, multiplexer_7_out, multiplexer_8_out, multiplexer_9_out;
  wire [9:0] mips_alu_1_result_2;
  wire [15:0] multiplexer_19_out, multiplexer_21_out, multiplexer_21_out_2, \总周期数 ;
  wire [21:0] mips_alu_1_result;
  wire [31:0] adder_1_out, adder_2_out, bit_extender_1_out, bit_extender_2_out, bit_extender_3_out,
       counter_1_q, EPCtoPC, JRADDR, multiplexer_2_out, multiplexer_3_out, multiplexer_4_out,
       multiplexer_10_out, multiplexer_12_out, multiplexer_13_out, multiplexer_15_out, multiplexer_16_out,
       normalPC, ram_1_data, realPC, register_1_q, register_2_q, register_3_q, shifter_1_out, shifter_2_out;

  Clock clock_1 (.out(CLK));
  Button _1 (.out(IRA));
  Button _2 (.out(IRB));
  Button _3 (.out(IRC));
  Button \u_继续运行  (.out(Go));
  LED led_1 (.in(W1));
  LED led_2 (.in(W2));
  LED led_3 (.in(W3));
  Hex_Digit_Display hex_digit_display_1 (.value(LedData[31:28]));  // open: dp
  Hex_Digit_Display hex_digit_display_2 (.value(LedData[23:20]));  // open: dp
  Hex_Digit_Display hex_digit_display_3 (.value(LedData[27:24]));  // open: dp
  Demultiplexer #(.select(2), .enable("false")) demultiplexer_1 (
    .out1(demultiplexer_1_out1), .out2(demultiplexer_1_out2), .out3(demultiplexer_1_out3), .in(ERET),
    .sel(IRX));  // open: out0
  Hex_Digit_Display hex_digit_display_4 (.value(LedData[15:12]));  // open: dp
  Hex_Digit_Display hex_digit_display_5 (.value(LedData[19:16]));  // open: dp
  Hex_Digit_Display hex_digit_display_6 (.value(LedData[11:8]));  // open: dp
  Hex_Digit_Display hex_digit_display_7 (.value(LedData[7:4]));  // open: dp
  // Probe on \总周期数 
  Decoder #(.enable("false")) decoder_1 (.out0(decoder_1_out0), .out1(decoder_1_out1), .sel(IR[23]));
  Comparator #(.width(6)) comparator_1 (.a(IR[31:26]), .b(6'b010000), .eq(comparator_1_eq));  // open: gt, lt
  Comparator #(.width(32)) comparator_2 (.a(IR), .b(32'h42000018), .eq(ERET));  // open: gt, lt
  Hex_Digit_Display hex_digit_display_8 (.value(LedData[3:0]));  // open: dp
  Multiplexer #(.width(32), .enable("false")) multiplexer_1 (
    .in0(adder_1_out), .in1(multiplexer_3_out), .out(normalPC), .sel(or_9_out));
  or or_1 (W1, IR1_q, d_ff_1_q);
  or or_2 (W2, IR2_q, d_ff_2_q);
  or or_3 (W3, IR3_q, d_ff_3_q);
  and and_1 (MFC0, decoder_1_out0, comparator_1_eq);
  and and_2 (MTC0, comparator_1_eq, decoder_1_out1);
  D_Flip_Flop d_ff_1 (.clk(IR1_t), .D(1'b1), .Q(d_ff_1_q), .reset(IR1_q));  // open: Qn, preset, en
  D_Flip_Flop d_ff_2 (.clk(IR2_t), .D(1'b1), .Q(d_ff_2_q), .reset(IR2_q));  // open: Qn, preset, en
  D_Flip_Flop d_ff_3 (.clk(IR3_t), .D(1'b1), .Q(d_ff_3_q), .reset(IR3_q));  // open: Qn, preset, en
  or or_4 (IR1_t, IR1, IRA);
  Multiplexer #(.width(32), .enable("false")) multiplexer_2 (
    .in0(realPC), .in1(EPCtoPC), .out(multiplexer_2_out), .sel(ERET));
  or or_5 (or_5_out, d_ff_1_q, IR1_q);
  or or_6 (or_6_out, d_ff_2_q, IR2_q);
  or or_7 (or_7_out, d_ff_3_q, IR3_q);
  or or_8 (IR2_t, IR2, IRB);
  Register #(.width(32)) u_PC (.D(multiplexer_2_out), .en(EN), .Q(PC), .clk(CLK));  // open: clr
  and and_3 (and_3_out, or_5_out, ~demultiplexer_1_out1);  // AND_Gate
  and and_4 (and_4_out, or_6_out, ~demultiplexer_1_out2);  // AND_Gate
  and and_5 (and_5_out, or_7_out, ~demultiplexer_1_out3);  // AND_Gate
  or or_9 (or_9_out, or_14_out, J);
  Adder #(.width(32)) adder_1 (.a(PC), .b(32'h4), .out(adder_1_out));  // open: cin, cout
  Multiplexer #(.width(32), .enable("false")) multiplexer_3 (
    .in0(adder_2_out), .in1(multiplexer_4_out), .out(multiplexer_3_out), .sel(J));
  not not_1 (not_1_out, Go);
  and and_6 (and_6_out, syscall, not_2_out);
  not not_2 (not_2_out, eq);
  D_Flip_Flop u_IR1 (.clk(CLK), .D(and_3_out), .Q(IR1_q));  // open: Qn, preset, en, reset
  D_Flip_Flop u_IR2 (.clk(CLK), .D(and_4_out), .Q(IR2_q));  // open: Qn, preset, en, reset
  D_Flip_Flop u_IR3 (.clk(CLK), .D(and_5_out), .Q(IR3_q));  // open: Qn, preset, en, reset
  Counter #(.width(32), .max('hffffffff)) counter_1 (.Q(counter_1_q), .clk(CLK));  // open: load, D, count, carry, clr
  or or_10 (IR3_t, IR3, IRC);
  Multiplexer #(.width(32), .enable("false")) multiplexer_4 (
    .in0(shifter_1_out), .in1(JRADDR), .out(multiplexer_4_out), .sel(JR));
  nand nand_1 (EN, not_1_out, and_6_out);
  or or_11 (or_11_out, Interupt, MTC0);
  ROM #(.addrWidth(10), .dataWidth(32)) rom_1 (.addr(PC[11:2]), .data(IR));  // open: sel
  Multiplexer #(.enable("false")) multiplexer_5 (.in0(1'b1), .in1(1'b0), .out(multiplexer_5_out), .sel(or_11_out));
  or or_12 (or_12_out, MTC0, MFC0, comparator_3_eq, ERET, Interupt);
  Comparator #(.width(32), .mode("unsigned")) comparator_3 (
    .a(counter_1_q), .b({32{1'b0}}), .eq(comparator_3_eq));  // open: gt, lt
  Register #(.width(1)) u_ie (.D(multiplexer_5_out), .en(or_12_out), .Q(IE), .clk(CLK));  // open: clr
  assign bit_extender_1_out = {{16{1'b0}}, IR[15:0]};  // Bit_Extender bit_extender_1
  assign bit_extender_2_out = {{16{IR[15]}}, IR[15:0]};  // Bit_Extender bit_extender_2
  assign bit_extender_3_out = {{6{1'b0}}, IR[25:0]};  // Bit_Extender bit_extender_3
  Counter #(.width(16), .max('hffff)) counter_2 (.count(EN), .Q(\总周期数 ), .clk(CLK));  // open: load, D, carry, clr
  \单周期硬布线控制器  \u_单周期硬布线控制器_1  (
    .Func(IR[5:0]), .OP(IR[31:26]), .ALU_OP(\单周期硬布线控制器_1_alu_op ), .MemToReg(\单周期硬布线控制器_1_memtoreg ),
    .MemWrite(MemWrite), .ALU_SRC(\单周期硬布线控制器_1_alu_src ), .RegWrite(RegWrite), .SysCALL(syscall),
    .SignedExt(SignedExt), .RegDst(\单周期硬布线控制器_1_regdst ), .JR(JR), .JMP(J), .Beq(\单周期硬布线控制器_1_beq ),
    .JAL(JAL), .Bne(\单周期硬布线控制器_1_bne ));
  Multiplexer #(.width(5), .enable("false")) multiplexer_6 (
    .in0(IR[25:21]), .in1(5'b00010), .out(multiplexer_6_out), .sel(syscall));
  Shifter #(.width(32)) shifter_1 (.in(bit_extender_3_out), .\dist (5'b00010), .out(shifter_1_out));
  Priority_Encoder #(.select(2), .disabled(0)) priority_encoder_1 (
    .in0(1'b1), .in1(IR1_q), .in2(IR2_q), .in3(IR3_q), .out(IRX));  // open: gs, en_out, en_in
  Decoder #(.select(2), .enable("false")) decoder_2 (
    .out1(decoder_2_out1), .out2(decoder_2_out2), .out3(decoder_2_out3), .sel(IRX));  // open: out0
  Multiplexer #(.width(5), .enable("false")) multiplexer_7 (
    .in0(IR[20:16]), .in1(5'b00100), .out(multiplexer_7_out), .sel(syscall));
  Multiplexer #(.width(5), .enable("false")) multiplexer_8 (
    .in0(IR[20:16]), .in1(IR[15:11]), .out(multiplexer_8_out), .sel(\单周期硬布线控制器_1_regdst ));
  Multiplexer #(.width(5), .enable("false")) multiplexer_9 (
    .in0(multiplexer_8_out), .in1({5{1'b1}}), .out(multiplexer_9_out), .sel(JAL));
  Comparator #(.width(2), .mode("unsigned")) comparator_4 (.a(IRX), .b(2'b00), .gt(comparator_4_gt));  // open: eq, lt
  Multiplexer #(.width(32), .enable("false")) multiplexer_10 (
    .in0(bit_extender_1_out), .in1(bit_extender_2_out), .out(multiplexer_10_out), .sel(SignedExt));
  Multiplexer #(.width(32), .enable("false")) multiplexer_11 (
    .in0(multiplexer_13_out), .in1({IR[15:0], {16{1'b0}}}), .out(RDin), .sel(comparator_5_eq));
  Comparator #(.width(6), .mode("unsigned")) comparator_5 (
    .a(IR[31:26]), .b(6'b001111), .eq(comparator_5_eq));  // open: gt, lt
  and and_7 (and_7_out[0], Interupt, IE, IRX[0]);
  and and_8 (and_7_out[1], IRX[1], IE, Interupt);
  and and_9 (Interupt, comparator_4_gt, lower, IE);
  and and_10 (and_10_out, Interupt, decoder_2_out1);
  and and_11 (and_11_out, Interupt, decoder_2_out2);
  and and_12 (and_12_out, Interupt, decoder_2_out3);
  and and_13 (and_13_out, eq, \单周期硬布线控制器_1_beq );
  MIPS_Regifile mips_regifile_1 (
    .Din(RDin), .Clk(CLK), .R1(JRADDR), .R2(MDin), .WE(RegWrite), .W_num(multiplexer_9_out),
    .R1_num(multiplexer_6_out), .R2_num(multiplexer_7_out));
  Multiplexer #(.width(32), .enable("false")) multiplexer_12 (
    .in0(MDin), .in1(multiplexer_10_out), .out(multiplexer_12_out), .sel(\单周期硬布线控制器_1_alu_src ));
  Multiplexer #(.width(32), .enable("false")) multiplexer_13 (
    .in0(multiplexer_16_out), .in1(adder_1_out), .out(multiplexer_13_out), .sel(JAL));
  Multiplexer #(.select(2), .width(32), .enable("false")) multiplexer_14 (
    .in0(normalPC), .in1(32'h30ac), .in2(32'h3158), .in3(32'h3204), .out(realPC), .sel(and_7_out));
  not not_3 (not_3_out, eq);
  and and_14 (and_14_out, not_3_out, \单周期硬布线控制器_1_bne );
  and and_15 (and_15_out, syscall, eq);
  Shifter #(.width(32)) shifter_2 (.in(multiplexer_10_out), .\dist (5'b00010), .out(shifter_2_out));
  Decoder #(.select(2), .enable("false")) decoder_3 (
    .out1(decoder_3_out1), .out2(decoder_3_out2), .out3(decoder_3_out3), .sel(load));  // open: out0
  Register #(.width(32)) register_1 (.D(normalPC), .en(and_10_out), .Q(register_1_q), .clk(CLK));  // open: clr
  Register #(.width(32)) register_2 (.D(normalPC), .en(and_11_out), .Q(register_2_q), .clk(CLK));  // open: clr
  Register #(.width(32)) register_3 (.D(normalPC), .en(and_12_out), .Q(register_3_q), .clk(CLK));  // open: clr
  or or_13 (or_13_out, and_13_out, and_14_out);
  Register #(.width(32)) PC_2 (.D(MDin), .en(and_15_out), .Q(LedData), .clk(CLK));  // open: clr
  Multiplexer #(.width(32), .enable("false")) multiplexer_15 (
    .in0(multiplexer_12_out), .in1(32'h22), .out(multiplexer_15_out), .sel(syscall));
  Adder #(.width(32)) adder_2 (.a(shifter_2_out), .b(adder_1_out), .out(adder_2_out));  // open: cin, cout
  Multiplexer #(.width(32), .enable("false")) multiplexer_16 (
    .in0({multiplexer_21_out_2, multiplexer_21_out}), .in1({{16{1'b0}}, multiplexer_19_out}),
    .out(multiplexer_16_out), .sel(comparator_6_eq));
  or or_14 (or_14_out, or_13_out, and_19_out);
  MIPS_ALU mips_alu_1 (
    .X(JRADDR), .Y(multiplexer_15_out), .AluOP(\单周期硬布线控制器_1_alu_op ), .Equal(eq),
    .Result({mips_alu_1_result[21:2], mips_alu_1_result_2, mips_alu_1_result[1:0]}), .shamt(IR[10:6]));  // open: Result_2
  Comparator #(.width(6), .mode("unsigned")) comparator_6 (
    .a(IR[31:26]), .b(6'b100101), .eq(comparator_6_eq));  // open: gt, lt
  and and_16 (and_16_out, Interupt, decoder_3_out1);
  and and_17 (and_17_out, Interupt, decoder_3_out2);
  and and_18 (and_18_out, Interupt, decoder_3_out3);
  Multiplexer #(.select(2), .width(32), .enable("false")) multiplexer_17 (
    .in1(register_1_q), .in2(register_2_q), .in3(register_3_q), .out(EPCtoPC), .sel(cur_IR));  // open: in0
  and and_19 (and_19_out, comparator_7_eq, mips_alu_1_result[0]);
  Comparator #(.width(6), .mode("unsigned")) comparator_7 (
    .a(IR[31:26]), .b(6'b000001), .eq(comparator_7_eq));  // open: gt, lt
  Adder #(.width(2)) adder_3 (.a(cur), .b(multiplexer_18_out), .out(adder_3_out));  // open: cin, cout
  Multiplexer #(.width(2), .enable("false")) multiplexer_18 (
    .in0(2'b11), .in1(2'b01), .out(multiplexer_18_out), .sel(Interupt));
  Register #(.width(2)) register_4 (.D(IRX), .en(and_16_out), .Q(register_4_q), .clk(CLK));  // open: clr
  Register #(.width(2)) register_5 (.D(IRX), .en(and_17_out), .Q(register_5_q), .clk(CLK));  // open: clr
  Register #(.width(2)) register_6 (.D(IRX), .en(and_18_out), .Q(register_6_q), .clk(CLK));  // open: clr
  Multiplexer #(.width(16), .enable("false")) multiplexer_19 (
    .in0(multiplexer_21_out), .in1(multiplexer_21_out_2), .out(multiplexer_19_out), .sel(IR[1]));
  or or_15 (or_15_out, Interupt, ERET);
  RAM #(.addrWidth(10), .dataWidth(32), .bus("separate")) ram_1 (
    .addr(mips_alu_1_result_2), .din(MDin), .data(ram_1_data), .str(MemWrite), .sel(1'b1), .clk(CLK));  // open: ld, clr
  Register #(.width(2)) register_7 (.D(adder_3_out), .en(or_15_out), .Q(cur), .clk(CLK));  // open: clr
  Multiplexer #(.select(2), .width(2), .enable("false")) multiplexer_20 (
    .in0(2'b00), .in1(register_4_q), .in2(register_5_q), .in3(register_6_q), .out(cur_IR), .sel(cur));
  Multiplexer #(.width(32), .enable("false")) multiplexer_21 (
    .in0({mips_alu_1_result[21:2], mips_alu_1_result_2, mips_alu_1_result[1:0]}), .in1(ram_1_data),
    .out({multiplexer_21_out_2, multiplexer_21_out}), .sel(\单周期硬布线控制器_1_memtoreg ));
  Comparator #(.width(2), .mode("unsigned")) comparator_8 (.a(cur_IR), .b(IRX), .lt(lower));  // open: gt, eq
  Adder #(.width(2)) adder_4 (.a(cur), .b(2'b01), .out(load));  // open: cin, cout
  // AND_Gate and_20 is placed but not wired

  // Other names for the same wires on the sheet: OP[5:0] = IR[31:26]; mw = MemWrite

  // Notes on the sheet:
  //   中断源
  //   中断等待指示
  //   总复位信号应将除ROM以外所有存储组件全部清零
  //   数码管输出
  //   数码管输出应该用寄存器锁存，否则显示数据只能一闪而过
  //   Reset 
  //   Reset 
  //   Reset 
  //   指令存储器
  //   contents of rom_1 (hex, n*v repeats v):
  //   201d07d0 20100001 109fc0 139fc3 8021 2012000c 24160008 26100001 3210000f 20080008 20090001 139900
  //   2709825 132020 20020022 c 1094022 1500fff9 22100001 2018000f 2188024 108700 20080008 20090001 139902
  //   2709825 132021 20020022 c 1094022 1500fff9 108702 2c9b022 12c00001 8000c07 4020 1084027 84400
  //   3508ffff 82021 20020022 c 8000c01 afa20000 23bd0004 afa40000 23bd0004 afb00000 23bd0004 afb30000
  //   23bd0004 afb40000 23bd0004 afb50000 23bd0004 afb60000 23bd0004 40000000 20160001 20140003 20150001
  //   168020 108100 2149825 132020 20020022 c 1600fffa 295a022 1680fff7 40800000 23bdfffc 8fb60000
  //   23bdfffc 8fb50000 23bdfffc 8fb40000 23bdfffc 8fb30000 23bdfffc 8fb00000 23bdfffc 8fa40000 23bdfffc
  //   8fa20000 42000018 afa20000 23bd0004 afa40000 23bd0004 afb00000 23bd0004 afb30000 23bd0004 afb40000
  //   23bd0004 afb50000 23bd0004 afb60000 23bd0004 40000000 20160002 20140003 20150001 168020 108100
  //   2149825 132020 20020022 c 1600fffa 295a022 1680fff7 40800000 23bdfffc 8fb60000 23bdfffc 8fb50000
  //   23bdfffc 8fb40000 23bdfffc 8fb30000 23bdfffc 8fb00000 23bdfffc 8fa40000 23bdfffc 8fa20000 42000018
  //   afa20000 23bd0004 afa40000 23bd0004 afb00000 23bd0004 afb30000 23bd0004 afb40000 23bd0004 afb50000
  //   23bd0004 afb60000 23bd0004 40000000 20160003 20140003 20150001 168020 108100 2149825 132020 20020022
  //   c 1600fffa 295a022 1680fff7 40800000 23bdfffc 8fb60000 23bdfffc 8fb50000 23bdfffc 8fb40000 23bdfffc
  //   8fb30000 23bdfffc 8fb00000 23bdfffc 8fa40000 23bdfffc 8fa20000 42000018
  //   rs
  //   指令字
  //   rt
  //   rd
  //   为方便自动评测，需要输出PC，IR，寄存器堆写如数据RDin
  //   JMP
  //   JR
  //   OP
  //   Func
  //   RAM写使能MemWrite、RAM写入数据MDin等信号
  //   Beq
  //   Bne
  //   MemToReg
  //   MemWrite
  //   AluOP
  //   AluSrcB
  //   RegWrite
  //   JAL
  //   RegDst
  //   Syscall
endmodule

// 单周期硬布线控制器
module \单周期硬布线控制器  (
  input  [5:0] OP,
  input  [5:0] Func,
  output [3:0] ALU_OP,
  output MemToReg,
  output MemWrite,
  output ALU_SRC,
  output RegWrite,
  output SysCALL,
  output SignedExt,
  output RegDst,
  output Beq,
  output Bne,
  output JR,
  output JMP,
  output JAL
);

  \运算控制器自动生成  \u_运算控制器自动生成_1  (
    .OP0(OP[0]), .OP1(OP[1]), .OP2(OP[2]), .OP3(OP[3]), .OP4(OP[4]), .OP5(OP[5]), .F0(Func[0]), .F1(Func[1]),
    .F2(Func[2]), .F3(Func[3]), .F4(Func[4]), .F5(Func[5]), .S0(ALU_OP[0]), .S1(ALU_OP[1]), .S2(ALU_OP[2]),
    .S3(ALU_OP[3]));
  \控制信号自动生成  \u_控制信号自动生成_1  (
    .OP0(OP[0]), .OP1(OP[1]), .OP2(OP[2]), .OP3(OP[3]), .OP4(OP[4]), .OP5(OP[5]), .F0(Func[0]), .F1(Func[1]),
    .F2(Func[2]), .F3(Func[3]), .F4(Func[4]), .F5(Func[5]), .MemToReg(MemToReg), .MemWrite(MemWrite),
    .ALU_SRC(ALU_SRC), .RegWrite(RegWrite), .SysCALL(SysCALL), .SignedExt(SignedExt), .RegDst(RegDst),
    .BEQ(Beq), .BNE(Bne), .JR(JR), .JUMP(JMP), .JAL(JAL));

  // Other names for the same wires on the sheet: OP_CODE[5:0] = OP

  // Notes on the sheet:
  //   运算器控制器，根据指令生成运算器功能选择信号
  //   控制信号生成，产生数据通路需要的其他控制信号
endmodule

// 运算器控制器
module \运算控制器自动生成  (
  input  OP0,
  input  OP1,
  input  OP2,
  input  OP3,
  input  OP4,
  input  OP5,
  input  F0,
  input  F1,
  input  F2,
  input  F3,
  input  F4,
  input  F5,
  output S0,
  output S1,
  output S2,
  output S3
);

  wire and_1_out, and_2_out, and_3_out, and_4_out, and_5_out, and_6_out, and_7_out, and_8_out, and_9_out,
       and_10_out, and_11_out, and_12_out, and_13_out, and_14_out, and_15_out, and_16_out, and_17_out,
       and_18_out, and_19_out, and_20_out, and_21_out, and_22_out, and_23_out, and_24_out, and_25_out,
       and_26_out, and_27_out, and_28_out, and_29_out, and_30_out, and_31_out, and_32_out, and_33_out,
       and_34_out, and_35_out, and_36_out, and_37_out, and_38_out, and_39_out, and_40_out, and_41_out,
       and_42_out, and_43_out, and_44_out, and_45_out, and_46_out, and_47_out, and_48_out, not_1_out,
       not_2_out, not_3_out, not_4_out, not_5_out, not_6_out, not_7_out, not_8_out, not_9_out, not_10_out,
       not_11_out, not_12_out, not_13_out, not_14_out, not_15_out, not_16_out, not_17_out, not_18_out,
       not_19_out, not_20_out, not_21_out, not_22_out, not_23_out, not_24_out, not_25_out, not_26_out,
       not_27_out, not_28_out, not_29_out, not_30_out, not_31_out, not_32_out, not_33_out, not_34_out,
       not_35_out, not_36_out, not_37_out, not_38_out, not_39_out, not_40_out, not_41_out, not_42_out,
       not_43_out, not_44_out, not_45_out, not_46_out, not_47_out, not_48_out, not_49_out, not_50_out,
       not_51_out, not_52_out, not_53_out, not_54_out, not_55_out, not_56_out, not_57_out, not_58_out,
       not_59_out, not_60_out, not_61_out, not_62_out, not_63_out, not_64_out, not_65_out, not_66_out,
       not_67_out, not_68_out, not_69_out, not_70_out, not_71_out, not_72_out, not_73_out, not_74_out,
       not_75_out, not_76_out, not_77_out, not_78_out, not_79_out, not_80_out, not_81_out, not_82_out,
       not_83_out, not_84_out, not_85_out, not_86_out, not_87_out, not_88_out, not_89_out, not_90_out,
       not_91_out, not_92_out, not_93_out, not_94_out, not_95_out, not_96_out, not_97_out, not_98_out,
       not_99_out, not_100_out, not_101_out, not_102_out, not_103_out, not_104_out, not_105_out, not_106_out,
       not_107_out, not_108_out, not_109_out, not_110_out, not_111_out, not_112_out, not_113_out,
       not_114_out, not_115_out, not_116_out, not_117_out, not_118_out, not_119_out, not_120_out,
       not_121_out, not_122_out, not_123_out, not_124_out, not_125_out, not_126_out, not_127_out,
       not_128_out, not_129_out, not_130_out, not_131_out, not_132_out, not_133_out, not_134_out,
       not_135_out, not_136_out, not_137_out, not_138_out, not_139_out, not_140_out, not_141_out,
       not_142_out, not_143_out, not_144_out, not_145_out, not_146_out, not_147_out, not_148_out,
       not_149_out, not_150_out, not_151_out, not_152_out, not_153_out, not_154_out, not_155_out,
       not_156_out, not_157_out, not_158_out, not_159_out, not_160_out, not_161_out, not_162_out,
       not_163_out, not_164_out, not_165_out, not_166_out, not_167_out, not_168_out, not_169_out,
       not_170_out, not_171_out, not_172_out, not_173_out, not_174_out, not_175_out, not_176_out,
       not_177_out, not_178_out, not_179_out, not_180_out, not_181_out, not_182_out, not_183_out,
       not_184_out, not_185_out, not_186_out, not_187_out, not_188_out, not_189_out, not_190_out,
       not_191_out, not_192_out, not_193_out, not_194_out, not_195_out, not_196_out, not_197_out,
       not_198_out, not_199_out, not_200_out, not_201_out, not_202_out, not_203_out, not_204_out,
       not_205_out, not_206_out, not_207_out, not_208_out, not_209_out, not_210_out, not_211_out,
       not_212_out, not_213_out, not_214_out, not_215_out, not_216_out, not_217_out, not_218_out,
       not_219_out, not_220_out, not_221_out, not_222_out, not_223_out, not_224_out, not_225_out,
       not_226_out, not_227_out, not_228_out, not_229_out, not_230_out, not_231_out, not_232_out,
       not_233_out, not_234_out, not_235_out, not_236_out, not_237_out, not_238_out, not_239_out,
       not_240_out, not_241_out, not_242_out, not_243_out, not_244_out, not_245_out, not_246_out,
       not_247_out, not_248_out, not_249_out, not_250_out, not_251_out, not_252_out, not_253_out,
       not_254_out, not_255_out, not_256_out, not_257_out, not_258_out, not_259_out, not_260_out,
       not_261_out, not_262_out, not_263_out, not_264_out, not_265_out, not_266_out, not_267_out,
       not_268_out, not_269_out, not_270_out, not_271_out, not_272_out, not_273_out, not_274_out,
       not_275_out, not_276_out, not_277_out, not_278_out, not_279_out, not_280_out, not_281_out,
       not_282_out, not_283_out, not_284_out, not_285_out, not_286_out, not_287_out, not_288_out,
       not_289_out, not_290_out, not_291_out, not_292_out, not_293_out;

  not not_1 (not_1_out, OP5);
  not not_2 (not_2_out, OP4);
  not not_3 (not_3_out, OP3);
  not not_4 (not_4_out, OP2);
  not not_5 (not_5_out, OP1);
  not not_6 (not_6_out, OP0);
  not not_7 (not_7_out, F5);
  not not_8 (not_8_out, F4);
  not not_9 (not_9_out, F3);
  not not_10 (not_10_out, F2);
  not not_11 (not_11_out, OP5);
  not not_12 (not_12_out, OP4);
  not not_13 (not_13_out, OP3);
  not not_14 (not_14_out, OP2);
  not not_15 (not_15_out, OP1);
  not not_16 (not_16_out, OP0);
  not not_17 (not_17_out, F4);
  not not_18 (not_18_out, F3);
  not not_19 (not_19_out, F2);
  not not_20 (not_20_out, F1);
  not not_21 (not_21_out, F0);
  not not_22 (not_22_out, OP5);
  not not_23 (not_23_out, OP4);
  not not_24 (not_24_out, OP3);
  not not_25 (not_25_out, OP2);
  not not_26 (not_26_out, OP1);
  not not_27 (not_27_out, OP0);
  not not_28 (not_28_out, F4);
  not not_29 (not_29_out, F3);
  not not_30 (not_30_out, F2);
  not not_31 (not_31_out, F1);
  not not_32 (not_32_out, OP5);
  not not_33 (not_33_out, OP4);
  not not_34 (not_34_out, OP3);
  not not_35 (not_35_out, OP2);
  not not_36 (not_36_out, OP1);
  not not_37 (not_37_out, OP0);
  not not_38 (not_38_out, F4);
  not not_39 (not_39_out, F3);
  not not_40 (not_40_out, F1);
  not not_41 (not_41_out, F0);
  not not_42 (not_42_out, OP5);
  not not_43 (not_43_out, OP4);
  not not_44 (not_44_out, OP3);
  not not_45 (not_45_out, OP2);
  not not_46 (not_46_out, OP1);
  not not_47 (not_47_out, OP0);
  not not_48 (not_48_out, F4);
  not not_49 (not_49_out, F2);
  not not_50 (not_50_out, F0);
  not not_51 (not_51_out, OP5);
  not not_52 (not_52_out, OP4);
  not not_53 (not_53_out, OP3);
  not not_54 (not_54_out, OP1);
  not not_55 (not_55_out, OP0);
  not not_56 (not_56_out, OP5);
  not not_57 (not_57_out, OP4);
  not not_58 (not_58_out, OP3);
  not not_59 (not_59_out, OP1);
  not not_60 (not_60_out, OP5);
  not not_61 (not_61_out, OP4);
  not not_62 (not_62_out, OP2);
  not not_63 (not_63_out, OP1);
  not not_64 (not_64_out, OP0);
  not not_65 (not_65_out, OP5);
  not not_66 (not_66_out, OP4);
  not not_67 (not_67_out, OP1);
  not not_68 (not_68_out, OP0);
  not not_69 (not_69_out, OP5);
  not not_70 (not_70_out, OP4);
  not not_71 (not_71_out, OP2);
  not not_72 (not_72_out, OP1);
  not not_73 (not_73_out, OP5);
  not not_74 (not_74_out, OP4);
  not not_75 (not_75_out, OP2);
  not not_76 (not_76_out, OP0);
  not not_77 (not_77_out, OP4);
  not not_78 (not_78_out, OP3);
  not not_79 (not_79_out, OP2);
  not not_80 (not_80_out, OP4);
  not not_81 (not_81_out, OP2);
  not not_82 (not_82_out, OP5);
  not not_83 (not_83_out, OP4);
  not not_84 (not_84_out, OP2);
  not not_85 (not_85_out, OP4);
  not not_86 (not_86_out, OP3);
  not not_87 (not_87_out, OP1);
  not not_88 (not_88_out, OP5);
  not not_89 (not_89_out, OP4);
  not not_90 (not_90_out, OP3);
  not not_91 (not_91_out, OP2);
  not not_92 (not_92_out, OP1);
  not not_93 (not_93_out, OP5);
  not not_94 (not_94_out, OP4);
  not not_95 (not_95_out, OP3);
  not not_96 (not_96_out, OP2);
  not not_97 (not_97_out, OP1);
  not not_98 (not_98_out, OP0);
  not not_99 (not_99_out, F5);
  not not_100 (not_100_out, F4);
  not not_101 (not_101_out, F3);
  not not_102 (not_102_out, F2);
  not not_103 (not_103_out, F0);
  not not_104 (not_104_out, OP5);
  not not_105 (not_105_out, OP4);
  not not_106 (not_106_out, OP3);
  not not_107 (not_107_out, OP2);
  not not_108 (not_108_out, OP1);
  not not_109 (not_109_out, OP0);
  not not_110 (not_110_out, F4);
  not not_111 (not_111_out, F3);
  not not_112 (not_112_out, F2);
  not not_113 (not_113_out, F0);
  not not_114 (not_114_out, OP5);
  not not_115 (not_115_out, OP4);
  not not_116 (not_116_out, OP3);
  not not_117 (not_117_out, OP2);
  not not_118 (not_118_out, OP1);
  not not_119 (not_119_out, OP0);
  not not_120 (not_120_out, F4);
  not not_121 (not_121_out, F3);
  not not_122 (not_122_out, F1);
  not not_123 (not_123_out, F0);
  not not_124 (not_124_out, OP5);
  not not_125 (not_125_out, OP4);
  not not_126 (not_126_out, OP3);
  not not_127 (not_127_out, OP2);
  not not_128 (not_128_out, OP1);
  not not_129 (not_129_out, OP0);
  not not_130 (not_130_out, F4);
  not not_131 (not_131_out, F3);
  not not_132 (not_132_out, OP5);
  not not_133 (not_133_out, OP4);
  not not_134 (not_134_out, OP3);
  not not_135 (not_135_out, OP2);
  not not_136 (not_136_out, OP1);
  not not_137 (not_137_out, OP0);
  not not_138 (not_138_out, F4);
  not not_139 (not_139_out, F2);
  not not_140 (not_140_out, F0);
  not not_141 (not_141_out, OP5);
  not not_142 (not_142_out, OP4);
  not not_143 (not_143_out, OP3);
  not not_144 (not_144_out, OP1);
  not not_145 (not_145_out, OP0);
  not not_146 (not_146_out, OP5);
  not not_147 (not_147_out, OP4);
  not not_148 (not_148_out, OP3);
  not not_149 (not_149_out, OP1);
  not not_150 (not_150_out, OP5);
  not not_151 (not_151_out, OP4);
  not not_152 (not_152_out, OP1);
  not not_153 (not_153_out, OP0);
  not not_154 (not_154_out, OP5);
  not not_155 (not_155_out, OP4);
  not not_156 (not_156_out, OP2);
  not not_157 (not_157_out, OP0);
  not not_158 (not_158_out, OP5);
  not not_159 (not_159_out, OP4);
  not not_160 (not_160_out, OP2);
  not not_161 (not_161_out, OP5);
  not not_162 (not_162_out, OP4);
  not not_163 (not_163_out, OP3);
  not not_164 (not_164_out, OP2);
  not not_165 (not_165_out, OP1);
  not not_166 (not_166_out, OP5);
  not not_167 (not_167_out, OP4);
  not not_168 (not_168_out, OP3);
  not not_169 (not_169_out, OP2);
  not not_170 (not_170_out, OP1);
  not not_171 (not_171_out, OP0);
  not not_172 (not_172_out, F4);
  not not_173 (not_173_out, F3);
  not not_174 (not_174_out, F2);
  not not_175 (not_175_out, F1);
  not not_176 (not_176_out, F0);
  not not_177 (not_177_out, OP5);
  not not_178 (not_178_out, OP4);
  not not_179 (not_179_out, OP3);
  not not_180 (not_180_out, OP2);
  not not_181 (not_181_out, OP1);
  not not_182 (not_182_out, OP0);
  not not_183 (not_183_out, F4);
  not not_184 (not_184_out, F3);
  not not_185 (not_185_out, F2);
  not not_186 (not_186_out, F1);
  not not_187 (not_187_out, OP5);
  not not_188 (not_188_out, OP4);
  not not_189 (not_189_out, OP3);
  not not_190 (not_190_out, OP2);
  not not_191 (not_191_out, OP1);
  not not_192 (not_192_out, OP0);
  not not_193 (not_193_out, F4);
  not not_194 (not_194_out, F3);
  not not_195 (not_195_out, F2);
  not not_196 (not_196_out, F0);
  not not_197 (not_197_out, OP5);
  not not_198 (not_198_out, OP4);
  not not_199 (not_199_out, OP3);
  not not_200 (not_200_out, OP2);
  not not_201 (not_201_out, OP1);
  not not_202 (not_202_out, OP0);
  not not_203 (not_203_out, F4);
  not not_204 (not_204_out, F3);
  not not_205 (not_205_out, F1);
  not not_206 (not_206_out, F0);
  not not_207 (not_207_out, OP5);
  not not_208 (not_208_out, OP4);
  not not_209 (not_209_out, OP3);
  not not_210 (not_210_out, OP2);
  not not_211 (not_211_out, OP1);
  not not_212 (not_212_out, OP0);
  not not_213 (not_213_out, F4);
  not not_214 (not_214_out, F2);
  not not_215 (not_215_out, OP5);
  not not_216 (not_216_out, OP4);
  not not_217 (not_217_out, OP2);
  not not_218 (not_218_out, OP1);
  not not_219 (not_219_out, OP0);
  not not_220 (not_220_out, OP5);
  not not_221 (not_221_out, OP4);
  not not_222 (not_222_out, OP1);
  not not_223 (not_223_out, OP0);
  not not_224 (not_224_out, OP5);
  not not_225 (not_225_out, OP4);
  not not_226 (not_226_out, OP2);
  not not_227 (not_227_out, OP1);
  not not_228 (not_228_out, OP4);
  not not_229 (not_229_out, OP3);
  not not_230 (not_230_out, OP2);
  not not_231 (not_231_out, OP4);
  not not_232 (not_232_out, OP2);
  not not_233 (not_233_out, OP4);
  not not_234 (not_234_out, OP3);
  not not_235 (not_235_out, OP1);
  not not_236 (not_236_out, OP5);
  not not_237 (not_237_out, OP4);
  not not_238 (not_238_out, OP3);
  not not_239 (not_239_out, OP2);
  not not_240 (not_240_out, OP1);
  not not_241 (not_241_out, OP0);
  not not_242 (not_242_out, F4);
  not not_243 (not_243_out, F3);
  not not_244 (not_244_out, F1);
  not not_245 (not_245_out, OP5);
  not not_246 (not_246_out, OP4);
  not not_247 (not_247_out, OP3);
  not not_248 (not_248_out, OP2);
  not not_249 (not_249_out, OP1);
  not not_250 (not_250_out, OP0);
  not not_251 (not_251_out, F4);
  not not_252 (not_252_out, F3);
  not not_253 (not_253_out, OP5);
  not not_254 (not_254_out, OP4);
  not not_255 (not_255_out, OP3);
  not not_256 (not_256_out, OP2);
  not not_257 (not_257_out, OP1);
  not not_258 (not_258_out, OP0);
  not not_259 (not_259_out, F4);
  not not_260 (not_260_out, F2);
  not not_261 (not_261_out, F0);
  not not_262 (not_262_out, OP5);
  not not_263 (not_263_out, OP4);
  not not_264 (not_264_out, OP3);
  not not_265 (not_265_out, OP2);
  not not_266 (not_266_out, OP1);
  not not_267 (not_267_out, OP0);
  not not_268 (not_268_out, F4);
  not not_269 (not_269_out, F2);
  not not_270 (not_270_out, OP5);
  not not_271 (not_271_out, OP4);
  not not_272 (not_272_out, OP3);
  not not_273 (not_273_out, OP1);
  not not_274 (not_274_out, OP0);
  not not_275 (not_275_out, OP5);
  not not_276 (not_276_out, OP4);
  not not_277 (not_277_out, OP3);
  not not_278 (not_278_out, OP1);
  not not_279 (not_279_out, OP5);
  not not_280 (not_280_out, OP4);
  not not_281 (not_281_out, OP2);
  not not_282 (not_282_out, OP0);
  not not_283 (not_283_out, OP5);
  not not_284 (not_284_out, OP4);
  not not_285 (not_285_out, OP1);
  not not_286 (not_286_out, OP5);
  not not_287 (not_287_out, OP4);
  not not_288 (not_288_out, OP2);
  not not_289 (not_289_out, OP5);
  not not_290 (not_290_out, OP4);
  not not_291 (not_291_out, OP3);
  not not_292 (not_292_out, OP2);
  not not_293 (not_293_out, OP1);
  and and_1 (and_1_out, not_1_out, not_2_out, not_3_out, not_4_out, not_5_out, not_6_out, not_7_out, not_8_out, not_9_out, not_10_out, F1, F0);
  and and_2 (and_2_out, not_11_out, not_12_out, not_13_out, not_14_out, not_15_out, not_16_out, F5, not_17_out, not_18_out, not_19_out, not_20_out, not_21_out);
  and and_3 (and_3_out, not_22_out, not_23_out, not_24_out, not_25_out, not_26_out, not_27_out, F5, not_28_out, not_29_out, not_30_out, not_31_out, F0);
  and and_4 (and_4_out, not_32_out, not_33_out, not_34_out, not_35_out, not_36_out, not_37_out, F5, not_38_out, not_39_out, F2, not_40_out, not_41_out);
  and and_5 (and_5_out, not_42_out, not_43_out, not_44_out, not_45_out, not_46_out, not_47_out, F5, not_48_out, F3, not_49_out, F1, not_50_out);
  and and_6 (and_6_out, not_51_out, not_52_out, not_53_out, OP2, not_54_out, not_55_out);
  and and_7 (and_7_out, not_56_out, not_57_out, not_58_out, OP2, not_59_out, OP0);
  and and_8 (and_8_out, not_60_out, not_61_out, OP3, not_62_out, not_63_out, not_64_out);
  and and_9 (and_9_out, not_65_out, not_66_out, OP3, OP2, not_67_out, not_68_out);
  and and_10 (and_10_out, not_69_out, not_70_out, OP3, not_71_out, not_72_out, OP0);
  and and_11 (and_11_out, not_73_out, not_74_out, OP3, not_75_out, OP1, not_76_out);
  and and_12 (and_12_out, OP5, not_77_out, not_78_out, not_79_out, OP1, OP0);
  and and_13 (and_13_out, OP5, not_80_out, OP3, not_81_out, OP1, OP0);
  and and_14 (and_14_out, not_82_out, not_83_out, OP3, not_84_out, OP1, OP0);
  and and_15 (and_15_out, OP5, not_85_out, not_86_out, OP2, not_87_out, OP0);
  and and_16 (and_16_out, not_88_out, not_89_out, not_90_out, not_91_out, not_92_out, OP0);
  and and_17 (and_17_out, not_93_out, not_94_out, not_95_out, not_96_out, not_97_out, not_98_out, not_99_out, not_100_out, not_101_out, not_102_out, F1, not_103_out);
  and and_18 (and_18_out, not_104_out, not_105_out, not_106_out, not_107_out, not_108_out, not_109_out, F5, not_110_out, not_111_out, not_112_out, F1, not_113_out);
  and and_19 (and_19_out, not_114_out, not_115_out, not_116_out, not_117_out, not_118_out, not_119_out, F5, not_120_out, not_121_out, F2, not_122_out, not_123_out);
  and and_20 (and_20_out, not_124_out, not_125_out, not_126_out, not_127_out, not_128_out, not_129_out, F5, not_130_out, not_131_out, F2, F1, F0);
  and and_21 (and_21_out, not_132_out, not_133_out, not_134_out, not_135_out, not_136_out, not_137_out, F5, not_138_out, F3, not_139_out, F1, not_140_out);
  and and_22 (and_22_out, not_141_out, not_142_out, not_143_out, OP2, not_144_out, not_145_out);
  and and_23 (and_23_out, not_146_out, not_147_out, not_148_out, OP2, not_149_out, OP0);
  and and_24 (and_24_out, not_150_out, not_151_out, OP3, OP2, not_152_out, not_153_out);
  and and_25 (and_25_out, not_154_out, not_155_out, OP3, not_156_out, OP1, not_157_out);
  and and_26 (and_26_out, not_158_out, not_159_out, OP3, not_160_out, OP1, OP0);
  and and_27 (and_27_out, not_161_out, not_162_out, not_163_out, not_164_out, not_165_out, OP0);
  and and_28 (and_28_out, not_166_out, not_167_out, not_168_out, not_169_out, not_170_out, not_171_out, F5, not_172_out, not_173_out, not_174_out, not_175_out, not_176_out);
  and and_29 (and_29_out, not_177_out, not_178_out, not_179_out, not_180_out, not_181_out, not_182_out, F5, not_183_out, not_184_out, not_185_out, not_186_out, F0);
  and and_30 (and_30_out, not_187_out, not_188_out, not_189_out, not_190_out, not_191_out, not_192_out, F5, not_193_out, not_194_out, not_195_out, F1, not_196_out);
  and and_31 (and_31_out, not_197_out, not_198_out, not_199_out, not_200_out, not_201_out, not_202_out, F5, not_203_out, not_204_out, F2, not_205_out, not_206_out);
  and and_32 (and_32_out, not_207_out, not_208_out, not_209_out, not_210_out, not_211_out, not_212_out, F5, not_213_out, F3, not_214_out, F1, F0);
  and and_33 (and_33_out, not_215_out, not_216_out, OP3, not_217_out, not_218_out, not_219_out);
  and and_34 (and_34_out, not_220_out, not_221_out, OP3, OP2, not_222_out, not_223_out);
  and and_35 (and_35_out, not_224_out, not_225_out, OP3, not_226_out, not_227_out, OP0);
  and and_36 (and_36_out, OP5, not_228_out, not_229_out, not_230_out, OP1, OP0);
  and and_37 (and_37_out, OP5, not_231_out, OP3, not_232_out, OP1, OP0);
  and and_38 (and_38_out, OP5, not_233_out, not_234_out, OP2, not_235_out, OP0);
  and and_39 (and_39_out, not_236_out, not_237_out, not_238_out, not_239_out, not_240_out, not_241_out, F5, not_242_out, not_243_out, F2, not_244_out, F0);
  and and_40 (and_40_out, not_245_out, not_246_out, not_247_out, not_248_out, not_249_out, not_250_out, F5, not_251_out, not_252_out, F2, F1, F0);
  and and_41 (and_41_out, not_253_out, not_254_out, not_255_out, not_256_out, not_257_out, not_258_out, F5, not_259_out, F3, not_260_out, F1, not_261_out);
  and and_42 (and_42_out, not_262_out, not_263_out, not_264_out, not_265_out, not_266_out, not_267_out, F5, not_268_out, F3, not_269_out, F1, F0);
  and and_43 (and_43_out, not_270_out, not_271_out, not_272_out, OP2, not_273_out, not_274_out);
  and and_44 (and_44_out, not_275_out, not_276_out, not_277_out, OP2, not_278_out, OP0);
  and and_45 (and_45_out, not_279_out, not_280_out, OP3, not_281_out, OP1, not_282_out);
  and and_46 (and_46_out, not_283_out, not_284_out, OP3, OP2, not_285_out, OP0);
  and and_47 (and_47_out, not_286_out, not_287_out, OP3, not_288_out, OP1, OP0);
  and and_48 (and_48_out, not_289_out, not_290_out, not_291_out, not_292_out, not_293_out, OP0);
  or or_1 (S1, and_17_out, and_18_out, and_19_out, and_20_out, and_21_out, and_22_out, and_23_out, and_24_out, and_25_out, and_26_out, and_27_out);
  or or_2 (S2, and_28_out, and_29_out, and_30_out, and_31_out, and_32_out, and_33_out, and_34_out, and_35_out, and_36_out, and_37_out, and_38_out);
  or or_3 (S3, and_39_out, and_40_out, and_41_out, and_42_out, and_43_out, and_44_out, and_45_out, and_46_out, and_47_out, and_48_out);
  or or_4 (S0, and_1_out, and_2_out, and_3_out, and_4_out, and_5_out, and_6_out, and_7_out, and_8_out, and_9_out, and_10_out, and_11_out, and_12_out, and_13_out, and_14_out, and_15_out, and_16_out);
endmodule

// 控制信号生成
module \控制信号自动生成  (
  input  OP0,
  input  OP1,
  input  OP2,
  input  OP3,
  input  OP4,
  input  OP5,
  input  F0,
  input  F1,
  input  F2,
  input  F3,
  input  F4,
  input  F5,
  output MemToReg,
  output MemWrite,
  output ALU_SRC,
  output RegWrite,
  output SysCALL,
  output SignedExt,
  output RegDst,
  output BEQ,
  output BNE,
  output JR,
  output JUMP,
  output JAL
);

  wire and_1_out, and_2_out, and_4_out, and_5_out, and_6_out, and_7_out, and_8_out, and_9_out, and_10_out,
       and_11_out, and_12_out, and_13_out, and_14_out, and_15_out, and_16_out, and_17_out, and_18_out,
       and_19_out, and_20_out, and_21_out, and_22_out, and_23_out, and_24_out, and_25_out, and_26_out,
       and_27_out, and_28_out, and_29_out, and_30_out, and_31_out, and_32_out, and_33_out, and_35_out,
       and_36_out, and_37_out, and_38_out, and_39_out, and_40_out, and_41_out, and_42_out, and_43_out,
       and_44_out, and_45_out, and_46_out, and_47_out, and_48_out, and_49_out, and_50_out, and_51_out,
       and_52_out, and_53_out, and_54_out, and_55_out, and_59_out, and_60_out, and_61_out, not_1_out,
       not_2_out, not_3_out, not_4_out, not_5_out, not_6_out, not_7_out, not_8_out, not_9_out, not_10_out,
       not_11_out, not_12_out, not_13_out, not_14_out, not_15_out, not_16_out, not_17_out, not_18_out,
       not_19_out, not_20_out, not_21_out, not_22_out, not_23_out, not_24_out, not_25_out, not_26_out,
       not_27_out, not_28_out, not_29_out, not_30_out, not_31_out, not_32_out, not_33_out, not_34_out,
       not_35_out, not_36_out, not_37_out, not_38_out, not_39_out, not_40_out, not_41_out, not_42_out,
       not_43_out, not_44_out, not_45_out, not_46_out, not_47_out, not_48_out, not_49_out, not_50_out,
       not_51_out, not_52_out, not_53_out, not_54_out, not_55_out, not_56_out, not_57_out, not_58_out,
       not_59_out, not_60_out, not_61_out, not_62_out, not_63_out, not_64_out, not_65_out, not_66_out,
       not_67_out, not_68_out, not_69_out, not_70_out, not_71_out, not_72_out, not_73_out, not_74_out,
       not_75_out, not_76_out, not_77_out, not_78_out, not_79_out, not_80_out, not_81_out, not_82_out,
       not_83_out, not_84_out, not_85_out, not_86_out, not_87_out, not_88_out, not_89_out, not_90_out,
       not_91_out, not_92_out, not_93_out, not_94_out, not_95_out, not_96_out, not_97_out, not_98_out,
       not_99_out, not_100_out, not_101_out, not_102_out, not_103_out, not_104_out, not_105_out, not_106_out,
       not_107_out, not_108_out, not_109_out, not_110_out, not_111_out, not_112_out, not_113_out,
       not_114_out, not_115_out, not_116_out, not_117_out, not_118_out, not_119_out, not_120_out,
       not_121_out, not_122_out, not_123_out, not_124_out, not_125_out, not_126_out, not_127_out,
       not_128_out, not_129_out, not_130_out, not_131_out, not_132_out, not_133_out, not_134_out,
       not_135_out, not_136_out, not_137_out, not_138_out, not_139_out, not_140_out, not_141_out,
       not_142_out, not_143_out, not_144_out, not_145_out, not_146_out, not_147_out, not_148_out,
       not_149_out, not_150_out, not_151_out, not_152_out, not_153_out, not_154_out, not_155_out,
       not_156_out, not_157_out, not_158_out, not_159_out, not_160_out, not_161_out, not_162_out,
       not_163_out, not_164_out, not_165_out, not_166_out, not_167_out, not_168_out, not_169_out,
       not_170_out, not_171_out, not_172_out, not_173_out, not_174_out, not_175_out, not_176_out,
       not_177_out, not_178_out, not_179_out, not_180_out, not_181_out, not_182_out, not_183_out,
       not_184_out, not_185_out, not_186_out, not_187_out, not_188_out, not_189_out, not_190_out,
       not_191_out, not_192_out, not_193_out, not_194_out, not_195_out, not_196_out, not_197_out,
       not_198_out, not_199_out, not_200_out, not_201_out, not_202_out, not_203_out, not_204_out,
       not_205_out, not_206_out, not_207_out, not_208_out, not_209_out, not_210_out, not_211_out,
       not_212_out, not_213_out, not_214_out, not_215_out, not_216_out, not_217_out, not_218_out,
       not_219_out, not_220_out, not_221_out, not_222_out, not_223_out, not_224_out, not_225_out,
       not_226_out, not_227_out, not_228_out, not_229_out, not_230_out, not_231_out, not_232_out,
       not_233_out, not_234_out, not_235_out, not_236_out, not_237_out, not_238_out, not_239_out,
       not_240_out, not_241_out, not_242_out, not_243_out, not_244_out, not_245_out, not_246_out,
       not_247_out, not_248_out, not_249_out, not_250_out, not_251_out, not_252_out, not_253_out,
       not_254_out, not_255_out, not_256_out, not_257_out, not_258_out, not_259_out, not_260_out,
       not_261_out, not_262_out, not_263_out, not_264_out, not_265_out, not_266_out, not_267_out,
       not_268_out, not_269_out, not_270_out, not_271_out, not_272_out, not_273_out, not_274_out,
       not_275_out, not_276_out, not_277_out, not_278_out, not_279_out, not_280_out, not_281_out,
       not_282_out, not_283_out, not_284_out, not_285_out, not_286_out, not_287_out, not_288_out,
       not_289_out, not_290_out, not_291_out, not_292_out, not_293_out, not_294_out, not_295_out,
       not_296_out, not_297_out, not_298_out, not_299_out, not_300_out, not_301_out, not_302_out,
       not_303_out, not_304_out, not_305_out, not_306_out, not_307_out, not_308_out, not_309_out,
       not_310_out, not_311_out, not_312_out, not_313_out, not_314_out, not_315_out, not_316_out,
       not_317_out, not_318_out, not_319_out, not_320_out, not_321_out, not_322_out, not_323_out,
       not_324_out, not_325_out, not_326_out, not_327_out, not_328_out, not_329_out, not_330_out,
       not_331_out, not_332_out, not_333_out, not_334_out, not_335_out, not_336_out, not_337_out,
       not_338_out, not_339_out, not_340_out, not_341_out, not_342_out, not_343_out, not_344_out,
       not_345_out, not_346_out, not_347_out, not_348_out, not_349_out, not_350_out, not_351_out,
       not_352_out, not_353_out, not_354_out, not_355_out, not_356_out, not_357_out, not_358_out,
       not_359_out, not_360_out, not_361_out, not_362_out, not_363_out, not_364_out, not_365_out,
       not_366_out, not_367_out, not_368_out, not_369_out, not_370_out, not_371_out, not_372_out,
       not_373_out, not_374_out, not_375_out, not_376_out, not_377_out, not_378_out, not_379_out,
       not_380_out, not_381_out, not_382_out;

  not not_1 (not_1_out, OP4);
  not not_2 (not_2_out, OP3);
  not not_3 (not_3_out, OP2);
  not not_4 (not_4_out, OP4);
  not not_5 (not_5_out, OP3);
  not not_6 (not_6_out, OP1);
  not not_7 (not_7_out, OP4);
  not not_8 (not_8_out, OP2);
  not not_9 (not_9_out, OP5);
  not not_10 (not_10_out, OP4);
  not not_11 (not_11_out, OP2);
  not not_12 (not_12_out, OP1);
  not not_13 (not_13_out, OP0);
  not not_14 (not_14_out, OP5);
  not not_15 (not_15_out, OP4);
  not not_16 (not_16_out, OP1);
  not not_17 (not_17_out, OP0);
  not not_18 (not_18_out, OP5);
  not not_19 (not_19_out, OP4);
  not not_20 (not_20_out, OP2);
  not not_21 (not_21_out, OP1);
  not not_22 (not_22_out, OP5);
  not not_23 (not_23_out, OP4);
  not not_24 (not_24_out, OP2);
  not not_25 (not_25_out, OP0);
  not not_26 (not_26_out, OP5);
  not not_27 (not_27_out, OP4);
  not not_28 (not_28_out, OP1);
  not not_29 (not_29_out, OP4);
  not not_30 (not_30_out, OP3);
  not not_31 (not_31_out, OP2);
  not not_32 (not_32_out, OP4);
  not not_33 (not_33_out, OP2);
  not not_34 (not_34_out, OP5);
  not not_35 (not_35_out, OP4);
  not not_36 (not_36_out, OP2);
  not not_37 (not_37_out, OP4);
  not not_38 (not_38_out, OP3);
  not not_39 (not_39_out, OP1);
  not not_40 (not_40_out, OP5);
  not not_41 (not_41_out, OP4);
  not not_42 (not_42_out, OP3);
  not not_43 (not_43_out, OP2);
  not not_44 (not_44_out, OP1);
  not not_45 (not_45_out, OP0);
  not not_46 (not_46_out, F5);
  not not_47 (not_47_out, F4);
  not not_48 (not_48_out, F3);
  not not_49 (not_49_out, F2);
  not not_50 (not_50_out, F1);
  not not_51 (not_51_out, F0);
  not not_52 (not_52_out, OP5);
  not not_53 (not_53_out, OP4);
  not not_54 (not_54_out, OP3);
  not not_55 (not_55_out, OP2);
  not not_56 (not_56_out, OP1);
  not not_57 (not_57_out, OP0);
  not not_58 (not_58_out, F5);
  not not_59 (not_59_out, F4);
  not not_60 (not_60_out, F3);
  not not_61 (not_61_out, F2);
  not not_62 (not_62_out, OP5);
  not not_63 (not_63_out, OP4);
  not not_64 (not_64_out, OP3);
  not not_65 (not_65_out, OP2);
  not not_66 (not_66_out, OP1);
  not not_67 (not_67_out, OP0);
  not not_68 (not_68_out, F5);
  not not_69 (not_69_out, F4);
  not not_70 (not_70_out, F3);
  not not_71 (not_71_out, F2);
  not not_72 (not_72_out, F0);
  not not_73 (not_73_out, OP5);
  not not_74 (not_74_out, OP4);
  not not_75 (not_75_out, OP3);
  not not_76 (not_76_out, OP2);
  not not_77 (not_77_out, OP1);
  not not_78 (not_78_out, OP0);
  not not_79 (not_79_out, F4);
  not not_80 (not_80_out, F3);
  not not_81 (not_81_out, F2);
  not not_82 (not_82_out, F1);
  not not_83 (not_83_out, F0);
  not not_84 (not_84_out, OP5);
  not not_85 (not_85_out, OP4);
  not not_86 (not_86_out, OP3);
  not not_87 (not_87_out, OP2);
  not not_88 (not_88_out, OP1);
  not not_89 (not_89_out, OP0);
  not not_90 (not_90_out, F4);
  not not_91 (not_91_out, F3);
  not not_92 (not_92_out, F2);
  not not_93 (not_93_out, F1);
  not not_94 (not_94_out, OP5);
  not not_95 (not_95_out, OP4);
  not not_96 (not_96_out, OP3);
  not not_97 (not_97_out, OP2);
  not not_98 (not_98_out, OP1);
  not not_99 (not_99_out, OP0);
  not not_100 (not_100_out, F4);
  not not_101 (not_101_out, F3);
  not not_102 (not_102_out, F2);
  not not_103 (not_103_out, F0);
  not not_104 (not_104_out, OP5);
  not not_105 (not_105_out, OP4);
  not not_106 (not_106_out, OP3);
  not not_107 (not_107_out, OP2);
  not not_108 (not_108_out, OP1);
  not not_109 (not_109_out, OP0);
  not not_110 (not_110_out, F4);
  not not_111 (not_111_out, F3);
  not not_112 (not_112_out, F1);
  not not_113 (not_113_out, F0);
  not not_114 (not_114_out, OP5);
  not not_115 (not_115_out, OP4);
  not not_116 (not_116_out, OP3);
  not not_117 (not_117_out, OP2);
  not not_118 (not_118_out, OP1);
  not not_119 (not_119_out, OP0);
  not not_120 (not_120_out, F4);
  not not_121 (not_121_out, F3);
  not not_122 (not_122_out, F1);
  not not_123 (not_123_out, OP5);
  not not_124 (not_124_out, OP4);
  not not_125 (not_125_out, OP3);
  not not_126 (not_126_out, OP2);
  not not_127 (not_127_out, OP1);
  not not_128 (not_128_out, OP0);
  not not_129 (not_129_out, F4);
  not not_130 (not_130_out, F3);
  not not_131 (not_131_out, OP5);
  not not_132 (not_132_out, OP4);
  not not_133 (not_133_out, OP3);
  not not_134 (not_134_out, OP2);
  not not_135 (not_135_out, OP1);
  not not_136 (not_136_out, OP0);
  not not_137 (not_137_out, F4);
  not not_138 (not_138_out, F2);
  not not_139 (not_139_out, F0);
  not not_140 (not_140_out, OP5);
  not not_141 (not_141_out, OP4);
  not not_142 (not_142_out, OP3);
  not not_143 (not_143_out, OP2);
  not not_144 (not_144_out, OP1);
  not not_145 (not_145_out, OP0);
  not not_146 (not_146_out, F4);
  not not_147 (not_147_out, F2);
  not not_148 (not_148_out, OP5);
  not not_149 (not_149_out, OP4);
  not not_150 (not_150_out, OP3);
  not not_151 (not_151_out, OP2);
  not not_152 (not_152_out, OP5);
  not not_153 (not_153_out, OP4);
  not not_154 (not_154_out, OP2);
  not not_155 (not_155_out, OP1);
  not not_156 (not_156_out, OP0);
  not not_157 (not_157_out, OP5);
  not not_158 (not_158_out, OP4);
  not not_159 (not_159_out, OP1);
  not not_160 (not_160_out, OP0);
  not not_161 (not_161_out, OP5);
  not not_162 (not_162_out, OP4);
  not not_163 (not_163_out, OP2);
  not not_164 (not_164_out, OP1);
  not not_165 (not_165_out, OP5);
  not not_166 (not_166_out, OP4);
  not not_167 (not_167_out, OP2);
  not not_168 (not_168_out, OP0);
  not not_169 (not_169_out, OP5);
  not not_170 (not_170_out, OP4);
  not not_171 (not_171_out, OP1);
  not not_172 (not_172_out, OP4);
  not not_173 (not_173_out, OP3);
  not not_174 (not_174_out, OP2);
  not not_175 (not_175_out, OP5);
  not not_176 (not_176_out, OP4);
  not not_177 (not_177_out, OP5);
  not not_178 (not_178_out, OP4);
  not not_179 (not_179_out, OP2);
  not not_180 (not_180_out, OP4);
  not not_181 (not_181_out, OP3);
  not not_182 (not_182_out, OP1);
  not not_183 (not_183_out, OP5);
  not not_184 (not_184_out, OP4);
  not not_185 (not_185_out, OP3);
  not not_186 (not_186_out, OP2);
  not not_187 (not_187_out, OP1);
  not not_188 (not_188_out, OP0);
  not not_189 (not_189_out, F5);
  not not_190 (not_190_out, F4);
  not not_191 (not_191_out, F1);
  not not_192 (not_192_out, F0);
  not not_193 (not_193_out, OP5);
  not not_194 (not_194_out, OP4);
  not not_195 (not_195_out, OP3);
  not not_196 (not_196_out, OP1);
  not not_197 (not_197_out, OP0);
  not not_198 (not_198_out, OP5);
  not not_199 (not_199_out, OP4);
  not not_200 (not_200_out, OP3);
  not not_201 (not_201_out, OP1);
  not not_202 (not_202_out, OP5);
  not not_203 (not_203_out, OP4);
  not not_204 (not_204_out, OP2);
  not not_205 (not_205_out, OP1);
  not not_206 (not_206_out, OP0);
  not not_207 (not_207_out, OP5);
  not not_208 (not_208_out, OP4);
  not not_209 (not_209_out, OP2);
  not not_210 (not_210_out, OP1);
  not not_211 (not_211_out, OP5);
  not not_212 (not_212_out, OP4);
  not not_213 (not_213_out, OP2);
  not not_214 (not_214_out, OP0);
  not not_215 (not_215_out, OP4);
  not not_216 (not_216_out, OP3);
  not not_217 (not_217_out, OP2);
  not not_218 (not_218_out, OP4);
  not not_219 (not_219_out, OP2);
  not not_220 (not_220_out, OP5);
  not not_221 (not_221_out, OP4);
  not not_222 (not_222_out, OP2);
  not not_223 (not_223_out, OP4);
  not not_224 (not_224_out, OP3);
  not not_225 (not_225_out, OP1);
  not not_226 (not_226_out, OP5);
  not not_227 (not_227_out, OP4);
  not not_228 (not_228_out, OP3);
  not not_229 (not_229_out, OP2);
  not not_230 (not_230_out, OP1);
  not not_231 (not_231_out, OP5);
  not not_232 (not_232_out, OP4);
  not not_233 (not_233_out, OP3);
  not not_234 (not_234_out, OP2);
  not not_235 (not_235_out, OP1);
  not not_236 (not_236_out, OP0);
  not not_237 (not_237_out, F5);
  not not_238 (not_238_out, F4);
  not not_239 (not_239_out, F3);
  not not_240 (not_240_out, F2);
  not not_241 (not_241_out, F1);
  not not_242 (not_242_out, F0);
  not not_243 (not_243_out, OP5);
  not not_244 (not_244_out, OP4);
  not not_245 (not_245_out, OP3);
  not not_246 (not_246_out, OP2);
  not not_247 (not_247_out, OP1);
  not not_248 (not_248_out, OP0);
  not not_249 (not_249_out, F5);
  not not_250 (not_250_out, F4);
  not not_251 (not_251_out, F3);
  not not_252 (not_252_out, F2);
  not not_253 (not_253_out, OP5);
  not not_254 (not_254_out, OP4);
  not not_255 (not_255_out, OP3);
  not not_256 (not_256_out, OP2);
  not not_257 (not_257_out, OP1);
  not not_258 (not_258_out, OP0);
  not not_259 (not_259_out, F5);
  not not_260 (not_260_out, F4);
  not not_261 (not_261_out, F3);
  not not_262 (not_262_out, F2);
  not not_263 (not_263_out, F0);
  not not_264 (not_264_out, OP5);
  not not_265 (not_265_out, OP4);
  not not_266 (not_266_out, OP3);
  not not_267 (not_267_out, OP2);
  not not_268 (not_268_out, OP1);
  not not_269 (not_269_out, OP0);
  not not_270 (not_270_out, F4);
  not not_271 (not_271_out, F3);
  not not_272 (not_272_out, F2);
  not not_273 (not_273_out, F1);
  not not_274 (not_274_out, F0);
  not not_275 (not_275_out, OP5);
  not not_276 (not_276_out, OP4);
  not not_277 (not_277_out, OP3);
  not not_278 (not_278_out, OP2);
  not not_279 (not_279_out, OP1);
  not not_280 (not_280_out, OP0);
  not not_281 (not_281_out, F4);
  not not_282 (not_282_out, F3);
  not not_283 (not_283_out, F2);
  not not_284 (not_284_out, F1);
  not not_285 (not_285_out, OP5);
  not not_286 (not_286_out, OP4);
  not not_287 (not_287_out, OP3);
  not not_288 (not_288_out, OP2);
  not not_289 (not_289_out, OP1);
  not not_290 (not_290_out, OP0);
  not not_291 (not_291_out, F4);
  not not_292 (not_292_out, F3);
  not not_293 (not_293_out, F2);
  not not_294 (not_294_out, F0);
  not not_295 (not_295_out, OP5);
  not not_296 (not_296_out, OP4);
  not not_297 (not_297_out, OP3);
  not not_298 (not_298_out, OP2);
  not not_299 (not_299_out, OP1);
  not not_300 (not_300_out, OP0);
  not not_301 (not_301_out, F4);
  not not_302 (not_302_out, F3);
  not not_303 (not_303_out, F1);
  not not_304 (not_304_out, F0);
  not not_305 (not_305_out, OP5);
  not not_306 (not_306_out, OP4);
  not not_307 (not_307_out, OP3);
  not not_308 (not_308_out, OP2);
  not not_309 (not_309_out, OP1);
  not not_310 (not_310_out, OP0);
  not not_311 (not_311_out, F4);
  not not_312 (not_312_out, F3);
  not not_313 (not_313_out, F1);
  not not_314 (not_314_out, OP5);
  not not_315 (not_315_out, OP4);
  not not_316 (not_316_out, OP3);
  not not_317 (not_317_out, OP2);
  not not_318 (not_318_out, OP1);
  not not_319 (not_319_out, OP0);
  not not_320 (not_320_out, F4);
  not not_321 (not_321_out, F3);
  not not_322 (not_322_out, OP5);
  not not_323 (not_323_out, OP4);
  not not_324 (not_324_out, OP3);
  not not_325 (not_325_out, OP2);
  not not_326 (not_326_out, OP1);
  not not_327 (not_327_out, OP0);
  not not_328 (not_328_out, F4);
  not not_329 (not_329_out, F2);
  not not_330 (not_330_out, F0);
  not not_331 (not_331_out, OP5);
  not not_332 (not_332_out, OP4);
  not not_333 (not_333_out, OP3);
  not not_334 (not_334_out, OP2);
  not not_335 (not_335_out, OP1);
  not not_336 (not_336_out, OP0);
  not not_337 (not_337_out, F4);
  not not_338 (not_338_out, F2);
  not not_339 (not_339_out, OP5);
  not not_340 (not_340_out, OP4);
  not not_341 (not_341_out, OP3);
  not not_342 (not_342_out, OP1);
  not not_343 (not_343_out, OP0);
  not not_344 (not_344_out, OP5);
  not not_345 (not_345_out, OP4);
  not not_346 (not_346_out, OP3);
  not not_347 (not_347_out, OP1);
  not not_348 (not_348_out, OP5);
  not not_349 (not_349_out, OP4);
  not not_350 (not_350_out, OP3);
  not not_351 (not_351_out, OP2);
  not not_352 (not_352_out, OP1);
  not not_353 (not_353_out, OP0);
  not not_354 (not_354_out, F5);
  not not_355 (not_355_out, F4);
  not not_356 (not_356_out, F2);
  not not_357 (not_357_out, F1);
  not not_358 (not_358_out, F0);
  not not_359 (not_359_out, OP5);
  not not_360 (not_360_out, OP4);
  not not_361 (not_361_out, OP3);
  not not_362 (not_362_out, OP2);
  not not_363 (not_363_out, OP1);
  not not_364 (not_364_out, OP0);
  not not_365 (not_365_out, F5);
  not not_366 (not_366_out, F4);
  not not_367 (not_367_out, F2);
  not not_368 (not_368_out, F1);
  not not_369 (not_369_out, F0);
  not not_370 (not_370_out, OP5);
  not not_371 (not_371_out, OP4);
  not not_372 (not_372_out, OP3);
  not not_373 (not_373_out, OP2);
  not not_374 (not_374_out, OP0);
  not not_375 (not_375_out, OP5);
  not not_376 (not_376_out, OP4);
  not not_377 (not_377_out, OP3);
  not not_378 (not_378_out, OP2);
  not not_379 (not_379_out, OP5);
  not not_380 (not_380_out, OP4);
  not not_381 (not_381_out, OP3);
  not not_382 (not_382_out, OP2);
  and and_1 (and_1_out, OP5, not_1_out, not_2_out, not_3_out, OP1, OP0);
  and and_2 (and_2_out, OP5, not_4_out, not_5_out, OP2, not_6_out, OP0);
  and and_3 (MemWrite, OP5, not_7_out, OP3, not_8_out, OP1, OP0);
  and and_4 (and_4_out, not_9_out, not_10_out, OP3, not_11_out, not_12_out, not_13_out);
  and and_5 (and_5_out, not_14_out, not_15_out, OP3, OP2, not_16_out, not_17_out);
  and and_6 (and_6_out, not_18_out, not_19_out, OP3, not_20_out, not_21_out, OP0);
  and and_7 (and_7_out, not_22_out, not_23_out, OP3, not_24_out, OP1, not_25_out);
  and and_8 (and_8_out, not_26_out, not_27_out, OP3, OP2, not_28_out, OP0);
  and and_9 (and_9_out, OP5, not_29_out, not_30_out, not_31_out, OP1, OP0);
  and and_10 (and_10_out, OP5, not_32_out, OP3, not_33_out, OP1, OP0);
  and and_11 (and_11_out, not_34_out, not_35_out, OP3, not_36_out, OP1, OP0);
  and and_12 (and_12_out, OP5, not_37_out, not_38_out, OP2, not_39_out, OP0);
  and and_13 (and_13_out, not_40_out, not_41_out, not_42_out, not_43_out, not_44_out, not_45_out, not_46_out, not_47_out, not_48_out, not_49_out, not_50_out, not_51_out);
  and and_14 (and_14_out, not_52_out, not_53_out, not_54_out, not_55_out, not_56_out, not_57_out, not_58_out, not_59_out, not_60_out, not_61_out, F1, F0);
  and and_15 (and_15_out, not_62_out, not_63_out, not_64_out, not_65_out, not_66_out, not_67_out, not_68_out, not_69_out, not_70_out, not_71_out, F1, not_72_out);
  and and_16 (and_16_out, not_73_out, not_74_out, not_75_out, not_76_out, not_77_out, not_78_out, F5, not_79_out, not_80_out, not_81_out, not_82_out, not_83_out);
  and and_17 (and_17_out, not_84_out, not_85_out, not_86_out, not_87_out, not_88_out, not_89_out, F5, not_90_out, not_91_out, not_92_out, not_93_out, F0);
  and and_18 (and_18_out, not_94_out, not_95_out, not_96_out, not_97_out, not_98_out, not_99_out, F5, not_100_out, not_101_out, not_102_out, F1, not_103_out);
  and and_19 (and_19_out, not_104_out, not_105_out, not_106_out, not_107_out, not_108_out, not_109_out, F5, not_110_out, not_111_out, F2, not_112_out, not_113_out);
  and and_20 (and_20_out, not_114_out, not_115_out, not_116_out, not_117_out, not_118_out, not_119_out, F5, not_120_out, not_121_out, F2, not_122_out, F0);
  and and_21 (and_21_out, not_123_out, not_124_out, not_125_out, not_126_out, not_127_out, not_128_out, F5, not_129_out, not_130_out, F2, F1, F0);
  and and_22 (and_22_out, not_131_out, not_132_out, not_133_out, not_134_out, not_135_out, not_136_out, F5, not_137_out, F3, not_138_out, F1, not_139_out);
  and and_23 (and_23_out, not_140_out, not_141_out, not_142_out, not_143_out, not_144_out, not_145_out, F5, not_146_out, F3, not_147_out, F1, F0);
  and and_24 (and_24_out, not_148_out, not_149_out, not_150_out, not_151_out, OP1, OP0);
  and and_25 (and_25_out, not_152_out, not_153_out, OP3, not_154_out, not_155_out, not_156_out);
  and and_26 (and_26_out, not_157_out, not_158_out, OP3, OP2, not_159_out, not_160_out);
  and and_27 (and_27_out, not_161_out, not_162_out, OP3, not_163_out, not_164_out, OP0);
  and and_28 (and_28_out, not_165_out, not_166_out, OP3, not_167_out, OP1, not_168_out);
  and and_29 (and_29_out, not_169_out, not_170_out, OP3, OP2, not_171_out, OP0);
  and and_30 (and_30_out, OP5, not_172_out, not_173_out, not_174_out, OP1, OP0);
  and and_31 (and_31_out, not_175_out, not_176_out, OP3, OP2, OP1, OP0);
  and and_32 (and_32_out, not_177_out, not_178_out, OP3, not_179_out, OP1, OP0);
  and and_33 (and_33_out, OP5, not_180_out, not_181_out, OP2, not_182_out, OP0);
  and and_34 (SysCALL, not_183_out, not_184_out, not_185_out, not_186_out, not_187_out, not_188_out, not_189_out, not_190_out, F3, F2, not_191_out, not_192_out);
  and and_35 (and_35_out, not_193_out, not_194_out, not_195_out, OP2, not_196_out, not_197_out);
  and and_36 (and_36_out, not_198_out, not_199_out, not_200_out, OP2, not_201_out, OP0);
  and and_37 (and_37_out, not_202_out, not_203_out, OP3, not_204_out, not_205_out, not_206_out);
  and and_38 (and_38_out, not_207_out, not_208_out, OP3, not_209_out, not_210_out, OP0);
  and and_39 (and_39_out, not_211_out, not_212_out, OP3, not_213_out, OP1, not_214_out);
  and and_40 (and_40_out, OP5, not_215_out, not_216_out, not_217_out, OP1, OP0);
  and and_41 (and_41_out, OP5, not_218_out, OP3, not_219_out, OP1, OP0);
  and and_42 (and_42_out, not_220_out, not_221_out, OP3, not_222_out, OP1, OP0);
  and and_43 (and_43_out, OP5, not_223_out, not_224_out, OP2, not_225_out, OP0);
  and and_44 (and_44_out, not_226_out, not_227_out, not_228_out, not_229_out, not_230_out, OP0);
  and and_45 (and_45_out, not_231_out, not_232_out, not_233_out, not_234_out, not_235_out, not_236_out, not_237_out, not_238_out, not_239_out, not_240_out, not_241_out, not_242_out);
  and and_46 (and_46_out, not_243_out, not_244_out, not_245_out, not_246_out, not_247_out, not_248_out, not_249_out, not_250_out, not_251_out, not_252_out, F1, F0);
  and and_47 (and_47_out, not_253_out, not_254_out, not_255_out, not_256_out, not_257_out, not_258_out, not_259_out, not_260_out, not_261_out, not_262_out, F1, not_263_out);
  and and_48 (and_48_out, not_264_out, not_265_out, not_266_out, not_267_out, not_268_out, not_269_out, F5, not_270_out, not_271_out, not_272_out, not_273_out, not_274_out);
  and and_49 (and_49_out, not_275_out, not_276_out, not_277_out, not_278_out, not_279_out, not_280_out, F5, not_281_out, not_282_out, not_283_out, not_284_out, F0);
  and and_50 (and_50_out, not_285_out, not_286_out, not_287_out, not_288_out, not_289_out, not_290_out, F5, not_291_out, not_292_out, not_293_out, F1, not_294_out);
  and and_51 (and_51_out, not_295_out, not_296_out, not_297_out, not_298_out, not_299_out, not_300_out, F5, not_301_out, not_302_out, F2, not_303_out, not_304_out);
  and and_52 (and_52_out, not_305_out, not_306_out, not_307_out, not_308_out, not_309_out, not_310_out, F5, not_311_out, not_312_out, F2, not_313_out, F0);
  and and_53 (and_53_out, not_314_out, not_315_out, not_316_out, not_317_out, not_318_out, not_319_out, F5, not_320_out, not_321_out, F2, F1, F0);
  and and_54 (and_54_out, not_322_out, not_323_out, not_324_out, not_325_out, not_326_out, not_327_out, F5, not_328_out, F3, not_329_out, F1, not_330_out);
  and and_55 (and_55_out, not_331_out, not_332_out, not_333_out, not_334_out, not_335_out, not_336_out, F5, not_337_out, F3, not_338_out, F1, F0);
  and and_56 (BEQ, not_339_out, not_340_out, not_341_out, OP2, not_342_out, not_343_out);
  and and_57 (BNE, not_344_out, not_345_out, not_346_out, OP2, not_347_out, OP0);
  and and_58 (JR, not_348_out, not_349_out, not_350_out, not_351_out, not_352_out, not_353_out, not_354_out, not_355_out, F3, not_356_out, not_357_out, not_358_out);
  and and_59 (and_59_out, not_359_out, not_360_out, not_361_out, not_362_out, not_363_out, not_364_out, not_365_out, not_366_out, F3, not_367_out, not_368_out, not_369_out);
  and and_60 (and_60_out, not_370_out, not_371_out, not_372_out, not_373_out, OP1, not_374_out);
  and and_61 (and_61_out, not_375_out, not_376_out, not_377_out, not_378_out, OP1, OP0);
  and and_62 (JAL, not_379_out, not_380_out, not_381_out, not_382_out, OP1, OP0);
  or or_1 (MemToReg, and_1_out, and_2_out);
  or or_2 (ALU_SRC, and_4_out, and_5_out, and_6_out, and_7_out, and_8_out, and_9_out, and_10_out, and_11_out, and_12_out);
  or or_3 (SignedExt, and_35_out, and_36_out, and_37_out, and_38_out, and_39_out, and_40_out, and_41_out, and_42_out, and_43_out, and_44_out);
  or or_4 (RegDst, and_45_out, and_46_out, and_47_out, and_48_out, and_49_out, and_50_out, and_51_out, and_52_out, and_53_out, and_54_out, and_55_out);
  or or_5 (JUMP, and_59_out, and_60_out, and_61_out);
  or or_6 (RegWrite, and_13_out, and_14_out, and_15_out, and_16_out, and_17_out, and_18_out, and_19_out, and_20_out, and_21_out, and_22_out, and_23_out, and_24_out, and_25_out, and_26_out, and_27_out, and_28_out, and_29_out, and_30_out, and_31_out, and_32_out, and_33_out);
endmodule

// ALU
module MIPS_ALU (
  input  [4:0] shamt,
  input  [31:0] X,
  input  [31:0] Y,
  input  [3:0] AluOP,
  output Equal,
  output [31:0] Result,
  output [31:0] Result_2
);

  wire [0:0] comparator_1_lt, comparator_2_lt;
  wire [31:0] adder_1_out, AND_out, divider_1_out, divider_1_rem, multiplier_1_cout, multiplier_1_out,
       NOR_out, OR_out, shifter_1_out, shifter_2_out, shifter_3_out, subtractor_1_out, XOR_out;

  assign AND_out = X & Y;  // AND_Gate AND, 32 bits wide
  assign OR_out = X | Y;  // OR_Gate OR, 32 bits wide
  Shifter #(.width(32)) shifter_1 (.in(Y), .\dist (shamt), .out(shifter_1_out));
  Shifter #(.width(32), .shift("ar")) shifter_2 (.in(Y), .\dist (shamt), .out(shifter_2_out));
  Shifter #(.width(32), .shift("lr")) shifter_3 (.in(Y), .\dist (shamt), .out(shifter_3_out));
  Multiplier #(.width(32)) multiplier_1 (.a(X), .b(Y), .out(multiplier_1_out), .cout(multiplier_1_cout));  // open: cin
  Divider #(.width(32)) divider_1 (.a(X), .b(Y), .out(divider_1_out), .rem(divider_1_rem));  // open: upper
  Adder #(.width(32)) adder_1 (.a(X), .b(Y), .out(adder_1_out));  // open: cin, cout
  Subtractor #(.width(32)) subtractor_1 (.a(X), .b(Y), .out(subtractor_1_out));  // open: bin, bout
  assign XOR_out = X ^ Y;  // XOR_Gate XOR, 32 bits wide
  assign NOR_out = ~(X | Y);  // NOR_Gate NOR, 32 bits wide
  Comparator #(.width(32)) comparator_1 (.a(X), .b(Y), .eq(Equal), .lt(comparator_1_lt[0]));  // open: gt
  Comparator #(.width(32), .mode("unsigned")) comparator_2 (.a(X), .b(Y), .lt(comparator_2_lt[0]));  // open: gt, eq
  Multiplexer #(.select(4), .width(32), .enable("false")) multiplexer_1 (
    .in0(shifter_1_out), .in1(shifter_2_out), .in2(shifter_3_out), .in3(multiplier_1_out),
    .in4(divider_1_out), .in5(adder_1_out), .in6(subtractor_1_out), .in7(AND_out), .in8(OR_out),
    .in9(XOR_out), .in10(NOR_out), .in11({{31{1'b0}}, comparator_1_lt[0]}),
    .in12({{31{1'b0}}, comparator_2_lt[0]}), .in13({32{1'b0}}), .in14({32{1'b0}}), .in15({32{1'b0}}),
    .out(Result), .sel(AluOP));
  Multiplexer #(.select(4), .width(32), .enable("false")) multiplexer_2 (
    .in0({32{1'b0}}), .in1({32{1'b0}}), .in2({32{1'b0}}), .in3(multiplier_1_cout), .in4(divider_1_rem),
    .in5({32{1'b0}}), .in6({32{1'b0}}), .in7({32{1'b0}}), .in8({32{1'b0}}), .in9({32{1'b0}}),
    .in10({32{1'b0}}), .in11({32{1'b0}}), .in12({32{1'b0}}), .in13({32{1'b0}}), .in14({32{1'b0}}),
    .in15({32{1'b0}}), .out(Result_2), .sel(AluOP));

  // Other names for the same wires on the sheet: Result2[31:0] = Result_2; S[3:0] = AluOP

  // Notes on the sheet:
  //   不要改变此引脚区域内容，也不要改变ALU封装形式
  //   输入引脚
  //   输出引脚
endmodule

module MIPS_Regifile (
  input  [31:0] Din,
  input  Clk,
  input  WE,
  input  [4:0] R1_num,
  input  [4:0] W_num,
  input  [4:0] R2_num,
  output [31:0] R1,
  output [31:0] R2
);

  // RegisterFile registerfile_1: pin names not known; wires that end beside it: Din, Clk, WE, W_num, R1_num, R2_num, R1, R2
endmodule

module \理想流水线  (
);

  wire CLK, Go, IR1, IR2, IR3, RST, W1, W2, W3;
  wire [11:0] EX_PC, ID_PC, IF_PC, MEM_PC, WB_PC;
  wire [15:0] \LoadUse次数 , \总周期数 , \插入气泡数 , \无条件分支数 , \条件分支成功数 ;
  wire [31:0] LedData;

  Button \u_总复位  (.out(RST));
  Button _1 (.out(IR1));
  Button _2 (.out(IR2));
  Button _3 (.out(IR3));
  Button \u_继续运行  (.out(Go));
  LED led_1 (.in(W1));
  LED led_2 (.in(W2));
  LED led_3 (.in(W3));
  Hex_Digit_Display hex_digit_display_1 (.value(LedData[31:28]));  // open: dp
  Hex_Digit_Display hex_digit_display_2 (.value(LedData[23:20]));  // open: dp
  Hex_Digit_Display hex_digit_display_3 (.value(LedData[27:24]));  // open: dp
  Hex_Digit_Display hex_digit_display_4 (.value(LedData[19:16]));  // open: dp
  Hex_Digit_Display hex_digit_display_5 (.value(LedData[15:12]));  // open: dp
  Hex_Digit_Display hex_digit_display_6 (.value(LedData[7:4]));  // open: dp
  Hex_Digit_Display hex_digit_display_7 (.value(LedData[11:8]));  // open: dp
  Clock clock_1 (.out(CLK));
  Hex_Digit_Display hex_digit_display_8 (.value(LedData[3:0]));  // open: dp
  // Probe on \总周期数 
  // Probe on \无条件分支数 
  // Probe on \条件分支成功数 
  // Probe on \插入气泡数 
  // Probe on \LoadUse次数 
  // Probe on IF_PC
  // Probe on EX_PC
  // Probe on ID_PC
  // Probe on MEM_PC
  // Probe on WB_PC

  // Notes on the sheet:
  //   中断源
  //   中断等待指示
  //   数码管输出
  //   流水调试日志用
endmodule
module \气泡流水线  (
  output RegWrite,
  output MemWrite,
  output [31:0] PC,
  output [31:0] IR,
  output [31:0] RDin,
  output [31:0] MDin
);

  wire and_1_out, and_2_out, and_3_out, and_4_out, CLK, comparator_4_eq, eq, ex_mem_1_j_out,
       ex_mem_1_j_out_2, ex_mem_1_j_out_3, ex_mem_1_j_out_4, ex_mem_1_jr_out, ex_mem_1_jr_out_2,
       ex_mem_1_jr_out_3, ex_mem_1_jr_out_4, Go, id_ex_1_p23, id_ex_1_p24, id_ex_1_p25, id_ex_1_p26,
       id_ex_1_p27, id_ex_1_p28, id_ex_1_p29, id_ex_1_p30, id_ex_1_p35, id_ex_1_p36, id_ex_1_p37, ID_EX_BLTZ,
       ID_EX_BRANCH, ID_EX_J, ID_EX_JR, IF_ID_BEQ, IF_ID_BLTZ, IF_ID_BNE, IF_ID_J, IF_ID_JR, IF_ID_LHU,
       IF_ID_LUI, IR1, IR2, IR3, mem_wb_1_jr_out, mem_wb_1_jr_out_2, mem_wb_1_jr_out_3, mips_regifile_1_p7,
       mips_regifile_1_p8, not_1_out, not_2_out, not_3_out, or_1_out, TOTAL_EN, W1, W2, W3, WB_JAL,
       WB_REGDST, WB_REGWRITE, WB_SYSCALL, \单周期硬布线控制器_1_p3 , \单周期硬布线控制器_1_p6 , \单周期硬布线控制器_1_p9 ,
       \单周期硬布线控制器_1_p10 , \单周期硬布线控制器_1_p11 , \单周期硬布线控制器_1_p12 , \单周期硬布线控制器_1_p13 , \单周期硬布线控制器_1_p14 ,
       \单周期硬布线控制器_1_p15 ;
  wire [3:0] id_ex_1_p34;
  wire [4:0] multiplexer_2_out, multiplexer_3_out, multiplexer_5_out, multiplexer_6_out;
  wire [15:0] multiplexer_14_out, \总周期数 ;
  wire [31:0] adder_1_out, adder_2_out, bit_extender_1_out, bit_extender_2_out, bit_extender_3_out,
       ex_mem_1_j_out_5, ex_mem_1_j_out_6, ex_mem_1_j_out_7, ex_mem_1_j_out_8, ex_mem_1_j_out_9, id_ex_1_p42,
       ID_EX_IR, ID_EX_PC, ID_EX_R1, ID_EX_R2, IF_ID_IR, IF_ID_PC, IF_IR, LedData, mem_wb_1_j_out_5,
       mem_wb_1_j_out_7, mem_wb_1_j_out_8, mips_alu_1_result, mips_regifile_1_p4, multiplexer_1_out,
       multiplexer_4_out, multiplexer_7_out, multiplexer_8_out, multiplexer_9_out, multiplexer_11_out,
       multiplexer_12_out, multiplexer_13_out, PC_q, ram_1_data, shifter_1_out, shifter_2_out, WB_IR, WB_R1,
       WB_R2;

  Clock clock_1 (.out(CLK));
  Button _1 (.out(IR1));
  Button _2 (.out(IR2));
  Button _3 (.out(IR3));
  Button \u_继续运行  (.out(Go));
  LED led_1 (.in(W1));
  LED led_2 (.in(W2));
  LED led_3 (.in(W3));
  Hex_Digit_Display hex_digit_display_1 (.value(LedData[31:28]));  // open: dp
  Multiplexer #(.width(32), .enable("false")) multiplexer_1 (
    .in0(adder_1_out), .in1(multiplexer_7_out), .out(multiplexer_1_out), .sel(ID_EX_BRANCH));
  Hex_Digit_Display hex_digit_display_2 (.value(LedData[23:20]));  // open: dp
  Hex_Digit_Display hex_digit_display_3 (.value(LedData[27:24]));  // open: dp
  Hex_Digit_Display hex_digit_display_4 (.value(LedData[15:12]));  // open: dp
  Hex_Digit_Display hex_digit_display_5 (.value(LedData[19:16]));  // open: dp
  Register #(.width(32)) u_PC (.D(multiplexer_1_out), .en(TOTAL_EN), .Q(PC_q), .clk(CLK));  // open: clr
  Hex_Digit_Display hex_digit_display_6 (.value(LedData[7:4]));  // open: dp
  Hex_Digit_Display hex_digit_display_7 (.value(LedData[11:8]));  // open: dp
  // Probe on \总周期数 
  Adder #(.width(32)) adder_1 (.a(PC_q), .b(32'h4), .out(adder_1_out));  // open: cin, cout
  Hex_Digit_Display hex_digit_display_8 (.value(LedData[3:0]));  // open: dp
  Counter #(.width(16), .max('hffff)) counter_1 (.count(TOTAL_EN), .Q(\总周期数 ), .clk(CLK));  // open: load, D, carry, clr
  ROM #(.addrWidth(10), .dataWidth(32)) rom_1 (.addr(PC_q[11:2]), .data(IF_IR));  // open: sel
  // IF_ID if_id_1: pin names not known; wires that end beside it: IF_IR, adder_1_out, TOTAL_EN, CLK, IF_ID_IR, IF_ID_PC, ID_EX_BRANCH
  Comparator #(.width(6), .mode("unsigned")) comparator_1 (
    .a(IF_ID_IR[31:26]), .b(6'b000001), .eq(IF_ID_BLTZ));  // open: gt, lt
  Comparator #(.width(6), .mode("unsigned")) comparator_2 (
    .a(IF_ID_IR[31:26]), .b(6'b100101), .eq(IF_ID_LHU));  // open: gt, lt
  Comparator #(.width(6), .mode("unsigned")) comparator_3 (
    .a(IF_ID_IR[31:26]), .b(6'b001111), .eq(IF_ID_LUI));  // open: gt, lt
  // 单周期硬布线控制器 单周期硬布线控制器_1: pin names not known; wires that end beside it: IF_ID_J, IF_ID_JR, \单周期硬布线控制器_1_p3 , IF_ID_IR[31:26], IF_ID_IR[5:0], \单周期硬布线控制器_1_p6 , IF_ID_BEQ, IF_ID_BNE, \单周期硬布线控制器_1_p9 , \单周期硬布线控制器_1_p10 , \单周期硬布线控制器_1_p11 , \单周期硬布线控制器_1_p12 , \单周期硬布线控制器_1_p13 , \单周期硬布线控制器_1_p14 , \单周期硬布线控制器_1_p15 
  Multiplexer #(.width(5), .enable("false")) multiplexer_2 (
    .in0(IF_ID_IR[25:21]), .in1(5'b00010), .out(multiplexer_2_out), .sel(\单周期硬布线控制器_1_p6 ));
  assign bit_extender_1_out = {{16{1'b0}}, IF_ID_IR[15:0]};  // Bit_Extender bit_extender_1
  assign bit_extender_2_out = {{16{IF_ID_IR[15]}}, IF_ID_IR[15:0]};  // Bit_Extender bit_extender_2
  Multiplexer #(.width(5), .enable("false")) multiplexer_3 (
    .in0(WB_IR[20:16]), .in1(WB_IR[15:11]), .out(multiplexer_3_out), .sel(WB_REGDST));
  Multiplexer #(.width(32), .enable("false")) multiplexer_4 (
    .in0(bit_extender_1_out), .in1(bit_extender_2_out), .out(multiplexer_4_out), .sel(\单周期硬布线控制器_1_p3 ));
  Multiplexer #(.width(5), .enable("false")) multiplexer_5 (
    .in0(IF_ID_IR[20:16]), .in1(5'b00100), .out(multiplexer_5_out), .sel(\单周期硬布线控制器_1_p6 ));
  Multiplexer #(.width(5), .enable("false")) multiplexer_6 (
    .in0(multiplexer_3_out), .in1({5{1'b1}}), .out(multiplexer_6_out), .sel(WB_JAL));
  // MIPS_Regifile mips_regifile_1: pin names not known; wires that end beside it: multiplexer_2_out, multiplexer_5_out, multiplexer_6_out, mips_regifile_1_p4, WB_REGWRITE, CLK, mips_regifile_1_p7, mips_regifile_1_p8
  // ID_EX id_ex_1: pin names not known; wires that end beside it: \单周期硬布线控制器_1_p6 , \单周期硬布线控制器_1_p15 , IF_ID_LHU, IF_ID_LUI, \单周期硬布线控制器_1_p13 , \单周期硬布线控制器_1_p9 , \单周期硬布线控制器_1_p10 , \单周期硬布线控制器_1_p14 , IF_ID_J, IF_ID_JR, IF_ID_BLTZ, \单周期硬布线控制器_1_p11 , \单周期硬布线控制器_1_p12 , IF_ID_BEQ, IF_ID_BNE, IF_ID_IR, IF_ID_PC, mips_regifile_1_p7, mips_regifile_1_p8, multiplexer_4_out, TOTAL_EN, CLK, id_ex_1_p23, id_ex_1_p24, id_ex_1_p25, id_ex_1_p26, id_ex_1_p27, id_ex_1_p28, id_ex_1_p29, id_ex_1_p30, ID_EX_J, ID_EX_JR, ID_EX_BLTZ, id_ex_1_p34, id_ex_1_p35, id_ex_1_p36, id_ex_1_p37, ID_EX_IR, ID_EX_PC, ID_EX_R1, ID_EX_R2, id_ex_1_p42, ID_EX_BRANCH
  Multiplexer #(.width(32), .enable("false")) multiplexer_7 (
    .in0(adder_2_out), .in1(multiplexer_8_out), .out(multiplexer_7_out), .sel(ID_EX_J));
  Multiplexer #(.width(32), .enable("false")) multiplexer_8 (
    .in0(shifter_2_out), .in1(ID_EX_R1), .out(multiplexer_8_out), .sel(ID_EX_JR));
  and and_1 (and_1_out, eq, id_ex_1_p36);
  Multiplexer #(.width(32), .enable("false")) multiplexer_9 (
    .in0(ID_EX_R2), .in1(id_ex_1_p42), .out(multiplexer_9_out), .sel(id_ex_1_p35));
  assign bit_extender_3_out = {{6{1'b0}}, ID_EX_IR[25:0]};  // Bit_Extender bit_extender_3
  not not_1 (not_1_out, eq);
  Shifter #(.width(32)) shifter_1 (.in(id_ex_1_p42), .\dist (5'b00010), .out(shifter_1_out));
  Shifter #(.width(32)) shifter_2 (.in(bit_extender_3_out), .\dist (5'b00010), .out(shifter_2_out));
  or or_1 (or_1_out, and_1_out, and_2_out);
  and and_2 (and_2_out, not_1_out, id_ex_1_p37);
  Adder #(.width(32)) adder_2 (.a(shifter_1_out), .b(ID_EX_PC), .out(adder_2_out));  // open: cin, cout
  MIPS_ALU mips_alu_1 (
    .X(ID_EX_R1), .Y(multiplexer_9_out), .AluOP(id_ex_1_p34), .Equal(eq), .Result(mips_alu_1_result),
    .shamt(ID_EX_IR[10:6]));  // open: Result_2
  or or_2 (ID_EX_BRANCH, or_1_out, ID_EX_J, and_3_out);
  and and_3 (and_3_out, ID_EX_BLTZ, mips_alu_1_result[0]);
  EX_MEM ex_mem_1 (
    .SYSCALL_in(id_ex_1_p23), .J_out(ex_mem_1_j_out), .REGDST_in(id_ex_1_p24), .J_out_2(ex_mem_1_j_out_2),
    .LHU_in(id_ex_1_p25), .JR_out(ex_mem_1_jr_out), .LUI_in(id_ex_1_p26), .JR_out_2(ex_mem_1_jr_out_2),
    .REGWRITE_in(id_ex_1_p27), .J_out_3(ex_mem_1_j_out_3), .MEM_TO_REG_in(id_ex_1_p28),
    .JR_out_3(ex_mem_1_jr_out_3), .MEMWRITE_in(id_ex_1_p29), .J_out_4(ex_mem_1_j_out_4),
    .JAL_in(id_ex_1_p30), .JR_out_4(ex_mem_1_jr_out_4), .IR_in(ID_EX_IR), .J_out_5(ex_mem_1_j_out_5),
    .PC_in(ID_EX_PC), .J_out_6(ex_mem_1_j_out_6), .R2_in(ID_EX_R2), .J_out_7(ex_mem_1_j_out_7),
    .ALURES_in(mips_alu_1_result), .J_out_8(ex_mem_1_j_out_8), .in_14(TOTAL_EN), .in_15(1'b0), .in_16(CLK),
    .r1_in(ID_EX_R1), .J_out_9(ex_mem_1_j_out_9));
  RAM #(.addrWidth(10), .dataWidth(32), .bus("separate")) ram_1 (
    .addr(ex_mem_1_j_out_8[11:2]), .din(ex_mem_1_j_out_7), .data(ram_1_data), .str(ex_mem_1_j_out_4),
    .sel(1'b1), .clk(CLK));  // open: ld, clr
  MEM_WB mem_wb_1 (
    .SYSCALL_in(ex_mem_1_j_out), .J_out(WB_SYSCALL), .REGDST_in(ex_mem_1_j_out_2), .J_out_2(WB_REGDST),
    .LHU_in(ex_mem_1_jr_out), .JR_out(mem_wb_1_jr_out), .LUI_in(ex_mem_1_jr_out_2),
    .JR_out_2(mem_wb_1_jr_out_2), .REGWRITE_in(ex_mem_1_j_out_3), .J_out_3(WB_REGWRITE),
    .MEM_TO_REG_in(ex_mem_1_jr_out_3), .JR_out_3(mem_wb_1_jr_out_3), .JAL_in(ex_mem_1_jr_out_4),
    .JR_out_4(WB_JAL), .IR_in(ex_mem_1_j_out_5), .J_out_4(WB_IR), .PC_in(ex_mem_1_j_out_6),
    .J_out_5(mem_wb_1_j_out_5), .MEMDATA_in(ram_1_data), .J_out_8(mem_wb_1_j_out_8),
    .ALURES_in(ex_mem_1_j_out_8), .J_out_7(mem_wb_1_j_out_7), .in_15(1'b0), .in_16(CLK), .in_14(TOTAL_EN),
    .R2_in(ex_mem_1_j_out_7), .J_out_6(WB_R2), .R1_in(ex_mem_1_j_out_9), .J_out_9(WB_R1));
  Multiplexer #(.width(32), .enable("false")) multiplexer_10 (
    .in0(multiplexer_11_out), .in1({WB_IR[15:0], {16{1'b0}}}), .out(mips_regifile_1_p4),
    .sel(mem_wb_1_jr_out_2));
  Multiplexer #(.width(32), .enable("false")) multiplexer_11 (
    .in0(multiplexer_12_out), .in1(mem_wb_1_j_out_5), .out(multiplexer_11_out), .sel(WB_JAL));
  Multiplexer #(.width(32), .enable("false")) multiplexer_12 (
    .in0(multiplexer_13_out), .in1({{16{1'b0}}, multiplexer_14_out}), .out(multiplexer_12_out),
    .sel(mem_wb_1_jr_out));
  Multiplexer #(.width(32), .enable("false")) multiplexer_13 (
    .in0(mem_wb_1_j_out_7), .in1(mem_wb_1_j_out_8), .out(multiplexer_13_out), .sel(mem_wb_1_jr_out_3));
  Comparator #(.width(32)) comparator_4 (.a(WB_R1), .b(32'h22), .eq(comparator_4_eq));  // open: gt, lt
  Multiplexer #(.width(16), .enable("false")) multiplexer_14 (
    .in0(multiplexer_13_out[15:0]), .in1(multiplexer_13_out[31:16]), .out(multiplexer_14_out), .sel(WB_IR[1]));
  not not_2 (not_2_out, comparator_4_eq);
  not not_3 (not_3_out, Go);
  and and_4 (and_4_out, WB_SYSCALL, not_2_out);
  nand nand_1 (TOTAL_EN, not_3_out, and_4_out);
  Register #(.width(32)) PC_2 (.D(WB_R2), .en(comparator_4_eq), .Q(LedData), .clk(CLK));  // open: clr
  // AND_Gate and_5 is placed but not wired

  // Notes on the sheet:
  //   中断源
  //   中断等待指示
  //   总复位信号应将除ROM以外所有存储组件全部清零
  //   数码管输出
  //   数码管输出应该用寄存器锁存，否则显示数据只能一闪而过
  //   指令存储器
  //   contents of rom_1 (hex, n*v repeats v):
  //   20110020 20020022 8000c06 20110004 20120005 20130006 10000003 20110007 20120008 20130009 14110003
  //   2011000a 2012000b 2013000c c000c14 2002000a 0 0 0 c 2231ffff 0 0 0 112020 0 0 0 c 1620fff6 3e00008
  //   为方便自动评测，需要输出PC，IR，寄存器文件写入端口RDin，内存写入端口MDin等信号
  //   指令字
  //   JMP
  //   JR
  //   OP
  //   Func
  //   rs
  //   rt
  //   AluOP
  //   AluSrcB
  //   RegWrite
  //   JAL
  //   RegDst
  //   Syscall
  //   MemToReg
  //   MemWrite
  //   PC+4
endmodule

module \重定向流水线  (
  output RegWrite,
  output MemWrite,
  output [31:0] IF_PC,
  output [31:0] ID_PC,
  output [31:0] EX_PC,
  output [31:0] M_PC,
  output [31:0] WB_PC,
  output [31:0] RDin,
  output [31:0] MDin,
  output [31:0] LedData
);

  wire and_1_out, and_2_out, and_3_out, and_4_out, and_5_out, and_6_out, and_7_out, and_8_out, and_9_out,
       CLK, comparator_4_eq, eq, ex_mem_1_j_out, ex_mem_1_jr_out, ex_mem_1_jr_out_2, EX_MEM_JAL,
       EX_MEM_MEMTOREG, EX_MEM_REGDST, EX_MEM_REGWRITE, Go, id_ex_1_j_out, id_ex_1_j_out_4, id_ex_1_jr_out,
       id_ex_1_jr_out_2, id_ex_1_jr_out_6, id_ex_1_jr_out_7, id_ex_1_jr_out_8, ID_EX_BLTZ, ID_EX_BRANCH,
       ID_EX_J, ID_EX_JAL, ID_EX_JR, ID_EX_MEMTOREG, ID_EX_REGDST, ID_EX_REGWRITE, ID_EX_SYSCALL, IF_ID_BEQ,
       IF_ID_BLTZ, IF_ID_BNE, IF_ID_J, IF_ID_JR, IF_ID_LHU, IF_ID_LUI, IR1, IR2, IR3, LOAD_USE,
       mem_wb_1_jr_out, mem_wb_1_jr_out_2, mem_wb_1_jr_out_3, not_1_out, not_2_out, not_3_out, not_4_out,
       not_5_out, or_1_out, or_2_out, RST, TOTAL_EN, W1, W2, W3, WB_JAL, WB_REGDST, WB_SYSCALL,
       \单周期硬布线控制器_1_alu_src , \单周期硬布线控制器_1_jal , \单周期硬布线控制器_1_memtoreg , \单周期硬布线控制器_1_memwrite ,
       \单周期硬布线控制器_1_regdst , \单周期硬布线控制器_1_regwrite , \单周期硬布线控制器_1_signedext ;
  wire [1:0] F1, F2, \数据相关检测_1_forward1 , \数据相关检测_1_forward2 ;
  wire [3:0] id_ex_1_syscall_out, \单周期硬布线控制器_1_alu_op ;
  wire [4:0] multiplexer_2_out, multiplexer_3_out, multiplexer_5_out, multiplexer_6_out;
  wire [15:0] \LoadUse次数 , multiplexer_16_out, \总周期数 , \插入气泡数 , \无条件分支数 , \条件分支成功数 ;
  wire [31:0] adder_1_out, adder_2_out, adder_3_out, adder_4_out, bit_extender_1_out, bit_extender_2_out,
       bit_extender_3_out, ex_mem_1_j_out_9, EX_MEM_ALURES, EX_MEM_IR, id_ex_1_j_out_11, ID_EX_IR, ID_EX_R1,
       ID_EX_R1_prime, ID_EX_R2, ID_EX_R2_prime, IF_ID_IR, IF_IR, MEM_WB_ALURES, MEM_WB_MEMDATA,
       mips_alu_1_result, mips_regifile_1_r1, mips_regifile_1_r2, multiplexer_1_out, multiplexer_4_out,
       multiplexer_7_out, multiplexer_8_out, multiplexer_11_out, multiplexer_13_out, multiplexer_14_out,
       multiplexer_15_out, ram_1_data, shifter_1_out, shifter_2_out, WB_IR, WB_R1, WB_R2;

  Button \u_总复位  (.out(RST));
  Button _1 (.out(IR1));
  Button _2 (.out(IR2));
  Button _3 (.out(IR3));
  Button \u_继续运行  (.out(Go));
  LED led_1 (.in(W1));
  LED led_2 (.in(W2));
  LED led_3 (.in(W3));
  Hex_Digit_Display hex_digit_display_1 (.value(LedData[31:28]));  // open: dp
  Multiplexer #(.width(32), .enable("false")) multiplexer_1 (
    .in0(adder_1_out), .in1(multiplexer_7_out), .out(multiplexer_1_out), .sel(ID_EX_BRANCH));
  Hex_Digit_Display hex_digit_display_2 (.value(LedData[27:24]));  // open: dp
  Hex_Digit_Display hex_digit_display_3 (.value(LedData[23:20]));  // open: dp
  Counter #(.width(16), .max('hffff)) counter_1 (.count(TOTAL_EN), .Q(\总周期数 ), .clk(CLK));  // open: load, D, carry, clr
  Counter #(.width(16), .max('hffff)) counter_2 (
    .count(and_1_out), .Q(\无条件分支数 ), .clk(CLK));  // open: load, D, carry, clr
  and and_1 (and_1_out, ID_EX_J, TOTAL_EN);
  Counter #(.width(16), .max('hffff)) counter_3 (
    .count(and_2_out), .Q(\条件分支成功数 ), .clk(CLK));  // open: load, D, carry, clr
  and and_2 (and_2_out, ID_EX_BRANCH, ~ID_EX_J, TOTAL_EN);  // AND_Gate
  Counter #(.width(16), .max('hffff)) counter_4 (
    .count(and_3_out), .Q(\LoadUse次数 ), .clk(CLK));  // open: load, D, carry, clr
  and and_3 (and_3_out, LOAD_USE, TOTAL_EN);
  and and_4 (and_4_out, TOTAL_EN, not_1_out);
  not not_1 (not_1_out, LOAD_USE);
  Hex_Digit_Display hex_digit_display_4 (.value(LedData[15:12]));  // open: dp
  Hex_Digit_Display hex_digit_display_5 (.value(LedData[19:16]));  // open: dp
  Register #(.width(32)) PC (.D(multiplexer_1_out), .en(and_4_out), .Q(IF_PC), .clk(CLK));  // open: clr
  Hex_Digit_Display hex_digit_display_6 (.value(LedData[7:4]));  // open: dp
  Hex_Digit_Display hex_digit_display_7 (.value(LedData[11:8]));  // open: dp
  Clock clock_1 (.out(CLK));
  Adder #(.width(32)) adder_1 (.a(IF_PC), .b(32'h4), .out(adder_1_out));  // open: cin, cout
  Hex_Digit_Display hex_digit_display_8 (.value(LedData[3:0]));  // open: dp
  ROM #(.addrWidth(10), .dataWidth(32)) rom_1 (.addr(IF_PC[11:2]), .data(IF_IR));  // open: sel
  not not_2 (not_2_out, LOAD_USE);
  // Probe on \总周期数 
  // Probe on \无条件分支数 
  // Probe on \条件分支成功数 
  // Probe on \插入气泡数 
  // Probe on \LoadUse次数 
  // Mips_Probe mips_probe_1: pin names not known; wires that end beside it: IF_IR
  and and_5 (and_5_out, TOTAL_EN, not_2_out);
  // Probe on IF_PC[11:0]
  IF_ID if_id_1 (
    .IRin(IF_IR), .PCin(IF_PC), .IRout(IF_ID_IR), .PCout(ID_PC), .clear(ID_EX_BRANCH), .clk(CLK),
    .enable(and_5_out));  // open: SYSCALL_in, J_out, REGDST_in, J_out_2
  // Probe on EX_PC[11:0]
  // Probe on ID_PC[11:0]
  // Mips_Probe mips_probe_2: pin names not known; wires that end beside it: IF_ID_IR
  Comparator #(.width(6), .mode("unsigned")) comparator_1 (
    .a(IF_ID_IR[31:26]), .b(6'b000001), .eq(IF_ID_BLTZ));  // open: gt, lt
  Comparator #(.width(6), .mode("unsigned")) comparator_2 (
    .a(IF_ID_IR[31:26]), .b(6'b100101), .eq(IF_ID_LHU));  // open: gt, lt
  Comparator #(.width(6), .mode("unsigned")) comparator_3 (
    .a(IF_ID_IR[31:26]), .b(6'b001111), .eq(IF_ID_LUI));  // open: gt, lt
  // Probe on M_PC[11:0]
  // Probe on WB_PC[11:0]
  // Mips_Probe mips_probe_3: pin names not known; wires that end beside it: ID_EX_IR
  \单周期硬布线控制器  \u_单周期硬布线控制器_1  (
    .Func(IF_ID_IR[5:0]), .OP(IF_ID_IR[31:26]), .ALU_OP(\单周期硬布线控制器_1_alu_op ),
    .MemToReg(\单周期硬布线控制器_1_memtoreg ), .MemWrite(\单周期硬布线控制器_1_memwrite ), .ALU_SRC(\单周期硬布线控制器_1_alu_src ),
    .RegWrite(\单周期硬布线控制器_1_regwrite ), .SysCALL(ID_EX_SYSCALL), .SignedExt(\单周期硬布线控制器_1_signedext ),
    .RegDst(\单周期硬布线控制器_1_regdst ), .JR(IF_ID_JR), .JMP(IF_ID_J), .Beq(IF_ID_BEQ), .JAL(\单周期硬布线控制器_1_jal ),
    .Bne(IF_ID_BNE));
  Multiplexer #(.width(5), .enable("false")) multiplexer_2 (
    .in0(IF_ID_IR[25:21]), .in1(5'b00010), .out(multiplexer_2_out), .sel(ID_EX_SYSCALL));
  assign bit_extender_1_out = {{16{1'b0}}, IF_ID_IR[15:0]};  // Bit_Extender bit_extender_1
  assign bit_extender_2_out = {{16{IF_ID_IR[15]}}, IF_ID_IR[15:0]};  // Bit_Extender bit_extender_2
  // Mips_Probe mips_probe_4: pin names not known; wires that end beside it: EX_MEM_IR
  Multiplexer #(.width(5), .enable("false")) multiplexer_3 (
    .in0(WB_IR[20:16]), .in1(WB_IR[15:11]), .out(multiplexer_3_out), .sel(WB_REGDST));
  Multiplexer #(.width(32), .enable("false")) multiplexer_4 (
    .in0(bit_extender_1_out), .in1(bit_extender_2_out), .out(multiplexer_4_out), .sel(\单周期硬布线控制器_1_signedext ));
  Multiplexer #(.width(5), .enable("false")) multiplexer_5 (
    .in0(IF_ID_IR[20:16]), .in1(5'b00100), .out(multiplexer_5_out), .sel(ID_EX_SYSCALL));
  Multiplexer #(.width(5), .enable("false")) multiplexer_6 (
    .in0(multiplexer_3_out), .in1({5{1'b1}}), .out(multiplexer_6_out), .sel(WB_JAL));
  // Mips_Probe mips_probe_5: pin names not known; wires that end beside it: WB_IR
  MIPS_Regifile mips_regifile_1 (
    .Din(RDin), .Clk(CLK), .R1(mips_regifile_1_r1), .R2(mips_regifile_1_r2), .WE(RegWrite),
    .W_num(multiplexer_6_out), .R1_num(multiplexer_2_out), .R2_num(multiplexer_5_out));
  \数据相关检测  \u_数据相关检测_1  (
    .in_1(ID_EX_REGDST), .in_2(EX_MEM_REGDST), .in_3(ID_EX_JAL), .in_4(EX_MEM_JAL), .in_5(ID_EX_REGWRITE),
    .in_6(EX_MEM_REGWRITE), .in_7(ID_EX_MEMTOREG), .in_8(EX_MEM_MEMTOREG), .ID_IR(IF_ID_IR),
    .EX_IR(ID_EX_IR), .MEM_IR(EX_MEM_IR), .FORWARD1(\数据相关检测_1_forward1 ), .FORWARD2(\数据相关检测_1_forward2 ),
    .LOAD_USE(LOAD_USE), .in_12(ID_EX_SYSCALL));
  ID_EX id_ex_1 (
    .J_in(IF_ID_J), .J_out_5(ID_EX_J), .JR_in(IF_ID_JR), .JR_out_5(ID_EX_JR), .BLTZ_in(IF_ID_BLTZ),
    .J_out_6(ID_EX_BLTZ), .ALUSRC_in(\单周期硬布线控制器_1_alu_src ), .JR_out_6(id_ex_1_jr_out_6),
    .ALUOP_in(\单周期硬布线控制器_1_alu_op ), .SYSCALL_out(id_ex_1_syscall_out), .BEQ_in(IF_ID_BEQ),
    .JR_out_7(id_ex_1_jr_out_7), .REGDST_in(\单周期硬布线控制器_1_regdst ), .J_out_2(ID_EX_REGDST),
    .LHU_in(IF_ID_LHU), .JR_out(id_ex_1_jr_out), .BNE_in(IF_ID_BNE), .JR_out_8(id_ex_1_jr_out_8),
    .IR_in(IF_ID_IR), .J_out_7(ID_EX_IR), .PC_in(ID_PC), .J_out_8(EX_PC), .R1_in(mips_regifile_1_r1),
    .J_out_9(ID_EX_R1), .R2_in(mips_regifile_1_r2), .J_out_10(ID_EX_R2), .IMM_in(multiplexer_4_out),
    .J_out_11(id_ex_1_j_out_11), .SYSCALL_in(ID_EX_SYSCALL), .J_out(id_ex_1_j_out), .LUI_in(IF_ID_LUI),
    .JR_out_2(id_ex_1_jr_out_2), .REGWRITE_in(\单周期硬布线控制器_1_regwrite ), .J_out_3(ID_EX_REGWRITE),
    .MEM_TO_REG_in(\单周期硬布线控制器_1_memtoreg ), .JR_out_3(ID_EX_MEMTOREG), .MEMWRITE_in(\单周期硬布线控制器_1_memwrite ),
    .J_out_4(id_ex_1_j_out_4), .JAL_in(\单周期硬布线控制器_1_jal ), .JR_out_4(ID_EX_JAL), .in_25(TOTAL_EN),
    .in_27(CLK), .in_26(or_1_out), .FORWARD1_in(\数据相关检测_1_forward1 ), .SYSCALL_out_2(F1),
    .FORWARD2_in(\数据相关检测_1_forward2 ), .SYSCALL_out_3(F2));  // open: MISS_in, JR_out_9, PREDICT_in, JR_out_10
  or or_1 (or_1_out, ID_EX_BRANCH, LOAD_USE);
  Multiplexer #(.width(32), .enable("false")) multiplexer_7 (
    .in0(adder_3_out), .in1(multiplexer_8_out), .out(multiplexer_7_out), .sel(ID_EX_J));
  Multiplexer #(.width(32), .enable("false")) multiplexer_8 (
    .in0(shifter_2_out), .in1(ID_EX_R1_prime), .out(multiplexer_8_out), .sel(ID_EX_JR));
  Multiplexer #(.select(2), .width(32), .enable("false")) multiplexer_9 (
    .in0(ID_EX_R1), .in1(MEM_WB_ALURES), .in2(EX_MEM_ALURES), .in3(MEM_WB_MEMDATA), .out(ID_EX_R1_prime),
    .sel(F1));
  Multiplexer #(.select(2), .width(32), .enable("false")) multiplexer_10 (
    .in0(ID_EX_R2), .in1(MEM_WB_ALURES), .in2(EX_MEM_ALURES), .in3(MEM_WB_MEMDATA), .out(ID_EX_R2_prime),
    .sel(F2));
  and and_6 (and_6_out, eq, id_ex_1_jr_out_7);
  Multiplexer #(.width(32), .enable("false")) multiplexer_11 (
    .in0(ID_EX_R2_prime), .in1(id_ex_1_j_out_11), .out(multiplexer_11_out), .sel(id_ex_1_jr_out_6));
  assign bit_extender_3_out = {{6{1'b0}}, ID_EX_IR[25:0]};  // Bit_Extender bit_extender_3
  not not_3 (not_3_out, eq);
  Shifter #(.width(32)) shifter_1 (.in(id_ex_1_j_out_11), .\dist (5'b00010), .out(shifter_1_out));
  Adder #(.width(32)) adder_2 (.a(EX_PC), .b(32'h4), .out(adder_2_out));  // open: cin, cout
  Shifter #(.width(32)) shifter_2 (.in(bit_extender_3_out), .\dist (5'b00010), .out(shifter_2_out));
  or or_2 (or_2_out, and_6_out, and_7_out);
  and and_7 (and_7_out, not_3_out, id_ex_1_jr_out_8);
  Adder #(.width(32)) adder_3 (.a(shifter_1_out), .b(adder_2_out), .out(adder_3_out));  // open: cin, cout
  MIPS_ALU mips_alu_1 (
    .X(ID_EX_R1_prime), .Y(multiplexer_11_out), .AluOP(id_ex_1_syscall_out), .Equal(eq),
    .Result(mips_alu_1_result), .shamt(ID_EX_IR[10:6]));  // open: Result_2
  or or_3 (ID_EX_BRANCH, or_2_out, ID_EX_J, and_8_out);
  and and_8 (and_8_out, ID_EX_BLTZ, mips_alu_1_result[0]);
  EX_MEM ex_mem_1 (
    .SYSCALL_in(id_ex_1_j_out), .J_out(ex_mem_1_j_out), .REGDST_in(ID_EX_REGDST), .J_out_2(EX_MEM_REGDST),
    .LHU_in(id_ex_1_jr_out), .JR_out(ex_mem_1_jr_out), .LUI_in(id_ex_1_jr_out_2),
    .JR_out_2(ex_mem_1_jr_out_2), .REGWRITE_in(ID_EX_REGWRITE), .J_out_3(EX_MEM_REGWRITE),
    .MEM_TO_REG_in(ID_EX_MEMTOREG), .JR_out_3(EX_MEM_MEMTOREG), .MEMWRITE_in(id_ex_1_j_out_4),
    .J_out_4(MemWrite), .JAL_in(ID_EX_JAL), .JR_out_4(EX_MEM_JAL), .IR_in(ID_EX_IR), .J_out_5(EX_MEM_IR),
    .PC_in(EX_PC), .J_out_6(M_PC), .R2_in(ID_EX_R2_prime), .J_out_7(MDin), .ALURES_in(mips_alu_1_result),
    .J_out_8(EX_MEM_ALURES), .in_14(TOTAL_EN), .in_15(1'b0), .in_16(CLK), .r1_in(ID_EX_R1_prime),
    .J_out_9(ex_mem_1_j_out_9));
  RAM #(.addrWidth(10), .dataWidth(32), .bus("separate")) ram_1 (
    .addr(EX_MEM_ALURES[11:2]), .din(MDin), .data(ram_1_data), .str(MemWrite), .sel(1'b1), .clk(CLK));  // open: ld, clr
  MEM_WB mem_wb_1 (
    .SYSCALL_in(ex_mem_1_j_out), .J_out(WB_SYSCALL), .REGDST_in(EX_MEM_REGDST), .J_out_2(WB_REGDST),
    .LHU_in(ex_mem_1_jr_out), .JR_out(mem_wb_1_jr_out), .LUI_in(ex_mem_1_jr_out_2),
    .JR_out_2(mem_wb_1_jr_out_2), .REGWRITE_in(EX_MEM_REGWRITE), .J_out_3(RegWrite),
    .MEM_TO_REG_in(EX_MEM_MEMTOREG), .JR_out_3(mem_wb_1_jr_out_3), .JAL_in(EX_MEM_JAL), .JR_out_4(WB_JAL),
    .IR_in(EX_MEM_IR), .J_out_4(WB_IR), .PC_in(M_PC), .J_out_5(WB_PC), .MEMDATA_in(ram_1_data),
    .J_out_8(MEM_WB_MEMDATA), .ALURES_in(EX_MEM_ALURES), .J_out_7(MEM_WB_ALURES), .in_15(1'b0), .in_16(CLK),
    .in_14(TOTAL_EN), .R2_in(MDin), .J_out_6(WB_R2), .R1_in(ex_mem_1_j_out_9), .J_out_9(WB_R1));
  Multiplexer #(.width(32), .enable("false")) multiplexer_12 (
    .in0(multiplexer_13_out), .in1({WB_IR[15:0], {16{1'b0}}}), .out(RDin), .sel(mem_wb_1_jr_out_2));
  Multiplexer #(.width(32), .enable("false")) multiplexer_13 (
    .in0(multiplexer_14_out), .in1(adder_4_out), .out(multiplexer_13_out), .sel(WB_JAL));
  Adder #(.width(32)) adder_4 (.a(WB_PC), .b(32'h4), .out(adder_4_out));  // open: cin, cout
  Multiplexer #(.width(32), .enable("false")) multiplexer_14 (
    .in0(multiplexer_15_out), .in1({{16{1'b0}}, multiplexer_16_out}), .out(multiplexer_14_out),
    .sel(mem_wb_1_jr_out));
  Comparator #(.width(32)) comparator_4 (.a(WB_R1), .b(32'h22), .eq(comparator_4_eq));  // open: gt, lt
  Multiplexer #(.width(32), .enable("false")) multiplexer_15 (
    .in0(MEM_WB_ALURES), .in1(MEM_WB_MEMDATA), .out(multiplexer_15_out), .sel(mem_wb_1_jr_out_3));
  Multiplexer #(.width(16), .enable("false")) multiplexer_16 (
    .in0(multiplexer_15_out[15:0]), .in1(multiplexer_15_out[31:16]), .out(multiplexer_16_out), .sel(WB_IR[1]));
  not not_4 (not_4_out, comparator_4_eq);
  not not_5 (not_5_out, Go);
  and and_9 (and_9_out, WB_SYSCALL, not_4_out);
  nand nand_1 (TOTAL_EN, not_5_out, and_9_out);
  Register #(.width(32)) PC_2 (.D(WB_R2), .en(comparator_4_eq), .Q(LedData), .clk(CLK));  // open: clr
  // AND_Gate and_10 is placed but not wired

  // Other names for the same wires on the sheet: ID_EX_PC[31:0] = EX_PC; IF_ID_PC[31:0] = ID_PC; MEM_PC[31:0] = M_PC;
  //   WB_REGWRITE = RegWrite

  // Notes on the sheet:
  //   中断源
  //   中断等待指示
  //   数码管输出
  //   指令存储器
  //   contents of rom_1 (hex, n*v repeats v):
  //   20110001 8000c05 20110001 20120002 20130003 8000c09 20110001 20120002 20130003 8000c0d 20110001
  //   20120002 20130003 8000c11 20110001 20120002 20130003 c000cb8 20100001 20110001 118fc0 112020
  //   20020022 c 118882 12200001 8000c15 112020 20020022 c 20110001 118880 112020 20020022 c 12200001
  //   8000c1f 20110001 118fc0 112020 20020022 c 1188c3 112020 20020022 c 118903 112020 20020022 c 118903
  //   112020 20020022 c 118903 112020 20020022 c 118903 112020 20020022 c 118903 112020 20020022 c 118903
  //   112020 20020022 c 118903 112020 20020022 c 20100001 109fc0 139fc3 8021 2012000c 24160003 26100001
  //   3210000f 20080008 20090001 139900 2709825 132020 20020022 c 1094022 1500fff9 22100001 2018000f
  //   2188024 108700 20080008 20090001 139902 2709825 132021 20020022 c 1094022 1500fff9 108702 2c9b022
  //   12c00001 8000c50 4020 1084027 84400 3508ffff 82021 20020022 c 2010ffff 20110000 ae300000 22100001
  //   22310004 ae300000 22100001 22310004 ae300000 22100001 22310004 ae300000 22100001 22310004 ae300000
  //   22100001 22310004 ae300000 22100001 22310004 ae300000 22100001 22310004 ae300000 22100001 22310004
  //   ae300000 22100001 22310004 ae300000 22100001 22310004 ae300000 22100001 22310004 ae300000 22100001
  //   22310004 ae300000 22100001 22310004 ae300000 22100001 22310004 ae300000 22100001 22310004 ae300000
  //   22100001 22310004 22100001 8020 2011003c 8e130000 8e340000 274402a 11000002 ae330000 ae140000
  //   2231fffc 1611fff8 102020 20020022 c 22100004 2011003c 1611fff2 20020032 c 20100000 22100001 102020
  //   20020022 c 22100002 102020 20020022 c 22100003 102020 20020022 c 22100004 102020 20020022 c 22100005
  //   102020 20020022 c 22100006 102020 20020022 c 22100007 102020 20020022 c 22100008 102020 20020022
  //   20020022 c 3e00008
  //   指令字
  //   流水调试日志用
  //   JMP
  //   JR
  //   OP
  //   Func
  //   rs
  //   rt
  //   AluOP
  //   AluSrcB
  //   RegWrite
  //   JAL
  //   RegDst
  //   Syscall
  //   MemToReg
  //   MemWrite
  //   为方便自动评测，需要输出流水线各段保存的PC值，注意是PC不是PC+4，另外ID段寄存器写入信息，Mem段内存写入信息也要输出
  //   PC+4
endmodule

module \数据相关检测  (
  input  in_1,
  input  in_2,
  input  in_3,
  input  in_4,
  input  in_5,
  input  in_6,
  input  in_7,
  input  in_8,
  input  [31:0] ID_IR,
  input  [31:0] EX_IR,
  input  [31:0] MEM_IR,
  input  in_12,
  output [1:0] FORWARD1,
  output [1:0] FORWARD2,
  output LOAD_USE
);

  wire and_2_out, and_4_out, and_6_out, and_7_out, and_8_out, and_9_out, and_10_out, and_11_out,
       comparator_1_eq, comparator_2_eq, comparator_3_eq, comparator_4_eq, EX_R1_USED, EX_R2_USED, ID_R1_BIG,
       ID_R1_USED, ID_R2_BIG, ID_R2_USED, MEM_R1_USED, MEM_R2_USED, not_1_out, not_2_out, not_3_out,
       not_4_out, or_1_out, R1, R2;
  wire [4:0] EX_WRITEREG, ID_R1_NUM, ID_R2_NUM, MEM_WRITEREG, multiplexer_3_out, multiplexer_5_out;

  Comparator #(.width(5)) comparator_1 (.a(ID_R1_NUM), .b(EX_WRITEREG), .eq(comparator_1_eq));  // open: gt, lt
  Comparator #(.width(5)) comparator_2 (.a(ID_R1_NUM), .b(MEM_WRITEREG), .eq(comparator_2_eq));  // open: gt, lt
  Comparator #(.width(5)) comparator_3 (.a(ID_R2_NUM), .b(EX_WRITEREG), .eq(comparator_3_eq));  // open: gt, lt
  Comparator #(.width(5)) comparator_4 (.a(ID_R2_NUM), .b(MEM_WRITEREG), .eq(comparator_4_eq));  // open: gt, lt
  \源寄存器使用情况  \u_源寄存器使用情况_1  (
    .OP0(ID_IR[26]), .OP1(ID_IR[27]), .OP2(ID_IR[28]), .OP3(ID_IR[29]), .OP4(ID_IR[30]), .OP5(ID_IR[31]),
    .F0(ID_IR[0]), .F1(ID_IR[1]), .F2(ID_IR[2]), .F3(ID_IR[3]), .F4(ID_IR[4]), .F5(ID_IR[5]),
    .R1_USED(ID_R1_USED), .R2_USED(ID_R2_USED));
  and and_1 (R1, ID_R1_BIG, comparator_1_eq, ID_R1_USED, in_5);
  and and_2 (and_2_out, ID_R1_BIG, comparator_2_eq, ID_R1_USED, in_6);
  and and_3 (R2, ID_R2_BIG, comparator_3_eq, ID_R2_USED, in_5);
  and and_4 (and_4_out, ID_R2_BIG, comparator_4_eq, ID_R2_USED, in_6);
  or or_1 (or_1_out, R2, R1);
  Multiplexer #(.width(5), .enable("false")) multiplexer_1 (
    .in0(ID_IR[25:21]), .in1(5'b00010), .out(ID_R1_NUM), .sel(in_12));
  Multiplexer #(.width(5), .enable("false")) multiplexer_2 (
    .in0(ID_IR[20:16]), .in1(5'b00100), .out(ID_R2_NUM), .sel(in_12));
  not not_1 (not_1_out, in_7);
  not not_2 (not_2_out, in_8);
  not not_3 (not_3_out, in_7);
  not not_4 (not_4_out, in_8);
  and and_5 (LOAD_USE, or_1_out, in_7);
  and and_6 (and_6_out, not_1_out, R1);
  and and_7 (and_7_out, and_2_out, not_2_out);
  and and_8 (and_8_out, and_2_out, in_8);
  and and_9 (and_9_out, not_3_out, R2);
  and and_10 (and_10_out, and_4_out, not_4_out);
  and and_11 (and_11_out, and_4_out, in_8);
  Priority_Encoder #(.select(2)) priority_encoder_1 (
    .in0(1'b1), .in1(and_7_out), .in2(and_6_out), .in3(and_8_out), .out(FORWARD1));  // open: gs, en_out, en_in
  Priority_Encoder #(.select(2)) priority_encoder_2 (
    .in0(1'b1), .in1(and_10_out), .in2(and_9_out), .in3(and_11_out), .out(FORWARD2));  // open: gs, en_out, en_in
  \源寄存器使用情况  \u_源寄存器使用情况_2  (
    .OP0(EX_IR[26]), .OP1(EX_IR[27]), .OP2(EX_IR[28]), .OP3(EX_IR[29]), .OP4(EX_IR[30]), .OP5(EX_IR[31]),
    .F0(EX_IR[0]), .F1(EX_IR[1]), .F2(EX_IR[2]), .F3(EX_IR[3]), .F4(EX_IR[4]), .F5(EX_IR[5]),
    .R1_USED(EX_R1_USED), .R2_USED(EX_R2_USED));
  Multiplexer #(.width(5), .enable("false")) multiplexer_3 (
    .in0(EX_IR[20:16]), .in1(EX_IR[15:11]), .out(multiplexer_3_out), .sel(in_1));
  Multiplexer #(.width(5), .enable("false")) multiplexer_4 (
    .in0(multiplexer_3_out), .in1({5{1'b1}}), .out(EX_WRITEREG), .sel(in_3));
  Comparator #(.width(5), .mode("unsigned")) comparator_5 (
    .a(ID_R1_NUM), .b({5{1'b0}}), .gt(ID_R1_BIG));  // open: eq, lt
  Comparator #(.width(5), .mode("unsigned")) comparator_6 (
    .a(ID_R2_NUM), .b({5{1'b0}}), .gt(ID_R2_BIG));  // open: eq, lt
  \源寄存器使用情况  \u_源寄存器使用情况_3  (
    .OP0(MEM_IR[26]), .OP1(MEM_IR[27]), .OP2(MEM_IR[28]), .OP3(MEM_IR[29]), .OP4(MEM_IR[30]),
    .OP5(MEM_IR[31]), .F0(MEM_IR[0]), .F1(MEM_IR[1]), .F2(MEM_IR[2]), .F3(MEM_IR[3]), .F4(MEM_IR[4]),
    .F5(MEM_IR[5]), .R1_USED(MEM_R1_USED), .R2_USED(MEM_R2_USED));
  Multiplexer #(.width(5), .enable("false")) multiplexer_5 (
    .in0(MEM_IR[20:16]), .in1(MEM_IR[15:11]), .out(multiplexer_5_out), .sel(in_2));
  Multiplexer #(.width(5), .enable("false")) multiplexer_6 (
    .in0(multiplexer_5_out), .in1({5{1'b1}}), .out(MEM_WRITEREG), .sel(in_4));

  // Other names for the same wires on the sheet: EX_R2_NUM[4:0] = EX_IR[20:16]; EX_R1_NUM[4:0] = EX_IR[25:21];
  //   EX_JAL = in_3; EX_MEMTOREG = in_7; EX_REGDST = in_1; EX_REGWRITE = in_5; ID_EX_SYSCALL = in_12;
  //   MEM_R2_NUM[4:0] = MEM_IR[20:16]; MEM_R1_NUM[4:0] = MEM_IR[25:21]; MEM_JAL = in_4; MEM_MEMTOREG = in_8;
  //   MEM_REGDST = in_2; MEM_REGWRITE = in_6

  // Notes on the sheet:
  //   OP
  //   Func
  //   rs
  //   rt
  //   rd
  //   OP
  //   Func
  //   rs
  //   rt
  //   rd
  //   OP
  //   Func
  //   rs
  //   rt
  //   rd
endmodule

module \源寄存器使用情况  (
  input  OP0,
  input  OP1,
  input  OP2,
  input  OP3,
  input  OP4,
  input  OP5,
  input  F0,
  input  F1,
  input  F2,
  input  F3,
  input  F4,
  input  F5,
  output R1_USED,
  output R2_USED
);

  wire and_1_out, and_2_out, and_3_out, and_4_out, and_5_out, and_6_out, and_7_out, and_8_out, and_9_out,
       and_10_out, and_11_out, and_12_out, and_13_out, and_14_out, and_15_out, and_16_out, and_17_out,
       and_18_out, and_19_out, and_20_out, and_21_out, and_22_out, and_23_out, and_24_out, and_25_out,
       and_26_out, and_27_out, and_28_out, and_29_out, and_30_out, and_31_out, and_32_out, and_33_out,
       and_34_out, and_35_out, and_36_out, and_37_out, not_1_out, not_2_out, not_3_out, not_4_out, not_5_out,
       not_6_out, not_7_out, not_8_out, not_9_out, not_10_out, not_11_out, not_12_out, not_13_out,
       not_14_out, not_15_out, not_16_out, not_17_out, not_18_out, not_19_out, not_20_out, not_21_out,
       not_22_out, not_23_out, not_24_out, not_25_out, not_26_out, not_27_out, not_28_out, not_29_out,
       not_30_out, not_31_out, not_32_out, not_33_out, not_34_out, not_35_out, not_36_out, not_37_out,
       not_38_out, not_39_out, not_40_out, not_41_out, not_42_out, not_43_out, not_44_out, not_45_out,
       not_46_out, not_47_out, not_48_out, not_49_out, not_50_out, not_51_out, not_52_out, not_53_out,
       not_54_out, not_55_out, not_56_out, not_57_out, not_58_out, not_59_out, not_60_out, not_61_out,
       not_62_out, not_63_out, not_64_out, not_65_out, not_66_out, not_67_out, not_68_out, not_69_out,
       not_70_out, not_71_out, not_72_out, not_73_out, not_74_out, not_75_out, not_76_out, not_77_out,
       not_78_out, not_79_out, not_80_out, not_81_out, not_82_out, not_83_out, not_84_out, not_85_out,
       not_86_out, not_87_out, not_88_out, not_89_out, not_90_out, not_91_out, not_92_out, not_93_out,
       not_94_out, not_95_out, not_96_out, not_97_out, not_98_out, not_99_out, not_100_out, not_101_out,
       not_102_out, not_103_out, not_104_out, not_105_out, not_106_out, not_107_out, not_108_out,
       not_109_out, not_110_out, not_111_out, not_112_out, not_113_out, not_114_out, not_115_out,
       not_116_out, not_117_out, not_118_out, not_119_out, not_120_out, not_121_out, not_122_out,
       not_123_out, not_124_out, not_125_out, not_126_out, not_127_out, not_128_out, not_129_out,
       not_130_out, not_131_out, not_132_out, not_133_out, not_134_out, not_135_out, not_136_out,
       not_137_out, not_138_out, not_139_out, not_140_out, not_141_out, not_142_out, not_143_out,
       not_144_out, not_145_out, not_146_out, not_147_out, not_148_out, not_149_out, not_150_out,
       not_151_out, not_152_out, not_153_out, not_154_out, not_155_out, not_156_out, not_157_out,
       not_158_out, not_159_out, not_160_out, not_161_out, not_162_out, not_163_out, not_164_out,
       not_165_out, not_166_out, not_167_out, not_168_out, not_169_out, not_170_out, not_171_out,
       not_172_out, not_173_out, not_174_out, not_175_out, not_176_out, not_177_out, not_178_out,
       not_179_out, not_180_out, not_181_out, not_182_out, not_183_out, not_184_out, not_185_out,
       not_186_out, not_187_out, not_188_out, not_189_out, not_190_out, not_191_out, not_192_out,
       not_193_out, not_194_out, not_195_out, not_196_out, not_197_out, not_198_out, not_199_out,
       not_200_out, not_201_out, not_202_out, not_203_out, not_204_out, not_205_out, not_206_out,
       not_207_out, not_208_out, not_209_out, not_210_out, not_211_out, not_212_out, not_213_out,
       not_214_out, not_215_out, not_216_out, not_217_out, not_218_out, not_219_out, not_220_out,
       not_221_out, not_222_out, not_223_out, not_224_out, not_225_out, not_226_out, not_227_out,
       not_228_out, not_229_out, not_230_out, not_231_out, not_232_out, not_233_out, not_234_out,
       not_235_out, not_236_out, not_237_out, not_238_out, not_239_out, not_240_out, not_241_out,
       not_242_out, not_243_out, not_244_out, not_245_out, not_246_out, not_247_out, not_248_out,
       not_249_out, not_250_out, not_251_out, not_252_out, not_253_out, not_254_out, not_255_out,
       not_256_out, not_257_out, not_258_out, not_259_out, not_260_out, not_261_out, not_262_out,
       not_263_out, not_264_out, not_265_out, not_266_out, not_267_out, not_268_out, not_269_out, not_270_out;

  not not_1 (not_1_out, OP5);
  not not_2 (not_2_out, OP4);
  not not_3 (not_3_out, OP3);
  not not_4 (not_4_out, OP2);
  not not_5 (not_5_out, OP1);
  not not_6 (not_6_out, OP0);
  not not_7 (not_7_out, F4);
  not not_8 (not_8_out, F3);
  not not_9 (not_9_out, F2);
  not not_10 (not_10_out, F1);
  not not_11 (not_11_out, F0);
  not not_12 (not_12_out, OP5);
  not not_13 (not_13_out, OP4);
  not not_14 (not_14_out, OP3);
  not not_15 (not_15_out, OP2);
  not not_16 (not_16_out, OP1);
  not not_17 (not_17_out, OP0);
  not not_18 (not_18_out, F4);
  not not_19 (not_19_out, F3);
  not not_20 (not_20_out, F2);
  not not_21 (not_21_out, F1);
  not not_22 (not_22_out, OP5);
  not not_23 (not_23_out, OP4);
  not not_24 (not_24_out, OP3);
  not not_25 (not_25_out, OP2);
  not not_26 (not_26_out, OP1);
  not not_27 (not_27_out, OP0);
  not not_28 (not_28_out, F4);
  not not_29 (not_29_out, F3);
  not not_30 (not_30_out, F2);
  not not_31 (not_31_out, F0);
  not not_32 (not_32_out, OP5);
  not not_33 (not_33_out, OP4);
  not not_34 (not_34_out, OP3);
  not not_35 (not_35_out, OP2);
  not not_36 (not_36_out, OP1);
  not not_37 (not_37_out, OP0);
  not not_38 (not_38_out, F4);
  not not_39 (not_39_out, F3);
  not not_40 (not_40_out, F1);
  not not_41 (not_41_out, F0);
  not not_42 (not_42_out, OP5);
  not not_43 (not_43_out, OP4);
  not not_44 (not_44_out, OP3);
  not not_45 (not_45_out, OP2);
  not not_46 (not_46_out, OP1);
  not not_47 (not_47_out, OP0);
  not not_48 (not_48_out, F4);
  not not_49 (not_49_out, F3);
  not not_50 (not_50_out, F1);
  not not_51 (not_51_out, OP5);
  not not_52 (not_52_out, OP4);
  not not_53 (not_53_out, OP3);
  not not_54 (not_54_out, OP2);
  not not_55 (not_55_out, OP1);
  not not_56 (not_56_out, OP0);
  not not_57 (not_57_out, F4);
  not not_58 (not_58_out, F3);
  not not_59 (not_59_out, OP5);
  not not_60 (not_60_out, OP4);
  not not_61 (not_61_out, OP3);
  not not_62 (not_62_out, OP2);
  not not_63 (not_63_out, OP1);
  not not_64 (not_64_out, OP0);
  not not_65 (not_65_out, F4);
  not not_66 (not_66_out, F2);
  not not_67 (not_67_out, F0);
  not not_68 (not_68_out, OP5);
  not not_69 (not_69_out, OP4);
  not not_70 (not_70_out, OP3);
  not not_71 (not_71_out, OP2);
  not not_72 (not_72_out, OP1);
  not not_73 (not_73_out, OP0);
  not not_74 (not_74_out, F4);
  not not_75 (not_75_out, F2);
  not not_76 (not_76_out, OP5);
  not not_77 (not_77_out, OP4);
  not not_78 (not_78_out, OP3);
  not not_79 (not_79_out, OP2);
  not not_80 (not_80_out, OP1);
  not not_81 (not_81_out, OP0);
  not not_82 (not_82_out, F5);
  not not_83 (not_83_out, F4);
  not not_84 (not_84_out, F2);
  not not_85 (not_85_out, F1);
  not not_86 (not_86_out, F0);
  not not_87 (not_87_out, OP5);
  not not_88 (not_88_out, OP4);
  not not_89 (not_89_out, OP3);
  not not_90 (not_90_out, OP2);
  not not_91 (not_91_out, OP1);
  not not_92 (not_92_out, OP0);
  not not_93 (not_93_out, F5);
  not not_94 (not_94_out, F4);
  not not_95 (not_95_out, F1);
  not not_96 (not_96_out, F0);
  not not_97 (not_97_out, OP5);
  not not_98 (not_98_out, OP4);
  not not_99 (not_99_out, OP3);
  not not_100 (not_100_out, OP1);
  not not_101 (not_101_out, OP0);
  not not_102 (not_102_out, OP5);
  not not_103 (not_103_out, OP4);
  not not_104 (not_104_out, OP3);
  not not_105 (not_105_out, OP1);
  not not_106 (not_106_out, OP5);
  not not_107 (not_107_out, OP4);
  not not_108 (not_108_out, OP2);
  not not_109 (not_109_out, OP1);
  not not_110 (not_110_out, OP0);
  not not_111 (not_111_out, OP5);
  not not_112 (not_112_out, OP4);
  not not_113 (not_113_out, OP1);
  not not_114 (not_114_out, OP0);
  not not_115 (not_115_out, OP5);
  not not_116 (not_116_out, OP4);
  not not_117 (not_117_out, OP2);
  not not_118 (not_118_out, OP1);
  not not_119 (not_119_out, OP5);
  not not_120 (not_120_out, OP4);
  not not_121 (not_121_out, OP2);
  not not_122 (not_122_out, OP0);
  not not_123 (not_123_out, OP5);
  not not_124 (not_124_out, OP4);
  not not_125 (not_125_out, OP1);
  not not_126 (not_126_out, OP4);
  not not_127 (not_127_out, OP3);
  not not_128 (not_128_out, OP2);
  not not_129 (not_129_out, OP4);
  not not_130 (not_130_out, OP2);
  not not_131 (not_131_out, OP5);
  not not_132 (not_132_out, OP4);
  not not_133 (not_133_out, OP2);
  not not_134 (not_134_out, OP4);
  not not_135 (not_135_out, OP3);
  not not_136 (not_136_out, OP1);
  not not_137 (not_137_out, OP5);
  not not_138 (not_138_out, OP4);
  not not_139 (not_139_out, OP3);
  not not_140 (not_140_out, OP2);
  not not_141 (not_141_out, OP1);
  not not_142 (not_142_out, OP5);
  not not_143 (not_143_out, OP4);
  not not_144 (not_144_out, OP3);
  not not_145 (not_145_out, OP2);
  not not_146 (not_146_out, OP1);
  not not_147 (not_147_out, OP0);
  not not_148 (not_148_out, F5);
  not not_149 (not_149_out, F4);
  not not_150 (not_150_out, F3);
  not not_151 (not_151_out, F2);
  not not_152 (not_152_out, F1);
  not not_153 (not_153_out, F0);
  not not_154 (not_154_out, OP5);
  not not_155 (not_155_out, OP4);
  not not_156 (not_156_out, OP3);
  not not_157 (not_157_out, OP2);
  not not_158 (not_158_out, OP1);
  not not_159 (not_159_out, OP0);
  not not_160 (not_160_out, F5);
  not not_161 (not_161_out, F4);
  not not_162 (not_162_out, F3);
  not not_163 (not_163_out, F2);
  not not_164 (not_164_out, OP5);
  not not_165 (not_165_out, OP4);
  not not_166 (not_166_out, OP3);
  not not_167 (not_167_out, OP2);
  not not_168 (not_168_out, OP1);
  not not_169 (not_169_out, OP0);
  not not_170 (not_170_out, F5);
  not not_171 (not_171_out, F4);
  not not_172 (not_172_out, F3);
  not not_173 (not_173_out, F2);
  not not_174 (not_174_out, F0);
  not not_175 (not_175_out, OP5);
  not not_176 (not_176_out, OP4);
  not not_177 (not_177_out, OP3);
  not not_178 (not_178_out, OP2);
  not not_179 (not_179_out, OP1);
  not not_180 (not_180_out, OP0);
  not not_181 (not_181_out, F4);
  not not_182 (not_182_out, F3);
  not not_183 (not_183_out, F2);
  not not_184 (not_184_out, F1);
  not not_185 (not_185_out, F0);
  not not_186 (not_186_out, OP5);
  not not_187 (not_187_out, OP4);
  not not_188 (not_188_out, OP3);
  not not_189 (not_189_out, OP2);
  not not_190 (not_190_out, OP1);
  not not_191 (not_191_out, OP0);
  not not_192 (not_192_out, F4);
  not not_193 (not_193_out, F3);
  not not_194 (not_194_out, F2);
  not not_195 (not_195_out, F1);
  not not_196 (not_196_out, OP5);
  not not_197 (not_197_out, OP4);
  not not_198 (not_198_out, OP3);
  not not_199 (not_199_out, OP2);
  not not_200 (not_200_out, OP1);
  not not_201 (not_201_out, OP0);
  not not_202 (not_202_out, F4);
  not not_203 (not_203_out, F3);
  not not_204 (not_204_out, F2);
  not not_205 (not_205_out, F0);
  not not_206 (not_206_out, OP5);
  not not_207 (not_207_out, OP4);
  not not_208 (not_208_out, OP3);
  not not_209 (not_209_out, OP2);
  not not_210 (not_210_out, OP1);
  not not_211 (not_211_out, OP0);
  not not_212 (not_212_out, F4);
  not not_213 (not_213_out, F3);
  not not_214 (not_214_out, F1);
  not not_215 (not_215_out, F0);
  not not_216 (not_216_out, OP5);
  not not_217 (not_217_out, OP4);
  not not_218 (not_218_out, OP3);
  not not_219 (not_219_out, OP2);
  not not_220 (not_220_out, OP1);
  not not_221 (not_221_out, OP0);
  not not_222 (not_222_out, F4);
  not not_223 (not_223_out, F3);
  not not_224 (not_224_out, F1);
  not not_225 (not_225_out, OP5);
  not not_226 (not_226_out, OP4);
  not not_227 (not_227_out, OP3);
  not not_228 (not_228_out, OP2);
  not not_229 (not_229_out, OP1);
  not not_230 (not_230_out, OP0);
  not not_231 (not_231_out, F4);
  not not_232 (not_232_out, F3);
  not not_233 (not_233_out, OP5);
  not not_234 (not_234_out, OP4);
  not not_235 (not_235_out, OP3);
  not not_236 (not_236_out, OP2);
  not not_237 (not_237_out, OP1);
  not not_238 (not_238_out, OP0);
  not not_239 (not_239_out, F4);
  not not_240 (not_240_out, F2);
  not not_241 (not_241_out, F0);
  not not_242 (not_242_out, OP5);
  not not_243 (not_243_out, OP4);
  not not_244 (not_244_out, OP3);
  not not_245 (not_245_out, OP2);
  not not_246 (not_246_out, OP1);
  not not_247 (not_247_out, OP0);
  not not_248 (not_248_out, F4);
  not not_249 (not_249_out, F2);
  not not_250 (not_250_out, OP5);
  not not_251 (not_251_out, OP4);
  not not_252 (not_252_out, OP3);
  not not_253 (not_253_out, OP2);
  not not_254 (not_254_out, OP1);
  not not_255 (not_255_out, OP0);
  not not_256 (not_256_out, F5);
  not not_257 (not_257_out, F4);
  not not_258 (not_258_out, F1);
  not not_259 (not_259_out, F0);
  not not_260 (not_260_out, OP5);
  not not_261 (not_261_out, OP4);
  not not_262 (not_262_out, OP3);
  not not_263 (not_263_out, OP1);
  not not_264 (not_264_out, OP0);
  not not_265 (not_265_out, OP5);
  not not_266 (not_266_out, OP4);
  not not_267 (not_267_out, OP3);
  not not_268 (not_268_out, OP1);
  not not_269 (not_269_out, OP4);
  not not_270 (not_270_out, OP2);
  and and_1 (and_1_out, not_1_out, not_2_out, not_3_out, not_4_out, not_5_out, not_6_out, F5, not_7_out, not_8_out, not_9_out, not_10_out, not_11_out);
  and and_2 (and_2_out, not_12_out, not_13_out, not_14_out, not_15_out, not_16_out, not_17_out, F5, not_18_out, not_19_out, not_20_out, not_21_out, F0);
  and and_3 (and_3_out, not_22_out, not_23_out, not_24_out, not_25_out, not_26_out, not_27_out, F5, not_28_out, not_29_out, not_30_out, F1, not_31_out);
  and and_4 (and_4_out, not_32_out, not_33_out, not_34_out, not_35_out, not_36_out, not_37_out, F5, not_38_out, not_39_out, F2, not_40_out, not_41_out);
  and and_5 (and_5_out, not_42_out, not_43_out, not_44_out, not_45_out, not_46_out, not_47_out, F5, not_48_out, not_49_out, F2, not_50_out, F0);
  and and_6 (and_6_out, not_51_out, not_52_out, not_53_out, not_54_out, not_55_out, not_56_out, F5, not_57_out, not_58_out, F2, F1, F0);
  and and_7 (and_7_out, not_59_out, not_60_out, not_61_out, not_62_out, not_63_out, not_64_out, F5, not_65_out, F3, not_66_out, F1, not_67_out);
  and and_8 (and_8_out, not_68_out, not_69_out, not_70_out, not_71_out, not_72_out, not_73_out, F5, not_74_out, F3, not_75_out, F1, F0);
  and and_9 (and_9_out, not_76_out, not_77_out, not_78_out, not_79_out, not_80_out, not_81_out, not_82_out, not_83_out, F3, not_84_out, not_85_out, not_86_out);
  and and_10 (and_10_out, not_87_out, not_88_out, not_89_out, not_90_out, not_91_out, not_92_out, not_93_out, not_94_out, F3, F2, not_95_out, not_96_out);
  and and_11 (and_11_out, not_97_out, not_98_out, not_99_out, OP2, not_100_out, not_101_out);
  and and_12 (and_12_out, not_102_out, not_103_out, not_104_out, OP2, not_105_out, OP0);
  and and_13 (and_13_out, not_106_out, not_107_out, OP3, not_108_out, not_109_out, not_110_out);
  and and_14 (and_14_out, not_111_out, not_112_out, OP3, OP2, not_113_out, not_114_out);
  and and_15 (and_15_out, not_115_out, not_116_out, OP3, not_117_out, not_118_out, OP0);
  and and_16 (and_16_out, not_119_out, not_120_out, OP3, not_121_out, OP1, not_122_out);
  and and_17 (and_17_out, not_123_out, not_124_out, OP3, OP2, not_125_out, OP0);
  and and_18 (and_18_out, OP5, not_126_out, not_127_out, not_128_out, OP1, OP0);
  and and_19 (and_19_out, OP5, not_129_out, OP3, not_130_out, OP1, OP0);
  and and_20 (and_20_out, not_131_out, not_132_out, OP3, not_133_out, OP1, OP0);
  and and_21 (and_21_out, OP5, not_134_out, not_135_out, OP2, not_136_out, OP0);
  and and_22 (and_22_out, not_137_out, not_138_out, not_139_out, not_140_out, not_141_out, OP0);
  and and_23 (and_23_out, not_142_out, not_143_out, not_144_out, not_145_out, not_146_out, not_147_out, not_148_out, not_149_out, not_150_out, not_151_out, not_152_out, not_153_out);
  and and_24 (and_24_out, not_154_out, not_155_out, not_156_out, not_157_out, not_158_out, not_159_out, not_160_out, not_161_out, not_162_out, not_163_out, F1, F0);
  and and_25 (and_25_out, not_164_out, not_165_out, not_166_out, not_167_out, not_168_out, not_169_out, not_170_out, not_171_out, not_172_out, not_173_out, F1, not_174_out);
  and and_26 (and_26_out, not_175_out, not_176_out, not_177_out, not_178_out, not_179_out, not_180_out, F5, not_181_out, not_182_out, not_183_out, not_184_out, not_185_out);
  and and_27 (and_27_out, not_186_out, not_187_out, not_188_out, not_189_out, not_190_out, not_191_out, F5, not_192_out, not_193_out, not_194_out, not_195_out, F0);
  and and_28 (and_28_out, not_196_out, not_197_out, not_198_out, not_199_out, not_200_out, not_201_out, F5, not_202_out, not_203_out, not_204_out, F1, not_205_out);
  and and_29 (and_29_out, not_206_out, not_207_out, not_208_out, not_209_out, not_210_out, not_211_out, F5, not_212_out, not_213_out, F2, not_214_out, not_215_out);
  and and_30 (and_30_out, not_216_out, not_217_out, not_218_out, not_219_out, not_220_out, not_221_out, F5, not_222_out, not_223_out, F2, not_224_out, F0);
  and and_31 (and_31_out, not_225_out, not_226_out, not_227_out, not_228_out, not_229_out, not_230_out, F5, not_231_out, not_232_out, F2, F1, F0);
  and and_32 (and_32_out, not_233_out, not_234_out, not_235_out, not_236_out, not_237_out, not_238_out, F5, not_239_out, F3, not_240_out, F1, not_241_out);
  and and_33 (and_33_out, not_242_out, not_243_out, not_244_out, not_245_out, not_246_out, not_247_out, F5, not_248_out, F3, not_249_out, F1, F0);
  and and_34 (and_34_out, not_250_out, not_251_out, not_252_out, not_253_out, not_254_out, not_255_out, not_256_out, not_257_out, F3, F2, not_258_out, not_259_out);
  and and_35 (and_35_out, not_260_out, not_261_out, not_262_out, OP2, not_263_out, not_264_out);
  and and_36 (and_36_out, not_265_out, not_266_out, not_267_out, OP2, not_268_out, OP0);
  and and_37 (and_37_out, OP5, not_269_out, OP3, not_270_out, OP1, OP0);
  or or_1 (R1_USED, and_1_out, and_2_out, and_3_out, and_4_out, and_5_out, and_6_out, and_7_out, and_8_out, and_9_out, and_10_out, and_11_out, and_12_out, and_13_out, and_14_out, and_15_out, and_16_out, and_17_out, and_18_out, and_19_out, and_20_out, and_21_out, and_22_out);
  or or_2 (R2_USED, and_23_out, and_24_out, and_25_out, and_26_out, and_27_out, and_28_out, and_29_out, and_30_out, and_31_out, and_32_out, and_33_out, and_34_out, and_35_out, and_36_out, and_37_out);
endmodule

module IF_ID (
  input  SYSCALL_in,
  input  REGDST_in,
  input  [31:0] IRin,
  input  [31:0] PCin,
  input  clear,
  input  clk,
  input  enable,
  output J_out,
  output J_out_2,
  output [31:0] IRout,
  output [31:0] PCout
);

  wire multiplexer_1_out, multiplexer_2_out;
  wire [31:0] multiplexer_3_out, multiplexer_4_out;

  Multiplexer #(.enable("false")) multiplexer_1 (.in0(SYSCALL_in), .in1(1'b0), .out(multiplexer_1_out), .sel(clear));
  Multiplexer #(.enable("false")) multiplexer_2 (.in0(REGDST_in), .in1(1'b0), .out(multiplexer_2_out), .sel(clear));
  Register #(.width(1)) SYSCALL (.D(multiplexer_1_out), .en(enable), .Q(J_out), .clk(clk));  // open: clr
  Register #(.width(1)) SYSCALL_2 (.D(multiplexer_2_out), .en(enable), .Q(J_out_2), .clk(clk));  // open: clr
  Multiplexer #(.width(32), .enable("false")) multiplexer_3 (
    .in0(IRin), .in1({32{1'b0}}), .out(multiplexer_3_out), .sel(clear));
  Multiplexer #(.width(32), .enable("false")) multiplexer_4 (
    .in0(PCin), .in1({32{1'b0}}), .out(multiplexer_4_out), .sel(clear));
  Register #(.width(32)) IR (.D(multiplexer_3_out), .en(enable), .Q(IRout), .clk(clk));  // open: clr
  Register #(.width(32)) PC (.D(multiplexer_4_out), .en(enable), .Q(PCout), .clk(clk));  // open: clr

  // Other names for the same wires on the sheet: EN = enable
endmodule

module ID_EX (
  input  SYSCALL_in,
  input  REGDST_in,
  input  LHU_in,
  input  LUI_in,
  input  REGWRITE_in,
  input  MEM_TO_REG_in,
  input  MEMWRITE_in,
  input  JAL_in,
  input  J_in,
  input  JR_in,
  input  BLTZ_in,
  input  [3:0] ALUOP_in,
  input  ALUSRC_in,
  input  BEQ_in,
  input  BNE_in,
  input  [31:0] IR_in,
  input  [31:0] PC_in,
  input  [31:0] R1_in,
  input  [31:0] R2_in,
  input  [31:0] IMM_in,
  input  [1:0] FORWARD1_in,
  input  [1:0] FORWARD2_in,
  input  MISS_in,
  input  PREDICT_in,
  input  in_25,
  input  in_26,
  input  in_27,
  output J_out,
  output J_out_2,
  output JR_out,
  output JR_out_2,
  output J_out_3,
  output JR_out_3,
  output J_out_4,
  output JR_out_4,
  output J_out_5,
  output JR_out_5,
  output J_out_6,
  output [3:0] SYSCALL_out,
  output JR_out_6,
  output JR_out_7,
  output JR_out_8,
  output [31:0] J_out_7,
  output [31:0] J_out_8,
  output [31:0] J_out_9,
  output [31:0] J_out_10,
  output [31:0] J_out_11,
  output [1:0] SYSCALL_out_2,
  output [1:0] SYSCALL_out_3,
  output JR_out_9,
  output JR_out_10
);

  wire multiplexer_1_out, multiplexer_2_out, multiplexer_3_out, multiplexer_4_out, multiplexer_5_out,
       multiplexer_6_out, multiplexer_7_out, multiplexer_10_out, multiplexer_11_out, multiplexer_12_out,
       multiplexer_13_out, multiplexer_14_out, multiplexer_15_out, multiplexer_17_out, multiplexer_18_out,
       multiplexer_19_out;
  wire [1:0] multiplexer_8_out, multiplexer_9_out;
  wire [3:0] multiplexer_16_out;
  wire [31:0] multiplexer_20_out, multiplexer_21_out, multiplexer_22_out, multiplexer_23_out,
       multiplexer_24_out;

  Multiplexer #(.enable("false")) multiplexer_1 (.in0(SYSCALL_in), .in1(1'b0), .out(multiplexer_1_out), .sel(in_26));
  Multiplexer #(.enable("false")) multiplexer_2 (.in0(REGDST_in), .in1(1'b0), .out(multiplexer_2_out), .sel(in_26));
  Multiplexer #(.enable("false")) multiplexer_3 (.in0(LHU_in), .in1(1'b0), .out(multiplexer_3_out), .sel(in_26));
  Multiplexer #(.enable("false")) multiplexer_4 (.in0(REGWRITE_in), .in1(1'b0), .out(multiplexer_4_out), .sel(in_26));
  Multiplexer #(.enable("false")) multiplexer_5 (.in0(MEM_TO_REG_in), .in1(1'b0), .out(multiplexer_5_out), .sel(in_26));
  Multiplexer #(.enable("false")) multiplexer_6 (.in0(MEMWRITE_in), .in1(1'b0), .out(multiplexer_6_out), .sel(in_26));
  Multiplexer #(.enable("false")) multiplexer_7 (.in0(JAL_in), .in1(1'b0), .out(multiplexer_7_out), .sel(in_26));
  Multiplexer #(.width(2), .enable("false")) multiplexer_8 (
    .in0(FORWARD1_in), .in1(2'b00), .out(multiplexer_8_out), .sel(in_26));
  Multiplexer #(.width(2), .enable("false")) multiplexer_9 (
    .in0(FORWARD2_in), .in1(2'b00), .out(multiplexer_9_out), .sel(in_26));
  Multiplexer #(.enable("false")) multiplexer_10 (.in0(MISS_in), .in1(1'b0), .out(multiplexer_10_out), .sel(in_26));
  Multiplexer #(.enable("false")) multiplexer_11 (.in0(PREDICT_in), .in1(1'b0), .out(multiplexer_11_out), .sel(in_26));
  Register #(.width(1)) SYSCALL (.D(multiplexer_1_out), .en(in_25), .Q(J_out), .clk(in_27));  // open: clr
  Register #(.width(1)) SYSCALL_2 (.D(multiplexer_2_out), .en(in_25), .Q(J_out_2), .clk(in_27));  // open: clr
  Multiplexer #(.enable("false")) multiplexer_12 (.in0(LUI_in), .in1(1'b0), .out(multiplexer_12_out), .sel(in_26));
  Multiplexer #(.enable("false")) multiplexer_13 (.in0(J_in), .in1(1'b0), .out(multiplexer_13_out), .sel(in_26));
  Multiplexer #(.enable("false")) multiplexer_14 (.in0(JR_in), .in1(1'b0), .out(multiplexer_14_out), .sel(in_26));
  Multiplexer #(.enable("false")) multiplexer_15 (.in0(BLTZ_in), .in1(1'b0), .out(multiplexer_15_out), .sel(in_26));
  Multiplexer #(.width(4), .enable("false")) multiplexer_16 (
    .in0(ALUOP_in), .in1(4'b0000), .out(multiplexer_16_out), .sel(in_26));
  Multiplexer #(.enable("false")) multiplexer_17 (.in0(ALUSRC_in), .in1(1'b0), .out(multiplexer_17_out), .sel(in_26));
  Multiplexer #(.enable("false")) multiplexer_18 (.in0(BEQ_in), .in1(1'b0), .out(multiplexer_18_out), .sel(in_26));
  Multiplexer #(.enable("false")) multiplexer_19 (.in0(BNE_in), .in1(1'b0), .out(multiplexer_19_out), .sel(in_26));
  Multiplexer #(.width(32), .enable("false")) multiplexer_20 (
    .in0(IR_in), .in1({32{1'b0}}), .out(multiplexer_20_out), .sel(in_26));
  Multiplexer #(.width(32), .enable("false")) multiplexer_21 (
    .in0(PC_in), .in1({32{1'b0}}), .out(multiplexer_21_out), .sel(in_26));
  Multiplexer #(.width(32), .enable("false")) multiplexer_22 (
    .in0(R1_in), .in1({32{1'b0}}), .out(multiplexer_22_out), .sel(in_26));
  Multiplexer #(.width(32), .enable("false")) multiplexer_23 (
    .in0(R2_in), .in1({32{1'b0}}), .out(multiplexer_23_out), .sel(in_26));
  Multiplexer #(.width(32), .enable("false")) multiplexer_24 (
    .in0(IMM_in), .in1({32{1'b0}}), .out(multiplexer_24_out), .sel(in_26));
  Register #(.width(2)) SYSCALL_3 (.D(multiplexer_8_out), .en(in_25), .Q(SYSCALL_out_2), .clk(in_27));  // open: clr
  Register #(.width(2)) SYSCALL_4 (.D(multiplexer_9_out), .en(in_25), .Q(SYSCALL_out_3), .clk(in_27));  // open: clr
  Register #(.width(1)) JR (.D(multiplexer_10_out), .en(in_25), .Q(JR_out_9), .clk(in_27));  // open: clr
  Register #(.width(1)) JR_2 (.D(multiplexer_11_out), .en(in_25), .Q(JR_out_10), .clk(in_27));  // open: clr
  Register #(.width(1)) JR_3 (.D(multiplexer_3_out), .en(in_25), .Q(JR_out), .clk(in_27));  // open: clr
  Register #(.width(1)) JR_4 (.D(multiplexer_12_out), .en(in_25), .Q(JR_out_2), .clk(in_27));  // open: clr
  Register #(.width(1)) SYSCALL_5 (.D(multiplexer_4_out), .en(in_25), .Q(J_out_3), .clk(in_27));  // open: clr
  Register #(.width(1)) JR_5 (.D(multiplexer_5_out), .en(in_25), .Q(JR_out_3), .clk(in_27));  // open: clr
  Register #(.width(1)) SYSCALL_6 (.D(multiplexer_6_out), .en(in_25), .Q(J_out_4), .clk(in_27));  // open: clr
  Register #(.width(1)) JR_6 (.D(multiplexer_7_out), .en(in_25), .Q(JR_out_4), .clk(in_27));  // open: clr
  Register #(.width(1)) J (.D(multiplexer_13_out), .en(in_25), .Q(J_out_5), .clk(in_27));  // open: clr
  Register #(.width(1)) JR_7 (.D(multiplexer_14_out), .en(in_25), .Q(JR_out_5), .clk(in_27));  // open: clr
  Register #(.width(1)) SYSCALL_7 (.D(multiplexer_15_out), .en(in_25), .Q(J_out_6), .clk(in_27));  // open: clr
  Register #(.width(4)) SYSCALL_8 (.D(multiplexer_16_out), .en(in_25), .Q(SYSCALL_out), .clk(in_27));  // open: clr
  Register #(.width(1)) JR_8 (.D(multiplexer_17_out), .en(in_25), .Q(JR_out_6), .clk(in_27));  // open: clr
  Register #(.width(1)) JR_9 (.D(multiplexer_18_out), .en(in_25), .Q(JR_out_7), .clk(in_27));  // open: clr
  Register #(.width(1)) JR_10 (.D(multiplexer_19_out), .en(in_25), .Q(JR_out_8), .clk(in_27));  // open: clr
  Register #(.width(32)) SYSCALL_9 (.D(multiplexer_20_out), .en(in_25), .Q(J_out_7), .clk(in_27));  // open: clr
  Register #(.width(32)) SYSCALL_10 (.D(multiplexer_21_out), .en(in_25), .Q(J_out_8), .clk(in_27));  // open: clr
  Register #(.width(32)) SYSCALL_11 (.D(multiplexer_22_out), .en(in_25), .Q(J_out_9), .clk(in_27));  // open: clr
  Register #(.width(32)) SYSCALL_12 (.D(multiplexer_23_out), .en(in_25), .Q(J_out_10), .clk(in_27));  // open: clr
  Register #(.width(32)) SYSCALL_13 (.D(multiplexer_24_out), .en(in_25), .Q(J_out_11), .clk(in_27));  // open: clr

  // Other names for the same wires on the sheet: clear = in_26; clk = in_27; EN = in_25
endmodule

module EX_MEM (
  input  SYSCALL_in,
  input  REGDST_in,
  input  LHU_in,
  input  LUI_in,
  input  REGWRITE_in,
  input  MEM_TO_REG_in,
  input  MEMWRITE_in,
  input  JAL_in,
  input  [31:0] IR_in,
  input  [31:0] PC_in,
  input  [31:0] R2_in,
  input  [31:0] ALURES_in,
  input  [31:0] r1_in,
  input  in_14,
  input  in_15,
  input  in_16,
  output J_out,
  output J_out_2,
  output JR_out,
  output JR_out_2,
  output J_out_3,
  output JR_out_3,
  output J_out_4,
  output JR_out_4,
  output [31:0] J_out_5,
  output [31:0] J_out_6,
  output [31:0] J_out_7,
  output [31:0] J_out_8,
  output [31:0] J_out_9
);

  wire multiplexer_1_out, multiplexer_2_out, multiplexer_3_out, multiplexer_4_out, multiplexer_5_out,
       multiplexer_6_out, multiplexer_7_out, multiplexer_13_out;
  wire [31:0] multiplexer_8_out, multiplexer_9_out, multiplexer_10_out, multiplexer_11_out,
       multiplexer_12_out;

  Multiplexer #(.enable("false")) multiplexer_1 (.in0(SYSCALL_in), .in1(1'b0), .out(multiplexer_1_out), .sel(in_15));
  Multiplexer #(.enable("false")) multiplexer_2 (.in0(REGDST_in), .in1(1'b0), .out(multiplexer_2_out), .sel(in_15));
  Multiplexer #(.enable("false")) multiplexer_3 (.in0(LHU_in), .in1(1'b0), .out(multiplexer_3_out), .sel(in_15));
  Multiplexer #(.enable("false")) multiplexer_4 (.in0(REGWRITE_in), .in1(1'b0), .out(multiplexer_4_out), .sel(in_15));
  Multiplexer #(.enable("false")) multiplexer_5 (.in0(MEM_TO_REG_in), .in1(1'b0), .out(multiplexer_5_out), .sel(in_15));
  Multiplexer #(.enable("false")) multiplexer_6 (.in0(MEMWRITE_in), .in1(1'b0), .out(multiplexer_6_out), .sel(in_15));
  Multiplexer #(.enable("false")) multiplexer_7 (.in0(JAL_in), .in1(1'b0), .out(multiplexer_7_out), .sel(in_15));
  Multiplexer #(.width(32), .enable("false")) multiplexer_8 (
    .in0(IR_in), .in1({32{1'b0}}), .out(multiplexer_8_out), .sel(in_15));
  Multiplexer #(.width(32), .enable("false")) multiplexer_9 (
    .in0(PC_in), .in1({32{1'b0}}), .out(multiplexer_9_out), .sel(in_15));
  Multiplexer #(.width(32), .enable("false")) multiplexer_10 (
    .in0(R2_in), .in1({32{1'b0}}), .out(multiplexer_10_out), .sel(in_15));
  Multiplexer #(.width(32), .enable("false")) multiplexer_11 (
    .in0(ALURES_in), .in1({32{1'b0}}), .out(multiplexer_11_out), .sel(in_15));
  Multiplexer #(.width(32), .enable("false")) multiplexer_12 (
    .in0(r1_in), .in1({32{1'b0}}), .out(multiplexer_12_out), .sel(in_15));
  Register #(.width(1)) SYSCALL (.D(multiplexer_1_out), .en(in_14), .Q(J_out), .clk(in_16));  // open: clr
  Register #(.width(1)) SYSCALL_2 (.D(multiplexer_2_out), .en(in_14), .Q(J_out_2), .clk(in_16));  // open: clr
  Multiplexer #(.enable("false")) multiplexer_13 (.in0(LUI_in), .in1(1'b0), .out(multiplexer_13_out), .sel(in_15));
  Register #(.width(32)) SYSCALL_3 (.D(multiplexer_8_out), .en(in_14), .Q(J_out_5), .clk(in_16));  // open: clr
  Register #(.width(32)) SYSCALL_4 (.D(multiplexer_9_out), .en(in_14), .Q(J_out_6), .clk(in_16));  // open: clr
  Register #(.width(32)) SYSCALL_5 (.D(multiplexer_10_out), .en(in_14), .Q(J_out_7), .clk(in_16));  // open: clr
  Register #(.width(32)) SYSCALL_6 (.D(multiplexer_11_out), .en(in_14), .Q(J_out_8), .clk(in_16));  // open: clr
  Register #(.width(32)) SYSCALL_7 (.D(multiplexer_12_out), .en(in_14), .Q(J_out_9), .clk(in_16));  // open: clr
  Register #(.width(1)) JR (.D(multiplexer_3_out), .en(in_14), .Q(JR_out), .clk(in_16));  // open: clr
  Register #(.width(1)) JR_2 (.D(multiplexer_13_out), .en(in_14), .Q(JR_out_2), .clk(in_16));  // open: clr
  Register #(.width(1)) SYSCALL_8 (.D(multiplexer_4_out), .en(in_14), .Q(J_out_3), .clk(in_16));  // open: clr
  Register #(.width(1)) JR_3 (.D(multiplexer_5_out), .en(in_14), .Q(JR_out_3), .clk(in_16));  // open: clr
  Register #(.width(1)) SYSCALL_9 (.D(multiplexer_6_out), .en(in_14), .Q(J_out_4), .clk(in_16));  // open: clr
  Register #(.width(1)) JR_4 (.D(multiplexer_7_out), .en(in_14), .Q(JR_out_4), .clk(in_16));  // open: clr

  // Other names for the same wires on the sheet: clear = in_15; clk = in_16; EN = in_14
endmodule

module MEM_WB (
  input  SYSCALL_in,
  input  REGDST_in,
  input  LHU_in,
  input  LUI_in,
  input  REGWRITE_in,
  input  MEM_TO_REG_in,
  input  JAL_in,
  input  [31:0] IR_in,
  input  [31:0] PC_in,
  input  [31:0] R2_in,
  input  [31:0] ALURES_in,
  input  [31:0] MEMDATA_in,
  input  [31:0] R1_in,
  input  in_14,
  input  in_15,
  input  in_16,
  output J_out,
  output J_out_2,
  output JR_out,
  output JR_out_2,
  output J_out_3,
  output JR_out_3,
  output JR_out_4,
  output [31:0] J_out_4,
  output [31:0] J_out_5,
  output [31:0] J_out_6,
  output [31:0] J_out_7,
  output [31:0] J_out_8,
  output [31:0] J_out_9
);

  wire multiplexer_1_out, multiplexer_2_out, multiplexer_3_out, multiplexer_4_out, multiplexer_5_out,
       multiplexer_6_out, multiplexer_7_out;
  wire [31:0] multiplexer_8_out, multiplexer_9_out, multiplexer_10_out, multiplexer_11_out,
       multiplexer_12_out, multiplexer_13_out;

  Multiplexer #(.enable("false")) multiplexer_1 (.in0(SYSCALL_in), .in1(1'b0), .out(multiplexer_1_out), .sel(in_15));
  Multiplexer #(.enable("false")) multiplexer_2 (.in0(REGDST_in), .in1(1'b0), .out(multiplexer_2_out), .sel(in_15));
  Multiplexer #(.enable("false")) multiplexer_3 (.in0(LHU_in), .in1(1'b0), .out(multiplexer_3_out), .sel(in_15));
  Multiplexer #(.enable("false")) multiplexer_4 (.in0(REGWRITE_in), .in1(1'b0), .out(multiplexer_4_out), .sel(in_15));
  Multiplexer #(.enable("false")) multiplexer_5 (.in0(MEM_TO_REG_in), .in1(1'b0), .out(multiplexer_5_out), .sel(in_15));
  Multiplexer #(.enable("false")) multiplexer_6 (.in0(JAL_in), .in1(1'b0), .out(multiplexer_6_out), .sel(in_15));
  Register #(.width(1)) SYSCALL (.D(multiplexer_1_out), .en(in_14), .Q(J_out), .clk(in_16));  // open: clr
  Register #(.width(1)) SYSCALL_2 (.D(multiplexer_2_out), .en(in_14), .Q(J_out_2), .clk(in_16));  // open: clr
  Multiplexer #(.enable("false")) multiplexer_7 (.in0(LUI_in), .in1(1'b0), .out(multiplexer_7_out), .sel(in_15));
  Multiplexer #(.width(32), .enable("false")) multiplexer_8 (
    .in0(IR_in), .in1({32{1'b0}}), .out(multiplexer_8_out), .sel(in_15));
  Multiplexer #(.width(32), .enable("false")) multiplexer_9 (
    .in0(PC_in), .in1({32{1'b0}}), .out(multiplexer_9_out), .sel(in_15));
  Multiplexer #(.width(32), .enable("false")) multiplexer_10 (
    .in0(R2_in), .in1({32{1'b0}}), .out(multiplexer_10_out), .sel(in_15));
  Multiplexer #(.width(32), .enable("false")) multiplexer_11 (
    .in0(ALURES_in), .in1({32{1'b0}}), .out(multiplexer_11_out), .sel(in_15));
  Multiplexer #(.width(32), .enable("false")) multiplexer_12 (
    .in0(MEMDATA_in), .in1({32{1'b0}}), .out(multiplexer_12_out), .sel(in_15));
  Multiplexer #(.width(32), .enable("false")) multiplexer_13 (
    .in0(R1_in), .in1({32{1'b0}}), .out(multiplexer_13_out), .sel(in_15));
  Register #(.width(1)) JR (.D(multiplexer_3_out), .en(in_14), .Q(JR_out), .clk(in_16));  // open: clr
  Register #(.width(1)) JR_2 (.D(multiplexer_7_out), .en(in_14), .Q(JR_out_2), .clk(in_16));  // open: clr
  Register #(.width(1)) SYSCALL_3 (.D(multiplexer_4_out), .en(in_14), .Q(J_out_3), .clk(in_16));  // open: clr
  Register #(.width(1)) JR_3 (.D(multiplexer_5_out), .en(in_14), .Q(JR_out_3), .clk(in_16));  // open: clr
  Register #(.width(1)) JR_4 (.D(multiplexer_6_out), .en(in_14), .Q(JR_out_4), .clk(in_16));  // open: clr
  Register #(.width(32)) SYSCALL_4 (.D(multiplexer_8_out), .en(in_14), .Q(J_out_4), .clk(in_16));  // open: clr
  Register #(.width(32)) SYSCALL_5 (.D(multiplexer_9_out), .en(in_14), .Q(J_out_5), .clk(in_16));  // open: clr
  Register #(.width(32)) SYSCALL_6 (.D(multiplexer_10_out), .en(in_14), .Q(J_out_6), .clk(in_16));  // open: clr
  Register #(.width(32)) SYSCALL_7 (.D(multiplexer_11_out), .en(in_14), .Q(J_out_7), .clk(in_16));  // open: clr
  Register #(.width(32)) SYSCALL_8 (.D(multiplexer_12_out), .en(in_14), .Q(J_out_8), .clk(in_16));  // open: clr
  Register #(.width(32)) SYSCALL_9 (.D(multiplexer_13_out), .en(in_14), .Q(J_out_9), .clk(in_16));  // open: clr

  // Other names for the same wires on the sheet: clear = in_15; clk = in_16; EN = in_14
endmodule

module \中断按键参考电路  (
  input  \同步清零信号 ,
  input  \同步清零信号_2 ,
  input  \同步清零信号_3 
);

  wire \_1号中断_out , \_2号中断_out , \_3号中断_out , and_1_out, and_2_out, and_3_out, and_4_out, and_5_out,
       clock_1_out, clock_2_out, clock_3_out, clock_4_out, d_ff_1_q, d_ff_2_q, d_ff_3_q, IR1_q, IR2_q, IR3_q,
       or_1_out, or_2_out, or_3_out, or_4_out, or_5_out, or_6_out, or_7_out, priority_encoder_1_gs, undriven,
       undriven_2, undriven_3;
  wire [1:0] priority_encoder_1_out;
  wire [31:0] EPC_q, multiplexer_1_out, undriven_4, undriven_5, undriven_6, undriven_7;

  LED \_1号中断等待指示灯  (.in(or_1_out));
  LED \_2号中断等待指示灯  (.in(or_2_out));
  LED \_3号中断等待指示灯  (.in(or_3_out));
  Clock clock_1 (.out(clock_1_out));
  Button \_1号中断  (.out(\_1号中断_out ));
  or or_1 (or_1_out, IR1_q, d_ff_1_q);
  Clock clock_2 (.out(clock_2_out));
  Button \_2号中断  (.out(\_2号中断_out ));
  or or_2 (or_2_out, IR2_q, d_ff_2_q);
  Clock clock_3 (.out(clock_3_out));
  Button \_3号中断  (.out(\_3号中断_out ));
  or or_3 (or_3_out, IR3_q, d_ff_3_q);
  D_Flip_Flop d_ff_1 (.clk(\_1号中断_out ), .D(1'b1), .Q(d_ff_1_q), .reset(IR1_q));  // open: Qn, preset, en
  D_Flip_Flop d_ff_2 (.clk(\_2号中断_out ), .D(1'b1), .Q(d_ff_2_q), .reset(IR2_q));  // open: Qn, preset, en
  D_Flip_Flop d_ff_3 (.clk(\_3号中断_out ), .D(1'b1), .Q(d_ff_3_q), .reset(IR3_q));  // open: Qn, preset, en
  Clock clock_4 (.out(clock_4_out));
  or or_4 (or_4_out, d_ff_1_q, IR1_q);
  or or_5 (or_5_out, d_ff_2_q, IR2_q);
  or or_6 (or_6_out, d_ff_3_q, IR3_q);
  and and_1 (and_1_out, or_4_out, ~\同步清零信号 );  // AND_Gate
  and and_2 (and_2_out, or_5_out, ~\同步清零信号_2 );  // AND_Gate
  and and_3 (and_3_out, or_6_out, ~\同步清零信号_3 );  // AND_Gate
  D_Flip_Flop IR1 (.clk(clock_1_out), .D(and_1_out), .Q(IR1_q));  // open: Qn, preset, en, reset
  D_Flip_Flop IR2 (.clk(clock_2_out), .D(and_2_out), .Q(IR2_q));  // open: Qn, preset, en, reset
  D_Flip_Flop IR3 (.clk(clock_3_out), .D(and_3_out), .Q(IR3_q));  // open: Qn, preset, en, reset
  Register #(.width(32)) EPC (.Q(EPC_q), .clk(undriven), .clr(or_7_out));  // open: D, en
  or or_7 (or_7_out, and_4_out, undriven_2);
  // AND_Gate and_4 has open pins: out=and_4_out
  Priority_Encoder #(.select(2), .disabled(0)) priority_encoder_1 (
    .in1(IR1_q), .in2(IR2_q), .in3(IR3_q), .out(priority_encoder_1_out), .gs(priority_encoder_1_gs));  // open: in0, en_out, en_in
  and and_5 (and_5_out, priority_encoder_1_gs, undriven_3);
  Multiplexer #(.select(2), .width(32), .enable("false")) multiplexer_1 (
    .in0(undriven_4), .in1(undriven_5), .in2(undriven_6), .in3(undriven_7), .out(multiplexer_1_out),
    .sel(priority_encoder_1_out));

  // Notes on the sheet:
  //   中断信号采样参考电路
  //   Reset 
  //   Reset 
  //   Reset 
endmodule

module \双位预测状态机组合逻辑电路  (
  input  h1,
  input  h0,
  input  branch,
  output h1_new,
  output h0_new
);

  wire and_1_out, and_2_out, and_3_out, and_4_out, not_1_out, not_2_out, not_3_out, not_4_out, not_5_out;

  not not_1 (not_1_out, h0);
  not not_2 (not_2_out, h1);
  not not_3 (not_3_out, h0);
  not not_4 (not_4_out, h0);
  not not_5 (not_5_out, branch);
  and and_1 (and_1_out, h0, branch);
  and and_2 (and_2_out, h1, not_1_out);
  and and_3 (and_3_out, not_2_out, not_3_out, branch);
  and and_4 (and_4_out, h1, not_4_out, not_5_out);
  or or_1 (h1_new, and_1_out, and_2_out);
  or or_2 (h0_new, and_3_out, and_4_out);
endmodule

module BHT (
  input  branch_success_EX,
  input  Enable,
  input  [31:0] PC_IF,
  input  Miss_EX,
  input  [31:0] branchaddr_EX,
  input  [31:0] PC_EX,
  input  branch_EX,
  input  CLK,
  output Miss,
  output [1:0] predict_IF,
  output [31:0] predictaddr_IF
);

  wire and_2_out, clear_tong0, clear_tong1, clear_tong2, clear_tong3, clear_tong4, clear_tong5, clear_tong6,
       clear_tong7, comparator_1_eq, comparator_2_eq, comparator_3_eq, comparator_4_eq, comparator_5_eq,
       comparator_6_eq, comparator_7_eq, comparator_8_eq, decoder_1_out0, decoder_1_out1, decoder_1_out2,
       decoder_1_out3, decoder_1_out4, decoder_1_out5, decoder_1_out6, decoder_1_out7, full, hit0_IF,
       hit1_IF, hit2_IF, hit3_IF, hit4_IF, hit5_IF, hit6_IF, hit7_IF, hit_IF, max3_1_p5, max3_1_p6,
       max3_2_p2, max3_2_p3, max3_2_p4, max3_2_p5, max3_4_p5, max3_4_p6, max3_5_p3, max3_5_p4, max3_6_p5,
       max3_6_p6, not_2_out, not_3_out, not_4_out, not_5_out, not_6_out, not_7_out, not_8_out, not_9_out,
       valid0, valid1, valid2, valid3, valid4, valid5, valid6, valid7, w0, w1, w2, w3, w4, w5, w6, w7;
  wire [1:0] history0_q, history1_q, history2_q, history3_q, history4_q, history5_q, history6_q, history7_q,
       multiplexer_1_out, multiplexer_2_out, multiplexer_3_out, multiplexer_4_out, multiplexer_5_out,
       multiplexer_6_out, multiplexer_7_out, multiplexer_8_out, undriven, \双位预测状态机组合逻辑电路_1_h0_new ,
       \双位预测状态机组合逻辑电路_2_h0_new , \双位预测状态机组合逻辑电路_3_h0_new , \双位预测状态机组合逻辑电路_4_h0_new ,
       \双位预测状态机组合逻辑电路_5_h0_new , \双位预测状态机组合逻辑电路_6_h0_new , \双位预测状态机组合逻辑电路_7_h0_new , \双位预测状态机组合逻辑电路_8_h0_new ;
  wire [2:0] max3_7_p5;
  wire [15:0] time0, time1, time2, time3, time4, time5, time6, time7;
  wire [31:0] branchaddr0_q, branchaddr1_q, branchaddr2_q, branchaddr3_q, branchaddr4_q, branchaddr5_q,
       branchaddr6_q, branchaddr7_q, PC0_q, PC1_q, PC2_q, PC3_q, PC4_q, PC5_q, PC6_q, PC7_q, valid_2_q,
       valid_q;

  Register #(.width(1)) u_valid0 (.D(1'b1), .en(w0), .Q(valid0), .clk(CLK));  // open: clr
  Register #(.width(1)) u_valid1 (.D(1'b1), .en(w1), .Q(valid1), .clk(CLK));  // open: clr
  Register #(.width(1)) u_valid2 (.D(1'b1), .en(w2), .Q(valid2), .clk(CLK));  // open: clr
  Register #(.width(1)) u_valid3 (.D(1'b1), .en(w3), .Q(valid3), .clk(CLK));  // open: clr
  Register #(.width(1)) u_valid4 (.D(1'b1), .en(w4), .Q(valid4), .clk(CLK));  // open: clr
  Register #(.width(1)) u_valid5 (.D(1'b1), .en(w5), .Q(valid5), .clk(CLK));  // open: clr
  Register #(.width(1)) u_valid6 (.D(1'b1), .en(w6), .Q(valid6), .clk(CLK));  // open: clr
  Register #(.width(1)) u_valid7 (.D(1'b1), .en(w7), .Q(valid7), .clk(CLK));  // open: clr
  // Max3 max3_1: pin names not known; wires that end beside it: time0, 3'b000, time1, 3'b001, max3_1_p5, max3_1_p6, max3_1_p5
  // Max3 max3_2: pin names not known; wires that end beside it: max3_1_p6, max3_2_p2, max3_2_p3, max3_2_p4, max3_2_p5
  // Max3 max3_3: pin names not known; wires that end beside it: time2, 3'b010, time3, 3'b011, max3_2_p2, max3_2_p3
  // Max3 max3_4: pin names not known; wires that end beside it: time4, 3'b100, time5, 3'b101, max3_4_p5, max3_4_p6
  // Max3 max3_5: pin names not known; wires that end beside it: max3_4_p5, max3_4_p6, max3_5_p3, max3_5_p4
  // Max3 max3_6: pin names not known; wires that end beside it: time6, 3'b110, time7, 3'b111, max3_6_p5, max3_6_p6, max3_6_p5, max3_6_p6
  and and_1 (full, valid0, valid1, valid2, valid3, valid4, valid5, valid6, valid7);
  // Max3 max3_7: pin names not known; wires that end beside it: max3_2_p4, max3_2_p5, max3_5_p3, max3_5_p4, max3_7_p5
  // Probe on max3_7_p5
  Register #(.width(32)) PC0 (.D(PC_EX), .en(w0), .Q(PC0_q), .clk(CLK));  // open: clr
  // Probe on PC0_q
  Register #(.width(32)) PC1 (.D(PC_EX), .en(w1), .Q(PC1_q), .clk(CLK));  // open: clr
  // Probe on PC1_q
  Register #(.width(32)) PC2 (.D(PC_EX), .en(w2), .Q(PC2_q), .clk(CLK));  // open: clr
  // Probe on PC2_q
  Register #(.width(32)) PC3 (.D(PC_EX), .en(w3), .Q(PC3_q), .clk(CLK));  // open: clr
  // Probe on PC3_q
  Register #(.width(32)) PC4 (.D(PC_EX), .en(w4), .Q(PC4_q), .clk(CLK));  // open: clr
  // Probe on PC4_q
  Register #(.width(32)) PC5 (.D(PC_EX), .en(w5), .Q(PC5_q), .clk(CLK));  // open: clr
  // Probe on PC5_q
  Register #(.width(32)) PC6 (.D(PC_EX), .en(w6), .Q(PC6_q), .clk(CLK));  // open: clr
  // Probe on PC6_q
  Register #(.width(32)) PC7 (.D(PC_EX), .en(w7), .Q(PC7_q), .clk(CLK));  // open: clr
  // Probe on PC7_q
  Decoder #(.select(3), .enable("false")) decoder_1 (
    .out0(decoder_1_out0), .out1(decoder_1_out1), .out2(decoder_1_out2), .out3(decoder_1_out3),
    .out4(decoder_1_out4), .out5(decoder_1_out5), .out6(decoder_1_out6), .out7(decoder_1_out7),
    .sel(max3_7_p5));
  and and_2 (and_2_out, branch_EX, Miss_EX, Enable, branch_success_EX);
  nor nor_1 (Miss, hit0_IF, hit1_IF, hit2_IF, hit3_IF, hit4_IF, hit5_IF, hit6_IF, hit7_IF);
  not not_1 (hit_IF, Miss);
  and and_3 (w6, and_2_out, decoder_1_out6);
  and and_4 (w7, and_2_out, decoder_1_out7);
  // Probe on PC_IF
  Comparator #(.width(32)) comparator_1 (.a(PC0_q), .b(PC_IF), .eq(comparator_1_eq));  // open: gt, lt
  Comparator #(.width(32)) comparator_2 (.a(PC1_q), .b(PC_IF), .eq(comparator_2_eq));  // open: gt, lt
  Comparator #(.width(32)) comparator_3 (.a(PC2_q), .b(PC_IF), .eq(comparator_3_eq));  // open: gt, lt
  Comparator #(.width(32)) comparator_4 (.a(PC3_q), .b(PC_IF), .eq(comparator_4_eq));  // open: gt, lt
  Comparator #(.width(32)) comparator_5 (.a(PC4_q), .b(PC_IF), .eq(comparator_5_eq));  // open: gt, lt
  Comparator #(.width(32)) comparator_6 (.a(PC5_q), .b(PC_IF), .eq(comparator_6_eq));  // open: gt, lt
  Comparator #(.width(32)) comparator_7 (.a(PC6_q), .b(PC_IF), .eq(comparator_7_eq));  // open: gt, lt
  Comparator #(.width(32)) comparator_8 (.a(PC7_q), .b(PC_IF), .eq(comparator_8_eq));  // open: gt, lt
  and and_5 (w4, and_2_out, decoder_1_out4);
  and and_6 (w5, and_2_out, decoder_1_out5);
  Register #(.width(32)) valid (.D(PC_IF), .Q(valid_q), .clk(CLK));  // open: en, clr
  and and_7 (hit0_IF, valid0, comparator_1_eq);
  and and_8 (hit1_IF, valid1, comparator_2_eq);
  and and_9 (hit2_IF, valid2, comparator_3_eq);
  and and_10 (hit3_IF, valid3, comparator_4_eq);
  and and_11 (hit4_IF, valid4, comparator_5_eq);
  and and_12 (hit5_IF, valid5, comparator_6_eq);
  and and_13 (hit6_IF, valid6, comparator_7_eq);
  and and_14 (hit7_IF, valid7, comparator_8_eq);
  and and_15 (w3, and_2_out, decoder_1_out3);
  and and_16 (w2, and_2_out, decoder_1_out2);
  or or_1 (clear_tong0, w0, hit0_IF);
  or or_2 (clear_tong1, w1, hit1_IF);
  or or_3 (clear_tong2, w2, hit2_IF);
  or or_4 (clear_tong3, w3, hit3_IF);
  or or_5 (clear_tong4, w4, hit4_IF);
  or or_6 (clear_tong5, w5, hit5_IF);
  or or_7 (clear_tong6, w6, hit6_IF);
  or or_8 (clear_tong7, w7, hit7_IF);
  Register #(.width(32)) valid_2 (.D(valid_q), .Q(valid_2_q), .clk(CLK));  // open: en, clr
  and and_17 (w1, and_2_out, decoder_1_out1);
  and and_18 (w0, and_2_out, decoder_1_out0);
  // Probe on valid_2_q
  not not_2 (not_2_out, clear_tong0);
  not not_3 (not_3_out, clear_tong1);
  not not_4 (not_4_out, clear_tong2);
  not not_5 (not_5_out, clear_tong3);
  not not_6 (not_6_out, clear_tong4);
  not not_7 (not_7_out, clear_tong5);
  not not_8 (not_8_out, clear_tong6);
  not not_9 (not_9_out, clear_tong7);
  // Probe on time0
  Counter #(.width(16), .max('hffff)) u_time0 (
    .load(clear_tong0), .D({16{1'b0}}), .count(not_2_out), .Q(time0), .clk(CLK));  // open: carry, clr
  // Probe on time1
  Counter #(.width(16), .max('hffff)) u_time1 (
    .load(clear_tong1), .D({16{1'b0}}), .count(not_3_out), .Q(time1), .clk(CLK));  // open: carry, clr
  // Probe on time2
  Counter #(.width(16), .max('hffff)) u_time2 (
    .load(clear_tong2), .D({16{1'b0}}), .count(not_4_out), .Q(time2), .clk(CLK));  // open: carry, clr
  // Probe on time3
  Counter #(.width(16), .max('hffff)) u_time3 (
    .load(clear_tong3), .D({16{1'b0}}), .count(not_5_out), .Q(time3), .clk(CLK));  // open: carry, clr
  // Probe on time4
  Counter #(.width(16), .max('hffff)) u_time4 (
    .load(clear_tong4), .D({16{1'b0}}), .count(not_6_out), .Q(time4), .clk(CLK));  // open: carry, clr
  // Probe on time5
  Counter #(.width(16), .max('hffff)) u_time5 (
    .load(clear_tong5), .D({16{1'b0}}), .count(not_7_out), .Q(time5), .clk(CLK));  // open: carry, clr
  // Probe on time6
  Counter #(.width(16), .max('hffff)) u_time6 (
    .load(clear_tong6), .D({16{1'b0}}), .count(not_8_out), .Q(time6), .clk(CLK));  // open: carry, clr
  // Probe on time7
  Counter #(.width(16), .max('hffff)) u_time7 (
    .load(clear_tong7), .D({16{1'b0}}), .count(not_9_out), .Q(time7), .clk(CLK));  // open: carry, clr
  Register #(.width(32)) branchaddr0 (.D(branchaddr_EX), .en(w0), .Q(branchaddr0_q), .clk(CLK));  // open: clr
  Register #(.width(32)) branchaddr1 (.D(branchaddr_EX), .en(w1), .Q(branchaddr1_q), .clk(CLK));  // open: clr
  Register #(.width(32)) branchaddr2 (.D(branchaddr_EX), .en(w2), .Q(branchaddr2_q), .clk(CLK));  // open: clr
  Register #(.width(32)) branchaddr3 (.D(branchaddr_EX), .en(w3), .Q(branchaddr3_q), .clk(CLK));  // open: clr
  Register #(.width(32)) branchaddr4 (.D(branchaddr_EX), .en(w4), .Q(branchaddr4_q), .clk(CLK));  // open: clr
  Register #(.width(32)) branchaddr5 (.D(branchaddr_EX), .en(w5), .Q(branchaddr5_q), .clk(CLK));  // open: clr
  Register #(.width(32)) branchaddr6 (.D(branchaddr_EX), .en(w6), .Q(branchaddr6_q), .clk(CLK));  // open: clr
  Register #(.width(32)) branchaddr7 (.D(branchaddr_EX), .en(w7), .Q(branchaddr7_q), .clk(CLK));  // open: clr
  // Probe on branchaddr_EX
  assign predictaddr_IF = hit0_IF ? branchaddr0_q : 32'bz;  // Controlled_Buffer controlled_buffer_1
  assign predictaddr_IF = hit1_IF ? branchaddr1_q : 32'bz;  // Controlled_Buffer controlled_buffer_2
  assign predictaddr_IF = hit2_IF ? branchaddr2_q : 32'bz;  // Controlled_Buffer controlled_buffer_3
  assign predictaddr_IF = hit3_IF ? branchaddr3_q : 32'bz;  // Controlled_Buffer controlled_buffer_4
  assign predictaddr_IF = hit4_IF ? branchaddr4_q : 32'bz;  // Controlled_Buffer controlled_buffer_5
  assign predictaddr_IF = hit5_IF ? branchaddr5_q : 32'bz;  // Controlled_Buffer controlled_buffer_6
  assign predictaddr_IF = hit6_IF ? branchaddr6_q : 32'bz;  // Controlled_Buffer controlled_buffer_7
  assign predictaddr_IF = hit7_IF ? branchaddr7_q : 32'bz;  // Controlled_Buffer controlled_buffer_8
  Register #(.width(2)) history0 (.D(multiplexer_1_out), .en(branch_EX), .Q(history0_q), .clk(CLK));  // open: clr
  Multiplexer #(.width(2), .enable("false")) multiplexer_1 (
    .in0(\双位预测状态机组合逻辑电路_1_h0_new ), .in1(2'b00), .out(multiplexer_1_out), .sel(w0));
  Multiplexer #(.width(2), .enable("false")) multiplexer_2 (
    .in0(\双位预测状态机组合逻辑电路_2_h0_new ), .in1(2'b00), .out(multiplexer_2_out), .sel(w1));
  Register #(.width(2)) history1 (.D(multiplexer_2_out), .en(branch_EX), .Q(history1_q), .clk(CLK));  // open: clr
  Multiplexer #(.width(2), .enable("false")) multiplexer_3 (
    .in0(\双位预测状态机组合逻辑电路_3_h0_new ), .in1(2'b00), .out(multiplexer_3_out), .sel(w2));
  Register #(.width(2)) history2 (.D(multiplexer_3_out), .en(branch_EX), .Q(history2_q), .clk(CLK));  // open: clr
  Multiplexer #(.width(2), .enable("false")) multiplexer_4 (
    .in0(\双位预测状态机组合逻辑电路_4_h0_new ), .in1(2'b00), .out(multiplexer_4_out), .sel(w3));
  Register #(.width(2)) history3 (.D(multiplexer_4_out), .en(branch_EX), .Q(history3_q), .clk(CLK));  // open: clr
  Multiplexer #(.width(2), .enable("false")) multiplexer_5 (
    .in0(\双位预测状态机组合逻辑电路_5_h0_new ), .in1(2'b00), .out(multiplexer_5_out), .sel(w4));
  Register #(.width(2)) history4 (.D(multiplexer_5_out), .en(branch_EX), .Q(history4_q), .clk(CLK));  // open: clr
  Multiplexer #(.width(2), .enable("false")) multiplexer_6 (
    .in0(undriven), .in1(2'b00), .out(multiplexer_6_out), .sel(w5));
  Register #(.width(2)) history5 (.D(multiplexer_6_out), .en(branch_EX), .Q(history5_q), .clk(CLK));  // open: clr
  Multiplexer #(.width(2), .enable("false")) multiplexer_7 (
    .in0(\双位预测状态机组合逻辑电路_7_h0_new ), .in1(2'b00), .out(multiplexer_7_out), .sel(w6));
  Register #(.width(2)) history6 (.D(multiplexer_7_out), .en(branch_EX), .Q(history6_q), .clk(CLK));  // open: clr
  Register #(.width(2)) history7 (.D(multiplexer_8_out), .en(branch_EX), .Q(history7_q), .clk(CLK));  // open: clr
  Multiplexer #(.width(2), .enable("false")) multiplexer_8 (
    .in0(\双位预测状态机组合逻辑电路_8_h0_new ), .in1(2'b00), .out(multiplexer_8_out), .sel(w7));
  \双位预测状态机组合逻辑电路  \u_双位预测状态机组合逻辑电路_1  (
    .h1(history0_q[1]), .h0(history0_q[0]), .branch(branch_success_EX), .h1_new(\双位预测状态机组合逻辑电路_1_h0_new [1]),
    .h0_new(\双位预测状态机组合逻辑电路_1_h0_new [0]));
  \双位预测状态机组合逻辑电路  \u_双位预测状态机组合逻辑电路_2  (
    .h1(history1_q[1]), .h0(history1_q[0]), .branch(branch_success_EX), .h1_new(\双位预测状态机组合逻辑电路_2_h0_new [1]),
    .h0_new(\双位预测状态机组合逻辑电路_2_h0_new [0]));
  \双位预测状态机组合逻辑电路  \u_双位预测状态机组合逻辑电路_3  (
    .h1(history2_q[1]), .h0(history2_q[0]), .branch(branch_success_EX), .h1_new(\双位预测状态机组合逻辑电路_3_h0_new [1]),
    .h0_new(\双位预测状态机组合逻辑电路_3_h0_new [0]));
  \双位预测状态机组合逻辑电路  \u_双位预测状态机组合逻辑电路_4  (
    .h1(history3_q[1]), .h0(history3_q[0]), .branch(branch_success_EX), .h1_new(\双位预测状态机组合逻辑电路_4_h0_new [1]),
    .h0_new(\双位预测状态机组合逻辑电路_4_h0_new [0]));
  \双位预测状态机组合逻辑电路  \u_双位预测状态机组合逻辑电路_5  (
    .h1(history4_q[1]), .h0(history4_q[0]), .branch(branch_success_EX), .h1_new(\双位预测状态机组合逻辑电路_5_h0_new [1]),
    .h0_new(\双位预测状态机组合逻辑电路_5_h0_new [0]));
  \双位预测状态机组合逻辑电路  \u_双位预测状态机组合逻辑电路_6  (
    .h1(history5_q[1]), .h0(history5_q[0]), .branch(branch_success_EX), .h1_new(\双位预测状态机组合逻辑电路_6_h0_new [1]),
    .h0_new(\双位预测状态机组合逻辑电路_6_h0_new [0]));
  \双位预测状态机组合逻辑电路  \u_双位预测状态机组合逻辑电路_7  (
    .h1(history6_q[1]), .h0(history6_q[0]), .branch(branch_success_EX), .h1_new(\双位预测状态机组合逻辑电路_7_h0_new [1]),
    .h0_new(\双位预测状态机组合逻辑电路_7_h0_new [0]));
  \双位预测状态机组合逻辑电路  \u_双位预测状态机组合逻辑电路_8  (
    .h1(history7_q[1]), .h0(history7_q[0]), .branch(branch_success_EX), .h1_new(\双位预测状态机组合逻辑电路_8_h0_new [1]),
    .h0_new(\双位预测状态机组合逻辑电路_8_h0_new [0]));
  assign predict_IF = hit0_IF ? history0_q : 2'bz;  // Controlled_Buffer controlled_buffer_9
  assign predict_IF = hit1_IF ? history1_q : 2'bz;  // Controlled_Buffer controlled_buffer_10
  assign predict_IF = hit2_IF ? history2_q : 2'bz;  // Controlled_Buffer controlled_buffer_11
  assign predict_IF = hit3_IF ? history3_q : 2'bz;  // Controlled_Buffer controlled_buffer_12
  assign predict_IF = hit4_IF ? history4_q : 2'bz;  // Controlled_Buffer controlled_buffer_13
  assign predict_IF = hit5_IF ? history5_q : 2'bz;  // Controlled_Buffer controlled_buffer_14
  assign predict_IF = hit6_IF ? history6_q : 2'bz;  // Controlled_Buffer controlled_buffer_15
  assign predict_IF = hit7_IF ? history7_q : 2'bz;  // Controlled_Buffer controlled_buffer_16
  // Probe on predict_IF

  // Other names for the same wires on the sheet: DataOut[31:0] = predictaddr_IF; En = Enable; Miss_IF = Miss

  // Notes on the sheet:
  //   请勿增改引脚，请勿修改子电路封装
  //   电路功能：利用上面给定的隧道构建8行的Cache，cache映射方式自选
  //   输入引脚区
  //   68
  //   不论满还是不满
  //   载入数据的cache行号
  //   请在下方利用上方输入输出引脚的隧道信号构建电路，ctrl+d复制选择部件
  //   输出引脚区
endmodule
module \重定向流水线_动态分支预测  (
  output RegWrite,
  output MemWrite,
  output [31:0] IF_PC,
  output [31:0] ID_PC,
  output [31:0] EX_PC,
  output [31:0] M_PC,
  output [31:0] WB_PC,
  output [31:0] RDin,
  output [31:0] MDin,
  output [31:0] LedData
);

  wire and_1_out, and_2_out, and_3_out, and_4_out, and_5_out, and_6_out, and_7_out, and_8_out, and_10_out,
       and_11_out, and_12_out, and_13_out, CLEAR, CLK, comparator_5_eq, eq, ex_mem_1_j_out, ex_mem_1_jr_out,
       ex_mem_1_jr_out_2, EX_MEM_JAL, EX_MEM_MEMTOREG, EX_MEM_REGDST, EX_MEM_REGWRITE, Go, id_ex_1_j_out,
       id_ex_1_j_out_4, id_ex_1_jr_out, id_ex_1_jr_out_2, id_ex_1_jr_out_6, ID_EX_B, ID_EX_BEQ, ID_EX_BLTZ,
       ID_EX_BNE, ID_EX_BRANCH, ID_EX_J, ID_EX_JAL, ID_EX_JR, ID_EX_MEMTOREG, ID_EX_REGDST, ID_EX_REGWRITE,
       ID_EX_SYSCALL, IF_ID_BEQ, IF_ID_BLTZ, IF_ID_BNE, IF_ID_J, IF_ID_JR, IF_ID_LHU, IF_ID_LUI, IR1, IR2,
       IR3, is_BRANCH, LOAD_USE, mem_wb_1_jr_out, mem_wb_1_jr_out_2, mem_wb_1_jr_out_3, Miss_EX, Miss_ID,
       Miss_IF, not_1_out, not_2_out, not_3_out, not_4_out, not_5_out, not_6_out, not_7_out, or_2_out,
       or_3_out, predictbranch_EX, predictbranch_ID, predictbranch_IF, RST, TOTAL_EN, W1, W2, W3, WB_JAL,
       WB_REGDST, WB_SYSCALL, xor_1_out, \单周期硬布线控制器_1_alu_src , \单周期硬布线控制器_1_jal , \单周期硬布线控制器_1_memtoreg ,
       \单周期硬布线控制器_1_memwrite , \单周期硬布线控制器_1_regdst , \单周期硬布线控制器_1_regwrite , \单周期硬布线控制器_1_signedext ;
  wire [1:0] F1, F2, predict_IF, \数据相关检测_1_forward1 , \数据相关检测_1_forward2 ;
  wire [3:0] id_ex_1_syscall_out, \单周期硬布线控制器_1_alu_op ;
  wire [4:0] multiplexer_3_out, multiplexer_4_out, multiplexer_6_out, multiplexer_7_out;
  wire [15:0] \LoadUse次数 , multiplexer_18_out, \总周期数 , \插入气泡数 , \无条件分支数 , \条件分支成功数 ;
  wire [31:0] adder_1_out, adder_2_out, adder_3_out, adder_4_out, bit_extender_1_out, bit_extender_2_out,
       bit_extender_3_out, ex_mem_1_j_out_9, EX_MEM_ALURES, EX_MEM_IR, id_ex_1_j_out_11, ID_EX_IR, ID_EX_R1,
       ID_EX_R1_prime, ID_EX_R2, ID_EX_R2_prime, IF_ID_IR, IF_IR, MEM_WB_ALURES, MEM_WB_MEMDATA,
       mips_alu_1_result, mips_regifile_1_r1, mips_regifile_1_r2, multiplexer_1_out, multiplexer_2_out,
       multiplexer_5_out, multiplexer_8_out, multiplexer_9_out, multiplexer_10_out, multiplexer_13_out,
       multiplexer_15_out, multiplexer_16_out, multiplexer_17_out, predictaddr_IF, ram_1_data, shifter_1_out,
       shifter_2_out, WB_IR, WB_R1, WB_R2;

  Button \u_总复位  (.out(RST));
  Button _1 (.out(IR1));
  Button _2 (.out(IR2));
  Button _3 (.out(IR3));
  Button \u_继续运行  (.out(Go));
  LED led_1 (.in(W1));
  LED led_2 (.in(W2));
  LED led_3 (.in(W3));
  not not_1 (not_1_out, Miss_IF);
  and and_1 (and_1_out, not_1_out, predictbranch_IF);
  Hex_Digit_Display hex_digit_display_1 (.value(LedData[31:28]));  // open: dp
  Multiplexer #(.width(32), .enable("false")) multiplexer_1 (
    .in0(adder_1_out), .in1(predictaddr_IF), .out(multiplexer_1_out), .sel(and_1_out));
  Hex_Digit_Display hex_digit_display_2 (.value(LedData[27:24]));  // open: dp
  Hex_Digit_Display hex_digit_display_3 (.value(LedData[23:20]));  // open: dp
  and and_2 (and_2_out, ID_EX_J, TOTAL_EN);
  and and_3 (and_3_out, ID_EX_BRANCH, ~ID_EX_J, TOTAL_EN);  // AND_Gate
  and and_4 (and_4_out, LOAD_USE, TOTAL_EN);
  Multiplexer #(.width(32), .enable("false")) multiplexer_2 (
    .in0(multiplexer_1_out), .in1(multiplexer_8_out), .out(multiplexer_2_out), .sel(CLEAR));
  not not_2 (not_2_out, LOAD_USE);
  Hex_Digit_Display hex_digit_display_4 (.value(LedData[19:16]));  // open: dp
  Hex_Digit_Display hex_digit_display_5 (.value(LedData[15:12]));  // open: dp
  Counter #(.width(16), .max('hffff)) counter_1 (.count(TOTAL_EN), .Q(\总周期数 ), .clk(CLK));  // open: load, D, carry, clr
  Counter #(.width(16), .max('hffff)) counter_2 (
    .count(and_2_out), .Q(\无条件分支数 ), .clk(CLK));  // open: load, D, carry, clr
  Counter #(.width(16), .max('hffff)) counter_3 (
    .count(and_3_out), .Q(\条件分支成功数 ), .clk(CLK));  // open: load, D, carry, clr
  Counter #(.width(16), .max('hffff)) counter_4 (
    .count(and_4_out), .Q(\LoadUse次数 ), .clk(CLK));  // open: load, D, carry, clr
  Register #(.width(32)) PC (.D(multiplexer_2_out), .en(and_5_out), .Q(IF_PC), .clk(CLK));  // open: clr
  and and_5 (and_5_out, TOTAL_EN, not_2_out);
  or or_1 (is_BRANCH, ID_EX_BEQ, ID_EX_BNE, ID_EX_J, ID_EX_BLTZ);
  // Mips_Probe mips_probe_1: pin names not known; wires that end beside it: IF_IR
  Hex_Digit_Display hex_digit_display_6 (.value(LedData[7:4]));  // open: dp
  Hex_Digit_Display hex_digit_display_7 (.value(LedData[11:8]));  // open: dp
  Clock clock_1 (.out(CLK));
  Adder #(.width(32)) adder_1 (.a(IF_PC), .b(32'h4), .out(adder_1_out));  // open: cin, cout
  Hex_Digit_Display hex_digit_display_8 (.value(LedData[3:0]));  // open: dp
  BHT bht_1 (
    .branch_success_EX(ID_EX_BRANCH), .Miss(Miss_IF), .Enable(TOTAL_EN), .predict_IF(predict_IF),
    .PC_IF(IF_PC), .Miss_EX(Miss_EX), .predictaddr_IF(predictaddr_IF), .branchaddr_EX(multiplexer_8_out),
    .PC_EX(EX_PC), .branch_EX(is_BRANCH), .CLK(CLK));
  Comparator #(.width(2), .mode("unsigned")) comparator_1 (
    .a(predict_IF), .b(2'b01), .gt(predictbranch_IF));  // open: eq, lt
  xor xor_1 (xor_1_out, ID_EX_BRANCH, predictbranch_EX);
  not not_3 (not_3_out, Miss_EX);
  // Mips_Probe mips_probe_2: pin names not known; wires that end beside it: IF_ID_IR
  ROM #(.addrWidth(10), .dataWidth(32)) rom_1 (.addr(IF_PC[11:2]), .data(IF_IR));  // open: sel
  and and_6 (and_6_out, xor_1_out, not_3_out);
  // Probe on \总周期数 
  // Probe on \无条件分支数 
  // Probe on \条件分支成功数 
  // Probe on \插入气泡数 
  // Probe on \LoadUse次数 
  and and_7 (and_7_out, TOTAL_EN, not_4_out);
  not not_4 (not_4_out, LOAD_USE);
  // Mips_Probe mips_probe_3: pin names not known; wires that end beside it: ID_EX_IR
  // Probe on IF_PC[11:0]
  IF_ID if_id_1 (
    .IRin(IF_IR), .PCin(IF_PC), .IRout(IF_ID_IR), .PCout(ID_PC), .SYSCALL_in(Miss_IF), .J_out(Miss_ID),
    .REGDST_in(predictbranch_IF), .J_out_2(predictbranch_ID), .clear(CLEAR), .clk(CLK), .enable(and_7_out));
  // Probe on ID_PC[11:0]
  Comparator #(.width(6), .mode("unsigned")) comparator_2 (
    .a(IF_ID_IR[31:26]), .b(6'b000001), .eq(IF_ID_BLTZ));  // open: gt, lt
  Comparator #(.width(6), .mode("unsigned")) comparator_3 (
    .a(IF_ID_IR[31:26]), .b(6'b100101), .eq(IF_ID_LHU));  // open: gt, lt
  Comparator #(.width(6), .mode("unsigned")) comparator_4 (
    .a(IF_ID_IR[31:26]), .b(6'b001111), .eq(IF_ID_LUI));  // open: gt, lt
  and and_8 (and_8_out, ID_EX_BRANCH, Miss_EX);
  // Mips_Probe mips_probe_4: pin names not known; wires that end beside it: EX_MEM_IR
  // Probe on M_PC[11:0]
  // Probe on EX_PC[11:0]
  or or_2 (or_2_out, and_8_out, and_6_out);
  and and_9 (CLEAR, or_2_out, is_BRANCH);
  // Probe on WB_PC[11:0]
  // Mips_Probe mips_probe_5: pin names not known; wires that end beside it: WB_IR
  \单周期硬布线控制器  \u_单周期硬布线控制器_1  (
    .Func(IF_ID_IR[5:0]), .OP(IF_ID_IR[31:26]), .ALU_OP(\单周期硬布线控制器_1_alu_op ),
    .MemToReg(\单周期硬布线控制器_1_memtoreg ), .MemWrite(\单周期硬布线控制器_1_memwrite ), .ALU_SRC(\单周期硬布线控制器_1_alu_src ),
    .RegWrite(\单周期硬布线控制器_1_regwrite ), .SysCALL(ID_EX_SYSCALL), .SignedExt(\单周期硬布线控制器_1_signedext ),
    .RegDst(\单周期硬布线控制器_1_regdst ), .JR(IF_ID_JR), .JMP(IF_ID_J), .Beq(IF_ID_BEQ), .JAL(\单周期硬布线控制器_1_jal ),
    .Bne(IF_ID_BNE));
  Multiplexer #(.width(5), .enable("false")) multiplexer_3 (
    .in0(IF_ID_IR[25:21]), .in1(5'b00010), .out(multiplexer_3_out), .sel(ID_EX_SYSCALL));
  assign bit_extender_1_out = {{16{1'b0}}, IF_ID_IR[15:0]};  // Bit_Extender bit_extender_1
  assign bit_extender_2_out = {{16{IF_ID_IR[15]}}, IF_ID_IR[15:0]};  // Bit_Extender bit_extender_2
  Multiplexer #(.width(5), .enable("false")) multiplexer_4 (
    .in0(WB_IR[20:16]), .in1(WB_IR[15:11]), .out(multiplexer_4_out), .sel(WB_REGDST));
  Multiplexer #(.width(32), .enable("false")) multiplexer_5 (
    .in0(bit_extender_1_out), .in1(bit_extender_2_out), .out(multiplexer_5_out), .sel(\单周期硬布线控制器_1_signedext ));
  Multiplexer #(.width(5), .enable("false")) multiplexer_6 (
    .in0(IF_ID_IR[20:16]), .in1(5'b00100), .out(multiplexer_6_out), .sel(ID_EX_SYSCALL));
  Multiplexer #(.width(5), .enable("false")) multiplexer_7 (
    .in0(multiplexer_4_out), .in1({5{1'b1}}), .out(multiplexer_7_out), .sel(WB_JAL));
  MIPS_Regifile mips_regifile_1 (
    .Din(RDin), .Clk(CLK), .R1(mips_regifile_1_r1), .R2(mips_regifile_1_r2), .WE(RegWrite),
    .W_num(multiplexer_7_out), .R1_num(multiplexer_3_out), .R2_num(multiplexer_6_out));
  \数据相关检测  \u_数据相关检测_1  (
    .in_1(ID_EX_REGDST), .in_2(EX_MEM_REGDST), .in_3(ID_EX_JAL), .in_4(EX_MEM_JAL), .in_5(ID_EX_REGWRITE),
    .in_6(EX_MEM_REGWRITE), .in_7(ID_EX_MEMTOREG), .in_8(EX_MEM_MEMTOREG), .ID_IR(IF_ID_IR),
    .EX_IR(ID_EX_IR), .MEM_IR(EX_MEM_IR), .FORWARD1(\数据相关检测_1_forward1 ), .FORWARD2(\数据相关检测_1_forward2 ),
    .LOAD_USE(LOAD_USE), .in_12(ID_EX_SYSCALL));
  ID_EX id_ex_1 (
    .J_in(IF_ID_J), .J_out_5(ID_EX_J), .JR_in(IF_ID_JR), .JR_out_5(ID_EX_JR), .BLTZ_in(IF_ID_BLTZ),
    .J_out_6(ID_EX_BLTZ), .ALUSRC_in(\单周期硬布线控制器_1_alu_src ), .JR_out_6(id_ex_1_jr_out_6),
    .ALUOP_in(\单周期硬布线控制器_1_alu_op ), .SYSCALL_out(id_ex_1_syscall_out), .BEQ_in(IF_ID_BEQ),
    .JR_out_7(ID_EX_BEQ), .REGDST_in(\单周期硬布线控制器_1_regdst ), .J_out_2(ID_EX_REGDST), .LHU_in(IF_ID_LHU),
    .JR_out(id_ex_1_jr_out), .BNE_in(IF_ID_BNE), .JR_out_8(ID_EX_BNE), .IR_in(IF_ID_IR), .J_out_7(ID_EX_IR),
    .PC_in(ID_PC), .J_out_8(EX_PC), .R1_in(mips_regifile_1_r1), .J_out_9(ID_EX_R1),
    .R2_in(mips_regifile_1_r2), .J_out_10(ID_EX_R2), .IMM_in(multiplexer_5_out), .J_out_11(id_ex_1_j_out_11),
    .SYSCALL_in(ID_EX_SYSCALL), .J_out(id_ex_1_j_out), .LUI_in(IF_ID_LUI), .JR_out_2(id_ex_1_jr_out_2),
    .REGWRITE_in(\单周期硬布线控制器_1_regwrite ), .J_out_3(ID_EX_REGWRITE), .MEM_TO_REG_in(\单周期硬布线控制器_1_memtoreg ),
    .JR_out_3(ID_EX_MEMTOREG), .MEMWRITE_in(\单周期硬布线控制器_1_memwrite ), .J_out_4(id_ex_1_j_out_4),
    .JAL_in(\单周期硬布线控制器_1_jal ), .JR_out_4(ID_EX_JAL), .in_25(TOTAL_EN), .in_27(CLK), .in_26(or_3_out),
    .FORWARD1_in(\数据相关检测_1_forward1 ), .SYSCALL_out_2(F1), .FORWARD2_in(\数据相关检测_1_forward2 ),
    .SYSCALL_out_3(F2), .MISS_in(Miss_ID), .JR_out_9(Miss_EX), .PREDICT_in(predictbranch_ID),
    .JR_out_10(predictbranch_EX));
  or or_3 (or_3_out, CLEAR, LOAD_USE);
  Multiplexer #(.width(32), .enable("false")) multiplexer_8 (
    .in0(multiplexer_13_out), .in1(multiplexer_9_out), .out(multiplexer_8_out), .sel(ID_EX_J));
  Multiplexer #(.width(32), .enable("false")) multiplexer_9 (
    .in0(shifter_2_out), .in1(ID_EX_R1_prime), .out(multiplexer_9_out), .sel(ID_EX_JR));
  and and_10 (and_10_out, eq, ID_EX_BEQ);
  Multiplexer #(.width(32), .enable("false")) multiplexer_10 (
    .in0(ID_EX_R2_prime), .in1(id_ex_1_j_out_11), .out(multiplexer_10_out), .sel(id_ex_1_jr_out_6));
  Multiplexer #(.select(2), .width(32), .enable("false")) multiplexer_11 (
    .in0(ID_EX_R1), .in1(MEM_WB_ALURES), .in2(EX_MEM_ALURES), .in3(MEM_WB_MEMDATA), .out(ID_EX_R1_prime),
    .sel(F1));
  Multiplexer #(.select(2), .width(32), .enable("false")) multiplexer_12 (
    .in0(ID_EX_R2), .in1(MEM_WB_ALURES), .in2(EX_MEM_ALURES), .in3(MEM_WB_MEMDATA), .out(ID_EX_R2_prime),
    .sel(F2));
  assign bit_extender_3_out = {{6{1'b0}}, ID_EX_IR[25:0]};  // Bit_Extender bit_extender_3
  not not_5 (not_5_out, eq);
  Shifter #(.width(32)) shifter_1 (.in(id_ex_1_j_out_11), .\dist (5'b00010), .out(shifter_1_out));
  Adder #(.width(32)) adder_2 (.a(EX_PC), .b(32'h4), .out(adder_2_out));  // open: cin, cout
  Multiplexer #(.width(32), .enable("false")) multiplexer_13 (
    .in0(adder_2_out), .in1(adder_3_out), .out(multiplexer_13_out), .sel(ID_EX_B));
  Shifter #(.width(32)) shifter_2 (.in(bit_extender_3_out), .\dist (5'b00010), .out(shifter_2_out));
  and and_11 (and_11_out, not_5_out, ID_EX_BNE);
  Adder #(.width(32)) adder_3 (.a(shifter_1_out), .b(adder_2_out), .out(adder_3_out));  // open: cin, cout
  or or_4 (ID_EX_B, and_10_out, and_11_out);
  MIPS_ALU mips_alu_1 (
    .X(ID_EX_R1_prime), .Y(multiplexer_10_out), .AluOP(id_ex_1_syscall_out), .Equal(eq),
    .Result(mips_alu_1_result), .shamt(ID_EX_IR[10:6]));  // open: Result_2
  and and_12 (and_12_out, ID_EX_BLTZ, mips_alu_1_result[0]);
  or or_5 (ID_EX_BRANCH, ID_EX_B, ID_EX_J, and_12_out);
  EX_MEM ex_mem_1 (
    .SYSCALL_in(id_ex_1_j_out), .J_out(ex_mem_1_j_out), .REGDST_in(ID_EX_REGDST), .J_out_2(EX_MEM_REGDST),
    .LHU_in(id_ex_1_jr_out), .JR_out(ex_mem_1_jr_out), .LUI_in(id_ex_1_jr_out_2),
    .JR_out_2(ex_mem_1_jr_out_2), .REGWRITE_in(ID_EX_REGWRITE), .J_out_3(EX_MEM_REGWRITE),
    .MEM_TO_REG_in(ID_EX_MEMTOREG), .JR_out_3(EX_MEM_MEMTOREG), .MEMWRITE_in(id_ex_1_j_out_4),
    .J_out_4(MemWrite), .JAL_in(ID_EX_JAL), .JR_out_4(EX_MEM_JAL), .IR_in(ID_EX_IR), .J_out_5(EX_MEM_IR),
    .PC_in(EX_PC), .J_out_6(M_PC), .R2_in(ID_EX_R2_prime), .J_out_7(MDin), .ALURES_in(mips_alu_1_result),
    .J_out_8(EX_MEM_ALURES), .in_14(TOTAL_EN), .in_15(1'b0), .in_16(CLK), .r1_in(ID_EX_R1_prime),
    .J_out_9(ex_mem_1_j_out_9));
  RAM #(.addrWidth(10), .dataWidth(32), .bus("separate")) ram_1 (
    .addr(EX_MEM_ALURES[11:2]), .din(MDin), .data(ram_1_data), .str(MemWrite), .sel(1'b1), .clk(CLK));  // open: ld, clr
  MEM_WB mem_wb_1 (
    .SYSCALL_in(ex_mem_1_j_out), .J_out(WB_SYSCALL), .REGDST_in(EX_MEM_REGDST), .J_out_2(WB_REGDST),
    .LHU_in(ex_mem_1_jr_out), .JR_out(mem_wb_1_jr_out), .LUI_in(ex_mem_1_jr_out_2),
    .JR_out_2(mem_wb_1_jr_out_2), .REGWRITE_in(EX_MEM_REGWRITE), .J_out_3(RegWrite),
    .MEM_TO_REG_in(EX_MEM_MEMTOREG), .JR_out_3(mem_wb_1_jr_out_3), .JAL_in(EX_MEM_JAL), .JR_out_4(WB_JAL),
    .IR_in(EX_MEM_IR), .J_out_4(WB_IR), .PC_in(M_PC), .J_out_5(WB_PC), .MEMDATA_in(ram_1_data),
    .J_out_8(MEM_WB_MEMDATA), .ALURES_in(EX_MEM_ALURES), .J_out_7(MEM_WB_ALURES), .in_15(1'b0), .in_16(CLK),
    .in_14(TOTAL_EN), .R2_in(MDin), .J_out_6(WB_R2), .R1_in(ex_mem_1_j_out_9), .J_out_9(WB_R1));
  Multiplexer #(.width(32), .enable("false")) multiplexer_14 (
    .in0(multiplexer_15_out), .in1({WB_IR[15:0], {16{1'b0}}}), .out(RDin), .sel(mem_wb_1_jr_out_2));
  Multiplexer #(.width(32), .enable("false")) multiplexer_15 (
    .in0(multiplexer_16_out), .in1(adder_4_out), .out(multiplexer_15_out), .sel(WB_JAL));
  Adder #(.width(32)) adder_4 (.a(WB_PC), .b(32'h4), .out(adder_4_out));  // open: cin, cout
  Multiplexer #(.width(32), .enable("false")) multiplexer_16 (
    .in0(multiplexer_17_out), .in1({{16{1'b0}}, multiplexer_18_out}), .out(multiplexer_16_out),
    .sel(mem_wb_1_jr_out));
  Multiplexer #(.width(32), .enable("false")) multiplexer_17 (
    .in0(MEM_WB_ALURES), .in1(MEM_WB_MEMDATA), .out(multiplexer_17_out), .sel(mem_wb_1_jr_out_3));
  Multiplexer #(.width(16), .enable("false")) multiplexer_18 (
    .in0(multiplexer_17_out[15:0]), .in1(multiplexer_17_out[31:16]), .out(multiplexer_18_out), .sel(WB_IR[1]));
  not not_6 (not_6_out, comparator_5_eq);
  Comparator #(.width(32)) comparator_5 (.a(WB_R1), .b(32'h22), .eq(comparator_5_eq));  // open: gt, lt
  not not_7 (not_7_out, Go);
  and and_13 (and_13_out, WB_SYSCALL, not_6_out);
  nand nand_1 (TOTAL_EN, not_7_out, and_13_out);
  Register #(.width(32)) PC_2 (.D(WB_R2), .en(comparator_5_eq), .Q(LedData), .clk(CLK));  // open: clr
  // AND_Gate and_14 is placed but not wired

  // Other names for the same wires on the sheet: ID_EX_PC[31:0] = EX_PC; IF_ID_PC[31:0] = ID_PC; MEM_PC[31:0] = M_PC;
  //   WB_REGWRITE = RegWrite

  // Notes on the sheet:
  //   中断源
  //   中断等待指示
  //   数码管输出
  //   branch addr
  //   指令存储器
  //   contents of rom_1 (hex, n*v repeats v):
  //   20110001 8000c05 20110001 20120002 20130003 8000c09 20110001 20120002 20130003 8000c0d 20110001
  //   20120002 20130003 8000c11 20110001 20120002 20130003 c000cb8 20100001 20110001 118fc0 112020
  //   20020022 c 118882 12200001 8000c15 112020 20020022 c 20110001 118880 112020 20020022 c 12200001
  //   8000c1f 20110001 118fc0 112020 20020022 c 1188c3 112020 20020022 c 118903 112020 20020022 c 118903
  //   112020 20020022 c 118903 112020 20020022 c 118903 112020 20020022 c 118903 112020 20020022 c 118903
  //   112020 20020022 c 118903 112020 20020022 c 20100001 109fc0 139fc3 8021 2012000c 24160003 26100001
  //   3210000f 20080008 20090001 139900 2709825 132020 20020022 c 1094022 1500fff9 22100001 2018000f
  //   2188024 108700 20080008 20090001 139902 2709825 132021 20020022 c 1094022 1500fff9 108702 2c9b022
  //   12c00001 8000c50 4020 1084027 84400 3508ffff 82021 20020022 c 2010ffff 20110000 ae300000 22100001
  //   22310004 ae300000 22100001 22310004 ae300000 22100001 22310004 ae300000 22100001 22310004 ae300000
  //   22100001 22310004 ae300000 22100001 22310004 ae300000 22100001 22310004 ae300000 22100001 22310004
  //   ae300000 22100001 22310004 ae300000 22100001 22310004 ae300000 22100001 22310004 ae300000 22100001
  //   22310004 ae300000 22100001 22310004 ae300000 22100001 22310004 ae300000 22100001 22310004 ae300000
  //   22100001 22310004 22100001 8020 2011003c 8e130000 8e340000 274402a 11000002 ae330000 ae140000
  //   2231fffc 1611fff8 102020 20020022 c 22100004 2011003c 1611fff2 20020032 c 20100000 22100001 102020
  //   20020022 c 22100002 102020 20020022 c 22100003 102020 20020022 c 22100004 102020 20020022 c 22100005
  //   102020 20020022 c 22100006 102020 20020022 c 22100007 102020 20020022 c 22100008 102020 20020022
  //   20020022 c 3e00008
  //   指令字
  //   流水调试日志用
  //   rs
  //   rt
  //   JMP
  //   JR
  //   OP
  //   Func
  //   Syscall
  //   MemToReg
  //   MemWrite
  //   AluOP
  //   AluSrcB
  //   RegWrite
  //   JAL
  //   RegDst
  //   为方便自动评测，需要输出流水线各段保存的PC值，注意是PC不是PC+4，另外ID段寄存器写入信息，Mem段内存写入信息也要输出
  //   PC+4
endmodule

module \流水中断  (
  output RegWrite,
  output MemWrite,
  output [31:0] IF_PC,
  output [31:0] ID_PC,
  output [31:0] EX_PC,
  output [31:0] M_PC,
  output [31:0] WB_PC,
  output [31:0] RDin,
  output [31:0] MDin,
  output [31:0] LedData,
  output [31:0] PC,
  output [31:0] PC_2
);

  wire and_1_out, and_2_out, and_3_out, and_4_out, and_5_out, and_6_out, and_7_out, and_8_out, and_12_out,
       and_13_out, and_14_out, and_15_out, CLK, comparator_5_eq, comparator_6_gt, comparator_7_eq, d_ff_1_q,
       d_ff_2_q, d_ff_3_q, demultiplexer_1_out1, demultiplexer_1_out2, demultiplexer_1_out3, eq, ERET,
       ex_mem_1_j_out, ex_mem_1_jr_out, ex_mem_1_jr_out_2, EX_MEM_JAL, EX_MEM_MEMTOREG, EX_MEM_REGDST,
       EX_MEM_REGWRITE, Go, id_ex_1_j_out, id_ex_1_j_out_4, id_ex_1_jr_out, id_ex_1_jr_out_2,
       id_ex_1_jr_out_6, id_ex_1_jr_out_7, id_ex_1_jr_out_8, ID_EX_BLTZ, ID_EX_BRANCH, ID_EX_J, ID_EX_JAL,
       ID_EX_JR, ID_EX_MEMTOREG, ID_EX_REGDST, ID_EX_REGWRITE, ID_EX_SYSCALL, IE, IF_ID_BEQ, IF_ID_BLTZ,
       IF_ID_BNE, IF_ID_J, IF_ID_JR, IF_ID_LHU, IF_ID_LUI, Interupt, IR1, IR1_q, IR2, IR2_q, IR3, IR3_q,
       LOAD_USE, mem_wb_1_jr_out, mem_wb_1_jr_out_2, mem_wb_1_jr_out_3, multiplexer_3_out, not_1_out,
       not_2_out, not_3_out, not_4_out, not_5_out, or_4_out, or_5_out, or_6_out, or_7_out, or_8_out,
       or_9_out, or_10_out, RST, TOTAL_EN, W1, W2, W3, WB_JAL, WB_REGDST, WB_SYSCALL, \单周期硬布线控制器_1_alu_src ,
       \单周期硬布线控制器_1_jal , \单周期硬布线控制器_1_memtoreg , \单周期硬布线控制器_1_memwrite , \单周期硬布线控制器_1_regdst ,
       \单周期硬布线控制器_1_regwrite , \单周期硬布线控制器_1_signedext ;
  wire [1:0] and_9_out, F1, F2, IRX, IRX_, \数据相关检测_1_forward1 , \数据相关检测_1_forward2 ;
  wire [3:0] id_ex_1_syscall_out, \单周期硬布线控制器_1_alu_op ;
  wire [4:0] multiplexer_4_out, multiplexer_5_out, multiplexer_6_out, multiplexer_8_out;
  wire [15:0] \LoadUse次数 , multiplexer_20_out, \总周期数 , \插入气泡数 , \无条件分支数 , \条件分支成功数 ;
  wire [31:0] adder_1_out, adder_2_out, adder_3_out, adder_4_out, bit_extender_1_out, bit_extender_2_out,
       bit_extender_3_out, counter_5_q, ex_mem_1_j_out_9, EX_MEM_ALURES, EX_MEM_IR, id_ex_1_j_out_11,
       ID_EX_IR, ID_EX_R1, ID_EX_R1_prime, ID_EX_R2, ID_EX_R2_prime, IF_ID_IR, IF_IR, MEM_WB_ALURES,
       MEM_WB_MEMDATA, mips_alu_1_result, mips_regifile_1_r1, mips_regifile_1_r2, multiplexer_2_out,
       multiplexer_7_out, multiplexer_10_out, multiplexer_11_out, multiplexer_14_out, multiplexer_17_out,
       multiplexer_18_out, multiplexer_19_out, normalPC, ram_1_data, realPC, shifter_1_out, shifter_2_out,
       WB_IR, WB_R1, WB_R2;

  Multiplexer #(.width(32), .enable("false")) multiplexer_1 (
    .in0(adder_1_out), .in1(multiplexer_10_out), .out(normalPC), .sel(ID_EX_BRANCH));
  Button \u_总复位  (.out(RST));
  Button _1 (.out(IR1));
  Button _2 (.out(IR2));
  Button _3 (.out(IR3));
  Button \u_继续运行  (.out(Go));
  LED led_1 (.in(W1));
  LED led_2 (.in(W2));
  LED led_3 (.in(W3));
  Hex_Digit_Display hex_digit_display_1 (.value(LedData[27:24]));  // open: dp
  Hex_Digit_Display hex_digit_display_2 (.value(LedData[31:28]));  // open: dp
  and and_1 (and_1_out, ID_EX_J, TOTAL_EN);
  and and_2 (and_2_out, ID_EX_BRANCH, ~ID_EX_J, TOTAL_EN);  // AND_Gate
  and and_3 (and_3_out, LOAD_USE, TOTAL_EN);
  not not_1 (not_1_out, LOAD_USE);
  Demultiplexer #(.select(2), .enable("false")) demultiplexer_1 (
    .out1(demultiplexer_1_out1), .out2(demultiplexer_1_out2), .out3(demultiplexer_1_out3), .in(ERET),
    .sel(IRX_));  // open: out0
  Hex_Digit_Display hex_digit_display_3 (.value(LedData[23:20]));  // open: dp
  Hex_Digit_Display hex_digit_display_4 (.value(LedData[19:16]));  // open: dp
  Counter #(.width(16), .max('hffff)) counter_1 (.count(TOTAL_EN), .Q(\总周期数 ), .clk(CLK));  // open: load, D, carry, clr
  Counter #(.width(16), .max('hffff)) counter_2 (
    .count(and_1_out), .Q(\无条件分支数 ), .clk(CLK));  // open: load, D, carry, clr
  Counter #(.width(16), .max('hffff)) counter_3 (
    .count(and_2_out), .Q(\条件分支成功数 ), .clk(CLK));  // open: load, D, carry, clr
  Counter #(.width(16), .max('hffff)) counter_4 (
    .count(and_3_out), .Q(\LoadUse次数 ), .clk(CLK));  // open: load, D, carry, clr
  Multiplexer #(.width(32), .enable("false")) multiplexer_2 (
    .in0(realPC), .in1(PC_2), .out(multiplexer_2_out), .sel(ERET));
  and and_4 (and_4_out, TOTAL_EN, not_1_out);
  Hex_Digit_Display hex_digit_display_5 (.value(LedData[15:12]));  // open: dp
  Hex_Digit_Display hex_digit_display_6 (.value(LedData[11:8]));  // open: dp
  Clock clock_1 (.out(CLK));
  Register #(.width(32)) u_PC (.D(multiplexer_2_out), .en(and_4_out), .Q(IF_PC), .clk(CLK));  // open: clr
  Comparator #(.width(32)) comparator_1 (.a(IF_IR), .b(32'h42000018), .eq(ERET));  // open: gt, lt
  Hex_Digit_Display hex_digit_display_7 (.value(LedData[3:0]));  // open: dp
  Hex_Digit_Display hex_digit_display_8 (.value(LedData[7:4]));  // open: dp
  Adder #(.width(32)) adder_1 (.a(IF_PC), .b(32'h4), .out(adder_1_out));  // open: cin, cout
  D_Flip_Flop d_ff_1 (.clk(IR1), .D(1'b1), .Q(d_ff_1_q), .reset(IR1_q));  // open: Qn, preset, en
  or or_1 (W1, IR1_q, d_ff_1_q);
  D_Flip_Flop d_ff_2 (.clk(IR2), .D(1'b1), .Q(d_ff_2_q), .reset(IR2_q));  // open: Qn, preset, en
  or or_2 (W2, IR2_q, d_ff_2_q);
  D_Flip_Flop d_ff_3 (.clk(IR3), .D(1'b1), .Q(d_ff_3_q), .reset(IR3_q));  // open: Qn, preset, en
  or or_3 (W3, IR3_q, d_ff_3_q);
  ROM #(.addrWidth(10), .dataWidth(32)) rom_1 (.addr(IF_PC[11:2]), .data(IF_IR));  // open: sel
  and and_5 (and_5_out, TOTAL_EN, not_2_out);
  not not_2 (not_2_out, LOAD_USE);
  or or_4 (or_4_out, d_ff_1_q, IR1_q);
  and and_6 (and_6_out, or_4_out, ~demultiplexer_1_out1);  // AND_Gate
  or or_5 (or_5_out, d_ff_2_q, IR2_q);
  and and_7 (and_7_out, or_5_out, ~demultiplexer_1_out2);  // AND_Gate
  or or_6 (or_6_out, d_ff_3_q, IR3_q);
  and and_8 (and_8_out, or_6_out, ~demultiplexer_1_out3);  // AND_Gate
  // Probe on \总周期数 
  // Probe on \无条件分支数 
  // Probe on \条件分支成功数 
  // Probe on \插入气泡数 
  // Probe on \LoadUse次数 
  // Mips_Probe mips_probe_1: pin names not known; wires that end beside it: IF_IR
  IF_ID if_id_1 (
    .IRin(IF_IR), .PCin(IF_PC), .IRout(IF_ID_IR), .PCout(ID_PC), .clear(or_7_out), .clk(CLK),
    .enable(and_5_out));  // open: SYSCALL_in, J_out, REGDST_in, J_out_2
  or or_7 (or_7_out, ID_EX_BRANCH, Interupt);
  D_Flip_Flop u_IR1 (.clk(CLK), .D(and_6_out), .Q(IR1_q));  // open: Qn, preset, en, reset
  D_Flip_Flop u_IR2 (.clk(CLK), .D(and_7_out), .Q(IR2_q));  // open: Qn, preset, en, reset
  D_Flip_Flop u_IR3 (.clk(CLK), .D(and_8_out), .Q(IR3_q));  // open: Qn, preset, en, reset
  // Probe on IF_PC[11:0]
  // Probe on ID_PC[11:0]
  Comparator #(.width(6), .mode("unsigned")) comparator_2 (
    .a(IF_ID_IR[31:26]), .b(6'b000001), .eq(IF_ID_BLTZ));  // open: gt, lt
  Comparator #(.width(6), .mode("unsigned")) comparator_3 (
    .a(IF_ID_IR[31:26]), .b(6'b100101), .eq(IF_ID_LHU));  // open: gt, lt
  Comparator #(.width(6), .mode("unsigned")) comparator_4 (
    .a(IF_ID_IR[31:26]), .b(6'b001111), .eq(IF_ID_LUI));  // open: gt, lt
  Counter #(.width(32), .max('hffffffff)) counter_5 (.Q(counter_5_q), .clk(CLK));  // open: load, D, count, carry, clr
  // Probe on EX_PC[11:0]
  // Mips_Probe mips_probe_2: pin names not known; wires that end beside it: IF_ID_IR
  Multiplexer #(.enable("false")) multiplexer_3 (.in0(1'b1), .in1(1'b0), .out(multiplexer_3_out), .sel(Interupt));
  // Probe on M_PC[11:0]
  // Probe on WB_PC[11:0]
  or or_8 (or_8_out, comparator_5_eq, ERET, Interupt);
  Comparator #(.width(32), .mode("unsigned")) comparator_5 (
    .a(counter_5_q), .b({32{1'b0}}), .eq(comparator_5_eq));  // open: gt, lt
  // Mips_Probe mips_probe_3: pin names not known; wires that end beside it: ID_EX_IR
  assign bit_extender_1_out = {{16{1'b0}}, IF_ID_IR[15:0]};  // Bit_Extender bit_extender_1
  assign bit_extender_2_out = {{16{IF_ID_IR[15]}}, IF_ID_IR[15:0]};  // Bit_Extender bit_extender_2
  Register #(.width(1)) u_ie (.D(multiplexer_3_out), .en(or_8_out), .Q(IE), .clk(CLK));  // open: clr
  // Mips_Probe mips_probe_4: pin names not known; wires that end beside it: EX_MEM_IR
  \单周期硬布线控制器  \u_单周期硬布线控制器_1  (
    .Func(IF_ID_IR[5:0]), .OP(IF_ID_IR[31:26]), .ALU_OP(\单周期硬布线控制器_1_alu_op ),
    .MemToReg(\单周期硬布线控制器_1_memtoreg ), .MemWrite(\单周期硬布线控制器_1_memwrite ), .ALU_SRC(\单周期硬布线控制器_1_alu_src ),
    .RegWrite(\单周期硬布线控制器_1_regwrite ), .SysCALL(ID_EX_SYSCALL), .SignedExt(\单周期硬布线控制器_1_signedext ),
    .RegDst(\单周期硬布线控制器_1_regdst ), .JR(IF_ID_JR), .JMP(IF_ID_J), .Beq(IF_ID_BEQ), .JAL(\单周期硬布线控制器_1_jal ),
    .Bne(IF_ID_BNE));
  Multiplexer #(.width(5), .enable("false")) multiplexer_4 (
    .in0(IF_ID_IR[25:21]), .in1(5'b00010), .out(multiplexer_4_out), .sel(ID_EX_SYSCALL));
  Multiplexer #(.width(5), .enable("false")) multiplexer_5 (
    .in0(WB_IR[20:16]), .in1(WB_IR[15:11]), .out(multiplexer_5_out), .sel(WB_REGDST));
  Multiplexer #(.width(5), .enable("false")) multiplexer_6 (
    .in0(IF_ID_IR[20:16]), .in1(5'b00100), .out(multiplexer_6_out), .sel(ID_EX_SYSCALL));
  Multiplexer #(.width(32), .enable("false")) multiplexer_7 (
    .in0(bit_extender_1_out), .in1(bit_extender_2_out), .out(multiplexer_7_out), .sel(\单周期硬布线控制器_1_signedext ));
  Priority_Encoder #(.select(2), .disabled(0)) priority_encoder_1 (
    .in0(1'b1), .in1(IR1_q), .in2(IR2_q), .in3(IR3_q), .out(IRX));  // open: gs, en_out, en_in
  // Mips_Probe mips_probe_5: pin names not known; wires that end beside it: WB_IR
  Multiplexer #(.width(5), .enable("false")) multiplexer_8 (
    .in0(multiplexer_5_out), .in1({5{1'b1}}), .out(multiplexer_8_out), .sel(WB_JAL));
  and and_9 (and_9_out[0], IE, IRX[0]);
  and and_10 (and_9_out[1], IRX[1], IE);
  Comparator #(.width(2), .mode("unsigned")) comparator_6 (.a(IRX), .b(2'b00), .gt(comparator_6_gt));  // open: eq, lt
  and and_11 (Interupt, comparator_6_gt, IE);
  Register #(.width(32)) epc (.D(PC), .en(Interupt), .Q(PC_2), .clk(CLK));  // open: clr
  MIPS_Regifile mips_regifile_1 (
    .Din(RDin), .Clk(CLK), .R1(mips_regifile_1_r1), .R2(mips_regifile_1_r2), .WE(RegWrite),
    .W_num(multiplexer_8_out), .R1_num(multiplexer_4_out), .R2_num(multiplexer_6_out));
  Multiplexer #(.select(2), .width(32), .enable("false")) multiplexer_9 (
    .in0(normalPC), .in1(32'h30ac), .in2(32'h3150), .in3(32'h31f4), .out(realPC), .sel(and_9_out));
  \数据相关检测  \u_数据相关检测_1  (
    .in_1(ID_EX_REGDST), .in_2(EX_MEM_REGDST), .in_3(ID_EX_JAL), .in_4(EX_MEM_JAL), .in_5(ID_EX_REGWRITE),
    .in_6(EX_MEM_REGWRITE), .in_7(ID_EX_MEMTOREG), .in_8(EX_MEM_MEMTOREG), .ID_IR(IF_ID_IR),
    .EX_IR(ID_EX_IR), .MEM_IR(EX_MEM_IR), .FORWARD1(\数据相关检测_1_forward1 ), .FORWARD2(\数据相关检测_1_forward2 ),
    .LOAD_USE(LOAD_USE), .in_12(ID_EX_SYSCALL));
  or or_9 (or_9_out, ID_EX_BRANCH, Interupt, LOAD_USE);
  ID_EX id_ex_1 (
    .J_in(IF_ID_J), .J_out_5(ID_EX_J), .JR_in(IF_ID_JR), .JR_out_5(ID_EX_JR), .BLTZ_in(IF_ID_BLTZ),
    .J_out_6(ID_EX_BLTZ), .ALUSRC_in(\单周期硬布线控制器_1_alu_src ), .JR_out_6(id_ex_1_jr_out_6),
    .ALUOP_in(\单周期硬布线控制器_1_alu_op ), .SYSCALL_out(id_ex_1_syscall_out), .BEQ_in(IF_ID_BEQ),
    .JR_out_7(id_ex_1_jr_out_7), .REGDST_in(\单周期硬布线控制器_1_regdst ), .J_out_2(ID_EX_REGDST),
    .LHU_in(IF_ID_LHU), .JR_out(id_ex_1_jr_out), .BNE_in(IF_ID_BNE), .JR_out_8(id_ex_1_jr_out_8),
    .IR_in(IF_ID_IR), .J_out_7(ID_EX_IR), .PC_in(ID_PC), .J_out_8(EX_PC), .R1_in(mips_regifile_1_r1),
    .J_out_9(ID_EX_R1), .R2_in(mips_regifile_1_r2), .J_out_10(ID_EX_R2), .IMM_in(multiplexer_7_out),
    .J_out_11(id_ex_1_j_out_11), .SYSCALL_in(ID_EX_SYSCALL), .J_out(id_ex_1_j_out), .LUI_in(IF_ID_LUI),
    .JR_out_2(id_ex_1_jr_out_2), .REGWRITE_in(\单周期硬布线控制器_1_regwrite ), .J_out_3(ID_EX_REGWRITE),
    .MEM_TO_REG_in(\单周期硬布线控制器_1_memtoreg ), .JR_out_3(ID_EX_MEMTOREG), .MEMWRITE_in(\单周期硬布线控制器_1_memwrite ),
    .J_out_4(id_ex_1_j_out_4), .JAL_in(\单周期硬布线控制器_1_jal ), .JR_out_4(ID_EX_JAL), .in_25(TOTAL_EN),
    .in_27(CLK), .in_26(or_9_out), .FORWARD1_in(\数据相关检测_1_forward1 ), .SYSCALL_out_2(F1),
    .FORWARD2_in(\数据相关检测_1_forward2 ), .SYSCALL_out_3(F2));  // open: MISS_in, JR_out_9, PREDICT_in, JR_out_10
  Register #(.width(2)) register_1 (.D(IRX), .en(IE), .Q(IRX_), .clk(CLK));  // open: clr
  Multiplexer #(.width(32), .enable("false")) multiplexer_10 (
    .in0(adder_3_out), .in1(multiplexer_11_out), .out(multiplexer_10_out), .sel(ID_EX_J));
  Multiplexer #(.width(32), .enable("false")) multiplexer_11 (
    .in0(shifter_1_out), .in1(ID_EX_R1_prime), .out(multiplexer_11_out), .sel(ID_EX_JR));
  and and_12 (and_12_out, eq, id_ex_1_jr_out_7);
  Multiplexer #(.select(2), .width(32), .enable("false")) multiplexer_12 (
    .in0(ID_EX_R1), .in1(MEM_WB_ALURES), .in2(EX_MEM_ALURES), .in3(MEM_WB_MEMDATA), .out(ID_EX_R1_prime),
    .sel(F1));
  Multiplexer #(.select(2), .width(32), .enable("false")) multiplexer_13 (
    .in0(ID_EX_R2), .in1(MEM_WB_ALURES), .in2(EX_MEM_ALURES), .in3(MEM_WB_MEMDATA), .out(ID_EX_R2_prime),
    .sel(F2));
  assign bit_extender_3_out = {{6{1'b0}}, ID_EX_IR[25:0]};  // Bit_Extender bit_extender_3
  Multiplexer #(.width(32), .enable("false")) multiplexer_14 (
    .in0(ID_EX_R2_prime), .in1(id_ex_1_j_out_11), .out(multiplexer_14_out), .sel(id_ex_1_jr_out_6));
  Shifter #(.width(32)) shifter_1 (.in(bit_extender_3_out), .\dist (5'b00010), .out(shifter_1_out));
  not not_3 (not_3_out, eq);
  and and_13 (and_13_out, not_3_out, id_ex_1_jr_out_8);
  Shifter #(.width(32)) shifter_2 (.in(id_ex_1_j_out_11), .\dist (5'b00010), .out(shifter_2_out));
  Adder #(.width(32)) adder_2 (.a(EX_PC), .b(32'h4), .out(adder_2_out));  // open: cin, cout
  or or_10 (or_10_out, and_12_out, and_13_out);
  Adder #(.width(32)) adder_3 (.a(shifter_2_out), .b(adder_2_out), .out(adder_3_out));  // open: cin, cout
  MIPS_ALU mips_alu_1 (
    .X(ID_EX_R1_prime), .Y(multiplexer_14_out), .AluOP(id_ex_1_syscall_out), .Equal(eq),
    .Result(mips_alu_1_result), .shamt(ID_EX_IR[10:6]));  // open: Result_2
  Multiplexer #(.width(32), .enable("false")) multiplexer_15 (
    .in0(adder_2_out), .in1(multiplexer_10_out), .out(PC), .sel(ID_EX_BRANCH));
  and and_14 (and_14_out, ID_EX_BLTZ, mips_alu_1_result[0]);
  or or_11 (ID_EX_BRANCH, or_10_out, ID_EX_J, and_14_out);
  EX_MEM ex_mem_1 (
    .SYSCALL_in(id_ex_1_j_out), .J_out(ex_mem_1_j_out), .REGDST_in(ID_EX_REGDST), .J_out_2(EX_MEM_REGDST),
    .LHU_in(id_ex_1_jr_out), .JR_out(ex_mem_1_jr_out), .LUI_in(id_ex_1_jr_out_2),
    .JR_out_2(ex_mem_1_jr_out_2), .REGWRITE_in(ID_EX_REGWRITE), .J_out_3(EX_MEM_REGWRITE),
    .MEM_TO_REG_in(ID_EX_MEMTOREG), .JR_out_3(EX_MEM_MEMTOREG), .MEMWRITE_in(id_ex_1_j_out_4),
    .J_out_4(MemWrite), .JAL_in(ID_EX_JAL), .JR_out_4(EX_MEM_JAL), .IR_in(ID_EX_IR), .J_out_5(EX_MEM_IR),
    .PC_in(EX_PC), .J_out_6(M_PC), .R2_in(ID_EX_R2_prime), .J_out_7(MDin), .ALURES_in(mips_alu_1_result),
    .J_out_8(EX_MEM_ALURES), .in_14(TOTAL_EN), .in_15(1'b0), .in_16(CLK), .r1_in(ID_EX_R1_prime),
    .J_out_9(ex_mem_1_j_out_9));
  RAM #(.addrWidth(10), .dataWidth(32), .bus("separate")) ram_1 (
    .addr(EX_MEM_ALURES[11:2]), .din(MDin), .data(ram_1_data), .str(MemWrite), .sel(1'b1), .clk(CLK));  // open: ld, clr
  MEM_WB mem_wb_1 (
    .SYSCALL_in(ex_mem_1_j_out), .J_out(WB_SYSCALL), .REGDST_in(EX_MEM_REGDST), .J_out_2(WB_REGDST),
    .LHU_in(ex_mem_1_jr_out), .JR_out(mem_wb_1_jr_out), .LUI_in(ex_mem_1_jr_out_2),
    .JR_out_2(mem_wb_1_jr_out_2), .REGWRITE_in(EX_MEM_REGWRITE), .J_out_3(RegWrite),
    .MEM_TO_REG_in(EX_MEM_MEMTOREG), .JR_out_3(mem_wb_1_jr_out_3), .JAL_in(EX_MEM_JAL), .JR_out_4(WB_JAL),
    .IR_in(EX_MEM_IR), .J_out_4(WB_IR), .PC_in(M_PC), .J_out_5(WB_PC), .MEMDATA_in(ram_1_data),
    .J_out_8(MEM_WB_MEMDATA), .ALURES_in(EX_MEM_ALURES), .J_out_7(MEM_WB_ALURES), .in_15(1'b0), .in_16(CLK),
    .in_14(TOTAL_EN), .R2_in(MDin), .J_out_6(WB_R2), .R1_in(ex_mem_1_j_out_9), .J_out_9(WB_R1));
  Multiplexer #(.width(32), .enable("false")) multiplexer_16 (
    .in0(multiplexer_17_out), .in1({WB_IR[15:0], {16{1'b0}}}), .out(RDin), .sel(mem_wb_1_jr_out_2));
  Multiplexer #(.width(32), .enable("false")) multiplexer_17 (
    .in0(multiplexer_18_out), .in1(adder_4_out), .out(multiplexer_17_out), .sel(WB_JAL));
  Adder #(.width(32)) adder_4 (.a(WB_PC), .b(32'h4), .out(adder_4_out));  // open: cin, cout
  Multiplexer #(.width(32), .enable("false")) multiplexer_18 (
    .in0(multiplexer_19_out), .in1({{16{1'b0}}, multiplexer_20_out}), .out(multiplexer_18_out),
    .sel(mem_wb_1_jr_out));
  Multiplexer #(.width(32), .enable("false")) multiplexer_19 (
    .in0(MEM_WB_ALURES), .in1(MEM_WB_MEMDATA), .out(multiplexer_19_out), .sel(mem_wb_1_jr_out_3));
  Multiplexer #(.width(16), .enable("false")) multiplexer_20 (
    .in0(multiplexer_19_out[15:0]), .in1(multiplexer_19_out[31:16]), .out(multiplexer_20_out), .sel(WB_IR[1]));
  Comparator #(.width(32)) comparator_7 (.a(WB_R1), .b(32'h22), .eq(comparator_7_eq));  // open: gt, lt
  not not_4 (not_4_out, Go);
  and and_15 (and_15_out, WB_SYSCALL, not_5_out);
  not not_5 (not_5_out, comparator_7_eq);
  nand nand_1 (TOTAL_EN, not_4_out, and_15_out);
  Register #(.width(32)) u_PC_2 (.D(WB_R2), .en(comparator_7_eq), .Q(LedData), .clk(CLK));  // open: clr
  // AND_Gate and_16 is placed but not wired

  // Other names for the same wires on the sheet: EPCtoPC[31:0] = PC_2; ID_EX_PC[31:0] = EX_PC; IF_ID_PC[31:0] = ID_PC;
  //   MEM_PC[31:0] = M_PC; ret_addr[31:0] = PC; WB_REGWRITE = RegWrite

  // Notes on the sheet:
  //   中断源
  //   中断等待指示
  //   数码管输出
  //   指令存储器
  //   contents of rom_1 (hex, n*v repeats v):
  //   201d07d0 20100001 109fc0 139fc3 8021 2012000c 24160008 26100001 3210000f 20080008 20090001 139900
  //   2709825 132020 20020022 c 1094022 1500fff9 22100001 2018000f 2188024 108700 20080008 20090001 139902
  //   2709825 132021 20020022 c 1094022 1500fff9 108702 2c9b022 12c00001 8000c07 4020 1084027 84400
  //   3508ffff 82021 20020022 c 8000c01 afa20000 23bd0004 afa40000 23bd0004 afb00000 23bd0004 afb30000
  //   23bd0004 afb40000 23bd0004 afb50000 23bd0004 afb60000 23bd0004 20160001 20140003 20150001 168020
  //   108100 2149825 132020 20020022 c 1600fffa 295a022 1680fff7 23bdfffc 8fb60000 23bdfffc 8fb50000
  //   23bdfffc 8fb40000 23bdfffc 8fb30000 23bdfffc 8fb00000 23bdfffc 8fa40000 23bdfffc 8fa20000 42000018
  //   afa20000 23bd0004 afa40000 23bd0004 afb00000 23bd0004 afb30000 23bd0004 afb40000 23bd0004 afb50000
  //   23bd0004 afb60000 23bd0004 20160002 20140003 20150001 168020 108100 2149825 132020 20020022 c
  //   1600fffa 295a022 1680fff7 23bdfffc 8fb60000 23bdfffc 8fb50000 23bdfffc 8fb40000 23bdfffc 8fb30000
  //   23bdfffc 8fb00000 23bdfffc 8fa40000 23bdfffc 8fa20000 42000018 afa20000 23bd0004 afa40000 23bd0004
  //   afb00000 23bd0004 afb30000 23bd0004 afb40000 23bd0004 afb50000 23bd0004 afb60000 23bd0004 20160003
  //   20140003 20150001 168020 108100 2149825 132020 20020022 c 1600fffa 295a022 1680fff7 23bdfffc
  //   8fb60000 23bdfffc 8fb50000 23bdfffc 8fb40000 23bdfffc 8fb30000 23bdfffc 8fb00000 23bdfffc 8fa40000
  //   23bdfffc 8fa20000 42000018
  //   Reset 
  //   Reset 
  //   Reset 
  //   指令字
  //   流水调试日志用
  //   rs
  //   rt
  //   JMP
  //   JR
  //   OP
  //   Func
  //   MemToReg
  //   MemWrite
  //   AluOP
  //   AluSrcB
  //   RegWrite
  //   JAL
  //   RegDst
  //   Syscall
  //   为方便自动评测，需要输出流水线各段保存的PC值，注意是PC不是PC+4，另外ID段寄存器写入信息，Mem段内存写入信息也要输出
  //   PC+4
endmodule
